// Logisim project Branch.circ as structural Verilog: 10 circuits, main circuit IF_ID
module main (
  output [15:0] \总周期数 
);

  wire alu_1_equal, and_1_out, and_3_out, btb_1_jmp, clear, clear1, clear2, clear3, clear4, clk,
       clock_source, comparator_1_eq, EX_MEM_halt_out, EX_MEM_memread_2, EX_MEM_memwrite_out,
       EX_MEM_regwrite_out, halt, halt_bubble, ID_EX_branch_out, ID_EX_jmp_out, ID_EX_lohi_out,
       ID_EX_memread_2, ID_EX_memwrite_out, ID_EX_regwrite_out, ID_EX_syscall_out, IF_ID_jmp_out,
       instr_fetch_wrong, jmp_count, main_1_bubble, main_2_branch, main_2_hi_lo, main_2_memread,
       main_2_memwrite, main_2_regwrite, main_2_rf_r1, main_2_syscall, no_pre, not_1_out, not_2_out,
       not_3_out, not_4_out, or_1_out, or_2_out, or_3_out, Pre_success, Pre_wrong, WE;
  wire [1:0] btb_1_pre_num, EX_MEM_selpc_out, ID_EX_alu_b_out, ID_EX_pre__out, ID_EX_selpc_out,
       IF_ID_pre__out, jmp_detect_1_pc_update, main_1_sel_a0, main_1_sel_r1, main_1_sel_r2, main_1_sel_v0,
       main_2_alu_b, main_2_pc, main_2_rf_w;
  wire [2:0] EX_MEM_rf_din_out, ID_EX_rf_din_out, main_2_rf_din, RF_Din;
  wire [3:0] ID_EX_alu_op_out, main_2_alu_op, register_1_q_2, register_1_q_3;
  wire [4:0] decode_rd, decode_rs, decode_rt, decode_shamt, EX_MEM_rw__out, ID_EX_rw__out, ID_EX_shamt_out,
       multiplexer_3_out, multiplexer_4_out, RW_num;
  wire [5:0] decode_funct, decode_op;
  wire [15:0] counter_2_q, counter_3_q, counter_4_q, counter_5_q, counter_6_q, decode_imm, ID_EX_imm_out,
       multiplexer_2_out, PCcount;
  wire [23:0] register_1_q;
  wire [25:0] decode_addr, ID_EX_addr_out;
  wire [31:0] alu_1_result, alu_1_result_2, ALU_out, bit_extender_1_out, bit_extender_3_out,
       btb_1_predict_pc, DM_out, EX_BACK, EX_MEM_alu_out_out, EX_MEM_hi_out, EX_MEM_ir_out, EX_MEM_lo_out,
       EX_MEM_pc_4_out, EX_MEM_pc_out, EX_MEM_rf_r2_out, Hi, Hi_q, ID_EX_a0_out, ID_EX_ir_out,
       ID_EX_pc_4_out, ID_EX_pc_out, ID_EX_rf_r1_out, ID_EX_rf_r2_out, ID_EX_v0_out, IF_ID_ir_out,
       IF_ID_pc_4_out, IF_ID_pc_out, jmp_detect_1_corret_pc, Lo, Lo_q, main_3_a0_value, main_3_ra_value,
       main_3_reg1, main_3_reg2, main_3_s0_value, main_3_s1_value, main_3_s2_value, main_3_v0_value,
       MEM_BACK, MEM_WB_ir_out, MEM_WB_pc_4_out, MEM_WB_pc_out, multiplexer_1_out, multiplexer_5_out,
       multiplexer_6_out, multiplexer_7_out, multiplexer_8_out, multiplexer_9_out, multiplexer_10_out, PC_4,
       PC_q, ram_1_data, rom_1_data, S_EXT;

  Button button_1 (.out(clear));
  Button button_2 (.out(clear1));
  Button button_3 (.out(clear2));
  Button button_4 (.out(clear3));
  Button button_5 (.out(clear4));
  Clock clock_1 (.out(clock_source));
  Multiplexer #(.width(32)) multiplexer_1 (
    .in0(btb_1_predict_pc), .in1(jmp_detect_1_corret_pc), .out(multiplexer_1_out), .sel(instr_fetch_wrong),
    .en(1'b1));
  Register #(.width(32)) PC (.D(multiplexer_1_out), .en(and_1_out), .Q(PC_q), .clk(clk), .clr(clear));
  and and_1 (and_1_out, or_1_out, not_1_out);
  not not_1 (not_1_out, halt);
  or or_1 (or_1_out, instr_fetch_wrong, not_2_out);
  not not_2 (not_2_out, main_1_bubble);
  not not_3 (not_3_out, main_1_bubble);
  Hex_Digit_Display hex_digit_display_1 (.value(register_1_q_3));  // open: dp
  Hex_Digit_Display hex_digit_display_2 (.value(register_1_q_2));  // open: dp
  Register #(.width(32)) register_1 (
    .D(ID_EX_a0_out), .en(ID_EX_syscall_out), .Q({register_1_q_3, register_1_q_2, register_1_q}), .clk(clk));  // open: clr
  Counter #(.width(16), .max('hffff)) counter_1 (.Q(PCcount), .clk(clk), .clr(clear));  // open: load, D, count, carry
  and and_2 (clk, ~halt, clock_source);  // AND_Gate
  or or_2 (or_2_out, not_3_out, instr_fetch_wrong);
  Hex_Digit_Display hex_digit_display_3 (.value(register_1_q[23:20]));  // open: dp
  Hex_Digit_Display hex_digit_display_4 (.value(register_1_q[19:16]));  // open: dp
  and and_3 (and_3_out, clk, ~halt_bubble);  // AND_Gate
  Multiplexer #(.width(16)) multiplexer_2 (
    .in0({16{1'b0}}), .in1(16'h1), .out(multiplexer_2_out), .sel(halt), .en(1'b1));
  BTB btb_1 (
    .pc_update(jmp_detect_1_pc_update), .Current_PC(PC_q), .Back_PC(ID_EX_pc_out), .clk(clk), .clear(clear),
    .Current_IR(rom_1_data), .Branch_PC(jmp_detect_1_corret_pc), .Wrong_num(ID_EX_pre__out),
    .Predict_PC(btb_1_predict_pc), .pre_num(btb_1_pre_num), .jmp(btb_1_jmp));
  ROM #(.addrWidth(10), .dataWidth(32)) rom_1 (.addr(PC_q[11:2]), .data(rom_1_data), .sel(1'b1));
  Hex_Digit_Display hex_digit_display_5 (.value(register_1_q[11:8]));  // open: dp
  Hex_Digit_Display hex_digit_display_6 (.value(register_1_q[15:12]));  // open: dp
  Counter #(.width(16), .max('hffff)) counter_2 (
    .count(main_1_bubble), .Q(counter_2_q), .clk(and_3_out));  // open: load, D, carry, clr
  Counter #(.width(16), .max('hffff)) counter_3 (
    .count(Pre_wrong), .Q(counter_3_q), .clk(and_3_out));  // open: load, D, carry, clr
  Counter #(.width(16), .max('hffff)) counter_4 (
    .count(Pre_success), .Q(counter_4_q), .clk(and_3_out));  // open: load, D, carry, clr
  Counter #(.width(16), .max('hffff)) counter_5 (
    .count(no_pre), .Q(counter_5_q), .clk(and_3_out));  // open: load, D, carry, clr
  Counter #(.width(16), .max('hffff)) counter_6 (
    .count(jmp_count), .Q(counter_6_q), .clk(and_3_out));  // open: load, D, carry, clr
  Adder #(.width(16)) adder_1 (.a(PCcount), .b(multiplexer_2_out), .out(\总周期数 ));  // open: cin, cout
  IF_ID IF_ID (
    .PC_in(PC_q), .PC_out(IF_ID_pc_out), .PC_4_in(btb_1_predict_pc), .PC_4_out(IF_ID_pc_4_out),
    .IR_in(rom_1_data), .IR_out(IF_ID_ir_out), .E(or_2_out), .in_7(instr_fetch_wrong), .clk(clk),
    .clear(clear1), .Pre__in(btb_1_pre_num), .Pre__out(IF_ID_pre__out), .jmp_in(btb_1_jmp),
    .jmp_out(IF_ID_jmp_out));
  Hex_Digit_Display hex_digit_display_7 (.value(register_1_q[7:4]));  // open: dp
  Hex_Digit_Display hex_digit_display_8 (.value(register_1_q[3:0]));  // open: dp
  // Probe on counter_2_q
  // Probe on counter_3_q
  // Probe on counter_4_q
  // Probe on counter_5_q
  // Probe on counter_6_q
  // Probe on \总周期数 
  // Probe on IF_ID_pc_out
  // Probe on IF_ID_ir_out
  decode_main decode (
    .in_1(IF_ID_ir_out), .OP(decode_op), .rs(decode_rs), .rt(decode_rt), .rd(decode_rd),
    .shamt(decode_shamt), .funct(decode_funct), .imm(decode_imm), .addr(decode_addr));
  reg_read_detect_main main_1 (
    .OP(decode_op), .funct(decode_funct), .syscall(main_2_syscall), .WE1(ID_EX_regwrite_out),
    .WE2(EX_MEM_regwrite_out), .MemRead(ID_EX_memread_2), .RW_1(ID_EX_rw__out), .RW_2(EX_MEM_rw__out),
    .R1_num(multiplexer_3_out), .R2_num(decode_rt), .PCcount(PCcount), .bubble(main_1_bubble),
    .sel_R1(main_1_sel_r1), .sel_R2(main_1_sel_r2), .sel_v0(main_1_sel_v0), .sel_a0(main_1_sel_a0));
  control_unit_main main_2 (
    .OP(decode_op), .funct(decode_funct), .Rf_R1(main_2_rf_r1), .PC(main_2_pc), .RF_Din(main_2_rf_din),
    .RF_W(main_2_rf_w), .MemWrite(main_2_memwrite), .ALU_B(main_2_alu_b), .RegWrite(main_2_regwrite),
    .ALU_OP(main_2_alu_op), .Branch(main_2_branch), .Hi_Lo(main_2_hi_lo), .syscall(main_2_syscall),
    .MemRead(main_2_memread));
  Multiplexer #(.width(5)) multiplexer_3 (
    .in0(decode_rs), .in1(decode_rt), .out(multiplexer_3_out), .sel(main_2_rf_r1), .en(1'b1));
  not not_4 (not_4_out, clk);
  Multiplexer #(.select(2), .width(5)) multiplexer_4 (
    .in0(decode_rd), .in1(decode_rt), .in2({5{1'b1}}), .out(multiplexer_4_out), .sel(main_2_rf_w), .en(1'b1));  // open: in3
  Multiplexer #(.select(3), .width(32)) multiplexer_5 (
    .in0(ALU_out), .in1(Lo), .in2(Hi), .in3(DM_out), .in4(MEM_WB_pc_4_out), .out(multiplexer_5_out),
    .sel(RF_Din), .en(1'b1));  // open: in5, in6, in7
  // Probe on main_3_s0_value
  // Probe on main_3_s1_value
  // Probe on main_3_s2_value
  // Probe on main_3_ra_value
  // Probe on main_3_v0_value
  // Probe on main_3_a0_value
  regfile_main main_3 (
    .Reg1_num(multiplexer_3_out), .Reg2_num(decode_rt), .Write_Reg_num(RW_num), .Din(multiplexer_5_out),
    .Write_Enable(WE), .Clock(not_4_out), .Reg1(main_3_reg1), .Reg2(main_3_reg2), .s0_Value(main_3_s0_value),
    .s1_Value(main_3_s1_value), .s2_Value(main_3_s2_value), .ra_Value(main_3_ra_value),
    .v0_Value(main_3_v0_value), .a0_Value(main_3_a0_value));
  ID_EX ID_EX (
    .PC_in(IF_ID_pc_out), .selPC_in(main_2_pc), .RW__in(multiplexer_4_out), .RF_Din_in(main_2_rf_din),
    .ALU_B_in(main_2_alu_b), .ALU_OP_in(main_2_alu_op), .MemWrite_in(main_2_memwrite),
    .RegWrite_in(main_2_regwrite), .Branch_in(main_2_branch), .LOHI_in(main_2_hi_lo),
    .Syscall_in(main_2_syscall), .IMM_in(decode_imm), .Addr_in(decode_addr), .shamt_in(decode_shamt),
    .v0_in(multiplexer_9_out), .a0_in(multiplexer_8_out), .RF_R1_in(multiplexer_7_out),
    .RF_R2_in(multiplexer_6_out), .PC_out(ID_EX_pc_out), .PC_4_out(ID_EX_pc_4_out),
    .selPC_out(ID_EX_selpc_out), .RW__out(ID_EX_rw__out), .RF_Din_out(ID_EX_rf_din_out),
    .ALU_B_out(ID_EX_alu_b_out), .ALU_OP_out(ID_EX_alu_op_out), .MemWrite_out(ID_EX_memwrite_out),
    .RegWrite_out(ID_EX_regwrite_out), .Branch_out(ID_EX_branch_out), .LOHI_out(ID_EX_lohi_out),
    .Syscall_out(ID_EX_syscall_out), .IMM_out(ID_EX_imm_out), .Addr_out(ID_EX_addr_out),
    .shamt_out(ID_EX_shamt_out), .v0_out(ID_EX_v0_out), .a0_out(ID_EX_a0_out), .RF_R1_out(ID_EX_rf_r1_out),
    .RF_R2_out(ID_EX_rf_r2_out), .clk(clk), .clear(clear2), .IR_in(IF_ID_ir_out), .IR_out(ID_EX_ir_out),
    .PC_4_in(IF_ID_pc_4_out), .in_24(or_3_out), .MemRead(main_2_memread), .MemRead_2(ID_EX_memread_2),
    .Pre__in(IF_ID_pre__out), .Pre__out(ID_EX_pre__out), .jmp_in(IF_ID_jmp_out), .jmp_out(ID_EX_jmp_out));
  Multiplexer #(.select(2), .width(32)) multiplexer_6 (
    .in0(main_3_reg2), .in1(EX_BACK), .in2(MEM_BACK), .in3(EX_BACK), .out(multiplexer_6_out),
    .sel(main_1_sel_r2), .en(1'b1));
  Multiplexer #(.select(2), .width(32)) multiplexer_7 (
    .in0(main_3_reg1), .in1(EX_BACK), .in2(MEM_BACK), .in3(EX_BACK), .out(multiplexer_7_out),
    .sel(main_1_sel_r1), .en(1'b1));
  Multiplexer #(.select(2), .width(32)) multiplexer_8 (
    .in0(main_3_a0_value), .in1(EX_BACK), .in2(MEM_BACK), .in3(EX_BACK), .out(multiplexer_8_out),
    .sel(main_1_sel_a0), .en(1'b1));
  Multiplexer #(.select(2), .width(32)) multiplexer_9 (
    .in0(main_3_v0_value), .in1(EX_BACK), .in2(MEM_BACK), .in3(EX_BACK), .out(multiplexer_9_out),
    .sel(main_1_sel_v0), .en(1'b1));
  // Probe on ID_EX_pc_out
  // Probe on ID_EX_ir_out
  assign bit_extender_1_out = {{27{1'b0}}, ID_EX_shamt_out};  // Bit_Extender bit_extender_1
  assign S_EXT = {{16{ID_EX_imm_out[15]}}, ID_EX_imm_out};  // Bit_Extender bit_extender_2
  assign bit_extender_3_out = {{16{1'b0}}, ID_EX_imm_out};  // Bit_Extender bit_extender_3
  or or_3 (or_3_out, main_1_bubble, instr_fetch_wrong);
  Multiplexer #(.select(2), .width(32)) multiplexer_10 (
    .in0(ID_EX_rf_r2_out), .in1(S_EXT), .in2(bit_extender_3_out), .in3(bit_extender_1_out),
    .out(multiplexer_10_out), .sel(ID_EX_alu_b_out), .en(1'b1));
  Comparator #(.width(32), .mode("unsigned")) comparator_1 (
    .a(ID_EX_v0_out), .b(32'ha), .eq(comparator_1_eq));  // open: gt, lt
  ALU alu_1 (
    .AluOP(ID_EX_alu_op_out), .X(ID_EX_rf_r1_out), .Equal(alu_1_equal), .Result(alu_1_result),
    .Y(multiplexer_10_out), .Result_2(alu_1_result_2));  // open: Signed_Overflow, UnSigned_Overflow
  Register #(.width(32), .trigger("falling")) u_Hi (
    .D(alu_1_result_2), .en(ID_EX_lohi_out), .Q(Hi_q), .clk(clk), .clr(clear));
  and and_4 (halt_bubble, ID_EX_syscall_out, comparator_1_eq);
  jmp_detect jmp_detect_1 (
    .selPC(ID_EX_selpc_out), .Branch(ID_EX_branch_out), .equal(alu_1_equal), .Pre_PC(ID_EX_pc_4_out),
    .Addr(ID_EX_addr_out), .S_EXT(S_EXT), .jmp(ID_EX_jmp_out), .RF_R1(ID_EX_rf_r1_out), .PC(ID_EX_pc_out),
    .Corret_PC(jmp_detect_1_corret_pc), .pre_wrong(Pre_wrong), .pre_success(Pre_success),
    .PC_update(jmp_detect_1_pc_update), .instr_fetch_wrong(instr_fetch_wrong), .no_pre(no_pre),
    .jmp_count(jmp_count));
  Register #(.width(32), .trigger("falling")) u_Lo (
    .D(alu_1_result), .en(ID_EX_lohi_out), .Q(Lo_q), .clk(clk), .clr(clear));
  EX_MEM EX_MEM (
    .PC_in(ID_EX_pc_out), .PC_4_in(ID_EX_pc_4_out), .IR_in(ID_EX_ir_out), .selPC_in(ID_EX_selpc_out),
    .RW__in(ID_EX_rw__out), .RF_Din_in(ID_EX_rf_din_out), .MemWrite_in(ID_EX_memwrite_out),
    .RegWrite_in(ID_EX_regwrite_out), .Lo_in(Lo_q), .Hi_in(Hi_q), .halt_in(halt_bubble),
    .ALU_out_in(alu_1_result), .RF_R2_in(ID_EX_rf_r2_out), .PC_out(EX_MEM_pc_out),
    .PC_4_out(EX_MEM_pc_4_out), .IR_out(EX_MEM_ir_out), .selPC_out(EX_MEM_selpc_out),
    .RW__out(EX_MEM_rw__out), .RF_Din_out(EX_MEM_rf_din_out), .MemWrite_out(EX_MEM_memwrite_out),
    .RegWrite_out(EX_MEM_regwrite_out), .Lo_out(EX_MEM_lo_out), .Hi_out(EX_MEM_hi_out),
    .halt_out(EX_MEM_halt_out), .ALU_out_out(EX_MEM_alu_out_out), .RF_R2_out(EX_MEM_rf_r2_out), .clk(clk),
    .clear(clear3), .MemRead(ID_EX_memread_2), .MemRead_2(EX_MEM_memread_2));  // open: Branch_in, equal_in, S_EXT_in, Addr_in, RF_R1_in, Branch_out, equal_out, S_EXT_out, Addr_out, RF_R1_out
  data_redirection data_redirection_1 (
    .ALU_R1(alu_1_result), .Lo(Lo_q), .Hi(Hi_q), .PC_4(PC_4), .RF_Din(ID_EX_rf_din_out), .out_7(EX_BACK));  // open: DM_out
  // Probe on EX_MEM_pc_out
  // Probe on EX_MEM_ir_out
  RAM #(.addrWidth(10), .dataWidth(32), .bus("separate")) ram_1 (
    .addr(EX_MEM_alu_out_out[11:2]), .din(EX_MEM_rf_r2_out), .data(ram_1_data), .str(EX_MEM_memwrite_out),
    .clk(clk), .ld(EX_MEM_memread_2));  // open: sel, clr
  MEM_WB MEM_WB (
    .PC_in(EX_MEM_pc_out), .PC_4_in(EX_MEM_pc_4_out), .IR_in(EX_MEM_ir_out), .selPC_in(EX_MEM_selpc_out),
    .RW__in(EX_MEM_rw__out), .RF_Din_in(EX_MEM_rf_din_out), .DM_out_in(ram_1_data),
    .RegWrite_in(EX_MEM_regwrite_out), .Lo_in(EX_MEM_lo_out), .Hi_in(EX_MEM_hi_out),
    .halt_in(EX_MEM_halt_out), .ALU_out_in(EX_MEM_alu_out_out), .PC_out(MEM_WB_pc_out),
    .PC_4_out(MEM_WB_pc_4_out), .IR_out(MEM_WB_ir_out), .RW__out(RW_num), .RF_Din_out(RF_Din),
    .DM_out_out(DM_out), .RegWrite_out(WE), .Lo_out(Lo), .Hi_out(Hi), .halt_out(halt), .ALU_out_out(ALU_out),
    .clk(clk), .clear(clear4));  // open: Branch_in, equal_in, S_EXT_in, Addr_in, RF_R1_in, selPC_out, Branch_out, equal_out, S_EXT_out, Addr_out, RF_R1_out
  data_redirection data_redirection_2 (
    .ALU_R1(EX_MEM_alu_out_out), .Lo(EX_MEM_lo_out), .Hi(EX_MEM_hi_out), .DM_out(ram_1_data),
    .PC_4(EX_MEM_pc_4_out), .RF_Din(EX_MEM_rf_din_out), .out_7(MEM_BACK));
  // Probe on MEM_WB_pc_out
  // Probe on MEM_WB_ir_out

  // Notes on the sheet:
  //   contents of rom_1 (hex, n*v repeats v):
  //   2010ffff 20110000 ae300000 22100001 22310004 ae300000 22100001 22310004 ae300000 22100001 22310004
  //   ae300000 22100001 22310004 ae300000 22100001 22310004 ae300000 22100001 22310004 ae300000 22100001
  //   22310004 ae300000 22100001 22310004 ae300000 22100001 22310004 ae300000 22100001 22310004 ae300000
  //   22100001 22310004 ae300000 22100001 22310004 ae300000 22100001 22310004 ae300000 22100001 22310004
  //   ae300000 22100001 22310004 ae300000 22100001 22310004 22100001 8020 2011003c 8e130000 8e340000
  //   274402a 11000002 ae330000 ae140000 2231fffc 1611fff8 102020 20020022 c 22100004 2011003c 1611fff2
  //   2002000a c
  //   R2
  //   R1
  //   a0
  //   v0
endmodule

module IF_ID (
  input  jmp_in,
  input  [1:0] Pre__in,
  input  [31:0] PC_in,
  input  [31:0] PC_4_in,
  input  [31:0] IR_in,
  input  E,
  input  in_7,
  input  clk,
  input  clear,
  output jmp_out,
  output [1:0] Pre__out,
  output [31:0] PC_out,
  output [31:0] PC_4_out,
  output [31:0] IR_out
);

  wire multiplexer_1_out;
  wire [1:0] multiplexer_2_out;
  wire [31:0] multiplexer_3_out, multiplexer_4_out, multiplexer_5_out;

  Multiplexer multiplexer_1 (.in0(jmp_in), .in1(1'b0), .out(multiplexer_1_out), .sel(in_7), .en(1'b1));
  Multiplexer #(.width(2)) multiplexer_2 (.in0(Pre__in), .in1(2'b00), .out(multiplexer_2_out), .sel(in_7), .en(1'b1));
  Multiplexer #(.width(32)) multiplexer_3 (
    .in0(PC_in), .in1({32{1'b0}}), .out(multiplexer_3_out), .sel(in_7), .en(1'b1));
  Multiplexer #(.width(32)) multiplexer_4 (
    .in0(PC_4_in), .in1({32{1'b0}}), .out(multiplexer_4_out), .sel(in_7), .en(1'b1));
  Multiplexer #(.width(32)) multiplexer_5 (
    .in0(IR_in), .in1({32{1'b0}}), .out(multiplexer_5_out), .sel(in_7), .en(1'b1));
  Register #(.width(1)) register_1 (.D(multiplexer_1_out), .en(E), .Q(jmp_out), .clk(clk), .clr(clear));
  Register #(.width(2)) register_2 (.D(multiplexer_2_out), .en(E), .Q(Pre__out), .clk(clk), .clr(clear));
  Register #(.width(32)) register_3 (.D(multiplexer_3_out), .en(E), .Q(PC_out), .clk(clk), .clr(clear));
  Register #(.width(32)) register_4 (.D(multiplexer_4_out), .en(E), .Q(PC_4_out), .clk(clk), .clr(clear));
  Register #(.width(32)) register_5 (.D(multiplexer_5_out), .en(E), .Q(IR_out), .clk(clk), .clr(clear));
endmodule

module ID_EX (
  input  jmp_in,
  input  [1:0] Pre__in,
  input  [31:0] PC_in,
  input  [31:0] PC_4_in,
  input  [31:0] IR_in,
  input  [1:0] selPC_in,
  input  [4:0] RW__in,
  input  [2:0] RF_Din_in,
  input  [1:0] ALU_B_in,
  input  [3:0] ALU_OP_in,
  input  MemWrite_in,
  input  RegWrite_in,
  input  Branch_in,
  input  LOHI_in,
  input  Syscall_in,
  input  [15:0] IMM_in,
  input  [25:0] Addr_in,
  input  [4:0] shamt_in,
  input  [31:0] v0_in,
  input  [31:0] a0_in,
  input  [31:0] RF_R1_in,
  input  [31:0] RF_R2_in,
  input  MemRead,
  input  in_24,
  input  clk,
  input  clear,
  output jmp_out,
  output [1:0] Pre__out,
  output [31:0] PC_out,
  output [31:0] PC_4_out,
  output [31:0] IR_out,
  output [1:0] selPC_out,
  output [4:0] RW__out,
  output [2:0] RF_Din_out,
  output [1:0] ALU_B_out,
  output [3:0] ALU_OP_out,
  output MemWrite_out,
  output RegWrite_out,
  output Branch_out,
  output LOHI_out,
  output Syscall_out,
  output [15:0] IMM_out,
  output [25:0] Addr_out,
  output [4:0] shamt_out,
  output [31:0] v0_out,
  output [31:0] a0_out,
  output [31:0] RF_R1_out,
  output [31:0] RF_R2_out,
  output MemRead_2
);

  wire multiplexer_1_out, multiplexer_11_out, multiplexer_12_out, multiplexer_13_out, multiplexer_14_out,
       multiplexer_15_out, multiplexer_23_out;
  wire [1:0] multiplexer_2_out, multiplexer_6_out, multiplexer_9_out;
  wire [2:0] multiplexer_8_out;
  wire [3:0] multiplexer_10_out;
  wire [4:0] multiplexer_7_out, multiplexer_18_out;
  wire [15:0] multiplexer_16_out;
  wire [25:0] multiplexer_17_out;
  wire [31:0] multiplexer_3_out, multiplexer_4_out, multiplexer_5_out, multiplexer_19_out,
       multiplexer_20_out, multiplexer_21_out, multiplexer_22_out;

  Multiplexer multiplexer_1 (.in0(jmp_in), .in1(1'b0), .out(multiplexer_1_out), .sel(in_24), .en(1'b1));
  Multiplexer #(.width(2)) multiplexer_2 (.in0(Pre__in), .in1(2'b00), .out(multiplexer_2_out), .sel(in_24), .en(1'b1));
  Multiplexer #(.width(32)) multiplexer_3 (
    .in0(PC_in), .in1({32{1'b0}}), .out(multiplexer_3_out), .sel(in_24), .en(1'b1));
  Multiplexer #(.width(32)) multiplexer_4 (
    .in0(PC_4_in), .in1({32{1'b0}}), .out(multiplexer_4_out), .sel(in_24), .en(1'b1));
  Multiplexer #(.width(32)) multiplexer_5 (
    .in0(IR_in), .in1({32{1'b0}}), .out(multiplexer_5_out), .sel(in_24), .en(1'b1));
  Multiplexer #(.width(2)) multiplexer_6 (.in0(selPC_in), .in1(2'b00), .out(multiplexer_6_out), .sel(in_24), .en(1'b1));
  Multiplexer #(.width(5)) multiplexer_7 (
    .in0(RW__in), .in1({5{1'b0}}), .out(multiplexer_7_out), .sel(in_24), .en(1'b1));
  Multiplexer #(.width(3)) multiplexer_8 (
    .in0(RF_Din_in), .in1(3'b000), .out(multiplexer_8_out), .sel(in_24), .en(1'b1));
  Multiplexer #(.width(2)) multiplexer_9 (.in0(ALU_B_in), .in1(2'b00), .out(multiplexer_9_out), .sel(in_24), .en(1'b1));
  Multiplexer #(.width(4)) multiplexer_10 (
    .in0(ALU_OP_in), .in1(4'b0000), .out(multiplexer_10_out), .sel(in_24), .en(1'b1));
  Multiplexer multiplexer_11 (.in0(MemWrite_in), .in1(1'b0), .out(multiplexer_11_out), .sel(in_24), .en(1'b1));
  Multiplexer multiplexer_12 (.in0(RegWrite_in), .in1(1'b0), .out(multiplexer_12_out), .sel(in_24), .en(1'b1));
  Multiplexer multiplexer_13 (.in0(Branch_in), .in1(1'b0), .out(multiplexer_13_out), .sel(in_24), .en(1'b1));
  Multiplexer multiplexer_14 (.in0(LOHI_in), .in1(1'b0), .out(multiplexer_14_out), .sel(in_24), .en(1'b1));
  Multiplexer multiplexer_15 (.in0(Syscall_in), .in1(1'b0), .out(multiplexer_15_out), .sel(in_24), .en(1'b1));
  Multiplexer #(.width(16)) multiplexer_16 (
    .in0(IMM_in), .in1({16{1'b0}}), .out(multiplexer_16_out), .sel(in_24), .en(1'b1));
  Multiplexer #(.width(26)) multiplexer_17 (
    .in0(Addr_in), .in1({26{1'b0}}), .out(multiplexer_17_out), .sel(in_24), .en(1'b1));
  Multiplexer #(.width(5)) multiplexer_18 (
    .in0(shamt_in), .in1({5{1'b0}}), .out(multiplexer_18_out), .sel(in_24), .en(1'b1));
  Multiplexer #(.width(32)) multiplexer_19 (
    .in0(v0_in), .in1({32{1'b0}}), .out(multiplexer_19_out), .sel(in_24), .en(1'b1));
  Multiplexer #(.width(32)) multiplexer_20 (
    .in0(a0_in), .in1({32{1'b0}}), .out(multiplexer_20_out), .sel(in_24), .en(1'b1));
  Multiplexer #(.width(32)) multiplexer_21 (
    .in0(RF_R1_in), .in1({32{1'b0}}), .out(multiplexer_21_out), .sel(in_24), .en(1'b1));
  Multiplexer #(.width(32)) multiplexer_22 (
    .in0(RF_R2_in), .in1({32{1'b0}}), .out(multiplexer_22_out), .sel(in_24), .en(1'b1));
  Multiplexer multiplexer_23 (.in0(MemRead), .in1(1'b0), .out(multiplexer_23_out), .sel(in_24), .en(1'b1));
  Register #(.width(1)) register_1 (.D(multiplexer_1_out), .en(1'b1), .Q(jmp_out), .clk(clk), .clr(clear));
  Register #(.width(2)) register_2 (.D(multiplexer_2_out), .en(1'b1), .Q(Pre__out), .clk(clk), .clr(clear));
  Register #(.width(32)) register_3 (.D(multiplexer_3_out), .en(1'b1), .Q(PC_out), .clk(clk), .clr(clear));
  Register #(.width(32)) register_4 (.D(multiplexer_4_out), .en(1'b1), .Q(PC_4_out), .clk(clk), .clr(clear));
  Register #(.width(32)) register_5 (.D(multiplexer_5_out), .en(1'b1), .Q(IR_out), .clk(clk), .clr(clear));
  Register #(.width(2)) register_6 (.D(multiplexer_6_out), .en(1'b1), .Q(selPC_out), .clk(clk), .clr(clear));
  Register #(.width(5)) register_7 (.D(multiplexer_7_out), .en(1'b1), .Q(RW__out), .clk(clk), .clr(clear));
  Register #(.width(3)) register_8 (.D(multiplexer_8_out), .en(1'b1), .Q(RF_Din_out), .clk(clk), .clr(clear));
  Register #(.width(2)) register_9 (.D(multiplexer_9_out), .en(1'b1), .Q(ALU_B_out), .clk(clk), .clr(clear));
  Register #(.width(4)) register_10 (.D(multiplexer_10_out), .en(1'b1), .Q(ALU_OP_out), .clk(clk), .clr(clear));
  Register #(.width(1)) register_11 (.D(multiplexer_11_out), .en(1'b1), .Q(MemWrite_out), .clk(clk), .clr(clear));
  Register #(.width(1)) register_12 (.D(multiplexer_12_out), .en(1'b1), .Q(RegWrite_out), .clk(clk), .clr(clear));
  Register #(.width(1)) register_13 (.D(multiplexer_13_out), .en(1'b1), .Q(Branch_out), .clk(clk), .clr(clear));
  Register #(.width(1)) register_14 (.D(multiplexer_14_out), .en(1'b1), .Q(LOHI_out), .clk(clk), .clr(clear));
  Register #(.width(1)) register_15 (.D(multiplexer_15_out), .en(1'b1), .Q(Syscall_out), .clk(clk), .clr(clear));
  Register #(.width(16)) register_16 (.D(multiplexer_16_out), .en(1'b1), .Q(IMM_out), .clk(clk), .clr(clear));
  Register #(.width(26)) register_17 (.D(multiplexer_17_out), .en(1'b1), .Q(Addr_out), .clk(clk), .clr(clear));
  Register #(.width(5)) register_18 (.D(multiplexer_18_out), .en(1'b1), .Q(shamt_out), .clk(clk), .clr(clear));
  Register #(.width(32)) register_19 (.D(multiplexer_19_out), .en(1'b1), .Q(v0_out), .clk(clk), .clr(clear));
  Register #(.width(32)) register_20 (.D(multiplexer_20_out), .en(1'b1), .Q(a0_out), .clk(clk), .clr(clear));
  Register #(.width(32)) register_21 (.D(multiplexer_21_out), .en(1'b1), .Q(RF_R1_out), .clk(clk), .clr(clear));
  Register #(.width(32)) register_22 (.D(multiplexer_22_out), .en(1'b1), .Q(RF_R2_out), .clk(clk), .clr(clear));
  Register #(.width(1)) register_23 (.D(multiplexer_23_out), .en(1'b1), .Q(MemRead_2), .clk(clk), .clr(clear));
endmodule

module EX_MEM (
  input  [31:0] PC_in,
  input  [31:0] PC_4_in,
  input  [31:0] IR_in,
  input  [1:0] selPC_in,
  input  [4:0] RW__in,
  input  [2:0] RF_Din_in,
  input  MemWrite_in,
  input  RegWrite_in,
  input  [31:0] Lo_in,
  input  [31:0] Hi_in,
  input  Branch_in,
  input  equal_in,
  input  [31:0] S_EXT_in,
  input  halt_in,
  input  [31:0] ALU_out_in,
  input  [25:0] Addr_in,
  input  [31:0] RF_R1_in,
  input  [31:0] RF_R2_in,
  input  MemRead,
  input  clk,
  input  clear,
  output [31:0] PC_out,
  output [31:0] PC_4_out,
  output [31:0] IR_out,
  output [1:0] selPC_out,
  output [4:0] RW__out,
  output [2:0] RF_Din_out,
  output MemWrite_out,
  output RegWrite_out,
  output [31:0] Lo_out,
  output [31:0] Hi_out,
  output Branch_out,
  output equal_out,
  output [31:0] S_EXT_out,
  output halt_out,
  output [31:0] ALU_out_out,
  output [25:0] Addr_out,
  output [31:0] RF_R1_out,
  output [31:0] RF_R2_out,
  output MemRead_2
);

  Register #(.width(32)) register_1 (.D(PC_in), .en(1'b1), .Q(PC_out), .clk(clk), .clr(clear));
  Register #(.width(32)) register_2 (.D(PC_4_in), .en(1'b1), .Q(PC_4_out), .clk(clk), .clr(clear));
  Register #(.width(32)) register_3 (.D(IR_in), .en(1'b1), .Q(IR_out), .clk(clk), .clr(clear));
  Register #(.width(2)) register_4 (.D(selPC_in), .en(1'b1), .Q(selPC_out), .clk(clk), .clr(clear));
  Register #(.width(5)) register_5 (.D(RW__in), .en(1'b1), .Q(RW__out), .clk(clk), .clr(clear));
  Register #(.width(3)) register_6 (.D(RF_Din_in), .en(1'b1), .Q(RF_Din_out), .clk(clk), .clr(clear));
  Register #(.width(1)) register_7 (.D(MemWrite_in), .en(1'b1), .Q(MemWrite_out), .clk(clk), .clr(clear));
  Register #(.width(1)) register_8 (.D(RegWrite_in), .en(1'b1), .Q(RegWrite_out), .clk(clk), .clr(clear));
  Register #(.width(32)) register_9 (.D(Lo_in), .en(1'b1), .Q(Lo_out), .clk(clk), .clr(clear));
  Register #(.width(32)) register_10 (.D(Hi_in), .en(1'b1), .Q(Hi_out), .clk(clk), .clr(clear));
  Register #(.width(1)) register_11 (.D(Branch_in), .en(1'b1), .Q(Branch_out), .clk(clk), .clr(clear));
  Register #(.width(1)) register_12 (.D(equal_in), .en(1'b1), .Q(equal_out), .clk(clk), .clr(clear));
  Register #(.width(32)) register_13 (.D(S_EXT_in), .en(1'b1), .Q(S_EXT_out), .clk(clk), .clr(clear));
  Register #(.width(1)) register_14 (.D(halt_in), .en(1'b1), .Q(halt_out), .clk(clk), .clr(clear));
  Register #(.width(32)) register_15 (.D(ALU_out_in), .en(1'b1), .Q(ALU_out_out), .clk(clk), .clr(clear));
  Register #(.width(26)) register_16 (.D(Addr_in), .en(1'b1), .Q(Addr_out), .clk(clk), .clr(clear));
  Register #(.width(32)) register_17 (.D(RF_R1_in), .en(1'b1), .Q(RF_R1_out), .clk(clk), .clr(clear));
  Register #(.width(32)) register_18 (.D(RF_R2_in), .en(1'b1), .Q(RF_R2_out), .clk(clk), .clr(clear));
  Register #(.width(1)) register_19 (.D(MemRead), .en(1'b1), .Q(MemRead_2), .clk(clk), .clr(clear));
endmodule

module MEM_WB (
  input  [31:0] PC_in,
  input  [31:0] PC_4_in,
  input  [31:0] IR_in,
  input  [1:0] selPC_in,
  input  [4:0] RW__in,
  input  [2:0] RF_Din_in,
  input  [31:0] DM_out_in,
  input  RegWrite_in,
  input  [31:0] Lo_in,
  input  [31:0] Hi_in,
  input  Branch_in,
  input  equal_in,
  input  [31:0] S_EXT_in,
  input  halt_in,
  input  [31:0] ALU_out_in,
  input  [25:0] Addr_in,
  input  [31:0] RF_R1_in,
  input  clk,
  input  clear,
  output [31:0] PC_out,
  output [31:0] PC_4_out,
  output [31:0] IR_out,
  output [1:0] selPC_out,
  output [4:0] RW__out,
  output [2:0] RF_Din_out,
  output [31:0] DM_out_out,
  output RegWrite_out,
  output [31:0] Lo_out,
  output [31:0] Hi_out,
  output Branch_out,
  output equal_out,
  output [31:0] S_EXT_out,
  output halt_out,
  output [31:0] ALU_out_out,
  output [25:0] Addr_out,
  output [31:0] RF_R1_out
);

  Register #(.width(32)) register_1 (.D(PC_in), .en(1'b1), .Q(PC_out), .clk(clk), .clr(clear));
  Register #(.width(32)) register_2 (.D(PC_4_in), .en(1'b1), .Q(PC_4_out), .clk(clk), .clr(clear));
  Register #(.width(32)) register_3 (.D(IR_in), .en(1'b1), .Q(IR_out), .clk(clk), .clr(clear));
  Register #(.width(2)) register_4 (.D(selPC_in), .en(1'b1), .Q(selPC_out), .clk(clk), .clr(clear));
  Register #(.width(5)) register_5 (.D(RW__in), .en(1'b1), .Q(RW__out), .clk(clk), .clr(clear));
  Register #(.width(3)) register_6 (.D(RF_Din_in), .en(1'b1), .Q(RF_Din_out), .clk(clk), .clr(clear));
  Register #(.width(32)) register_7 (.D(DM_out_in), .en(1'b1), .Q(DM_out_out), .clk(clk), .clr(clear));
  Register #(.width(1)) register_8 (.D(RegWrite_in), .en(1'b1), .Q(RegWrite_out), .clk(clk), .clr(clear));
  Register #(.width(32)) register_9 (.D(Lo_in), .en(1'b1), .Q(Lo_out), .clk(clk), .clr(clear));
  Register #(.width(32)) register_10 (.D(Hi_in), .en(1'b1), .Q(Hi_out), .clk(clk), .clr(clear));
  Register #(.width(1)) register_11 (.D(Branch_in), .en(1'b1), .Q(Branch_out), .clk(clk), .clr(clear));
  Register #(.width(1)) register_12 (.D(equal_in), .en(1'b1), .Q(equal_out), .clk(clk), .clr(clear));
  Register #(.width(32)) register_13 (.D(S_EXT_in), .en(1'b1), .Q(S_EXT_out), .clk(clk), .clr(clear));
  Register #(.width(1)) register_14 (.D(halt_in), .en(1'b1), .Q(halt_out), .clk(clk), .clr(clear));
  Register #(.width(32)) register_15 (.D(ALU_out_in), .en(1'b1), .Q(ALU_out_out), .clk(clk), .clr(clear));
  Register #(.width(26)) register_16 (.D(Addr_in), .en(1'b1), .Q(Addr_out), .clk(clk), .clr(clear));
  Register #(.width(32)) register_17 (.D(RF_R1_in), .en(1'b1), .Q(RF_R1_out), .clk(clk), .clr(clear));
endmodule

module jmp_detect (
  input  [1:0] selPC,
  input  Branch,
  input  equal,
  input  [31:0] Pre_PC,
  input  [25:0] Addr,
  input  [31:0] S_EXT,
  input  jmp,
  input  [31:0] RF_R1,
  input  [31:0] PC,
  output [31:0] Corret_PC,
  output pre_wrong,
  output pre_success,
  output [1:0] PC_update,
  output instr_fetch_wrong,
  output no_pre,
  output jmp_count
);

  wire and_1_out, comparator_1_eq, comparator_2_eq, comparator_3_eq, multiplexer_1_out, multiplexer_2_out,
       not_1_out, not_2_out, not_3_out, not_5_out, or_1_out;
  wire [31:0] adder_1_out, multiplexer_3_out, PC_4, shifter_1_out;

  Shifter #(.width(32)) shifter_1 (.in(S_EXT), .\dist (5'b00010), .out(shifter_1_out));
  not not_1 (not_1_out, equal);
  Adder #(.width(32)) adder_1 (.a(shifter_1_out), .b(PC_4), .out(adder_1_out), .cin(1'b0));  // open: cout
  Comparator #(.width(2)) comparator_1 (.a(selPC), .b(2'b00), .eq(comparator_1_eq));  // open: gt, lt
  Comparator #(.width(2)) comparator_2 (.a(selPC), .b(2'b01), .eq(comparator_2_eq));  // open: gt, lt
  Multiplexer multiplexer_1 (.in0(equal), .in1(not_1_out), .out(multiplexer_1_out), .sel(Branch), .en(1'b1));
  Multiplexer multiplexer_2 (.in0(equal), .in1(not_2_out), .out(multiplexer_2_out), .sel(Branch), .en(1'b1));
  not not_2 (not_2_out, equal);
  Multiplexer #(.width(32)) multiplexer_3 (
    .in0(PC_4), .in1(adder_1_out), .out(multiplexer_3_out), .sel(multiplexer_2_out), .en(1'b1));
  and and_1 (and_1_out, comparator_2_eq, ~multiplexer_1_out);  // AND_Gate
  Multiplexer #(.select(2), .width(32)) multiplexer_4 (
    .in0(PC_4), .in1(multiplexer_3_out), .in2({Pre_PC[31:28], Addr, 2'b00}), .in3(RF_R1), .out(Corret_PC),
    .sel(selPC), .en(1'b1));
  or or_1 (or_1_out, comparator_1_eq, and_1_out);
  not not_3 (not_3_out, jmp);
  not not_4 (jmp_count, or_1_out);
  Comparator #(.width(32), .mode("unsigned")) comparator_3 (
    .a(Corret_PC), .b(Pre_PC), .eq(comparator_3_eq));  // open: gt, lt
  and and_2 (no_pre, not_3_out, jmp_count);
  not not_5 (not_5_out, comparator_3_eq);
  Adder #(.width(32)) adder_2 (.a(PC), .b(32'h4), .out(PC_4), .cin(1'b0));  // open: cout
  and and_3 (PC_update[0], not_5_out, jmp);
  and and_4 (pre_success, comparator_3_eq, jmp);
  or or_2 (instr_fetch_wrong, no_pre, PC_update[0]);

  assign PC_update[1] = no_pre;
  assign pre_wrong = PC_update[0];
endmodule

module data_redirection (
  input  [31:0] ALU_R1,
  input  [31:0] Lo,
  input  [31:0] Hi,
  input  [31:0] DM_out,
  input  [31:0] PC_4,
  input  [2:0] RF_Din,
  output [31:0] out_7
);

  Multiplexer #(.select(3), .width(32), .enable("false")) multiplexer_1 (
    .in0(ALU_R1), .in1(Lo), .in2(Hi), .in3(DM_out), .in4(PC_4), .out(out_7), .sel(RF_Din));  // open: in5, in6, in7
endmodule

module BTB (
  input  [1:0] pc_update,
  input  [31:0] Current_PC,
  input  [31:0] Back_PC,
  input  clk,
  input  clear,
  input  [31:0] Current_IR,
  input  [31:0] Branch_PC,
  input  [1:0] Wrong_num,
  output [31:0] Predict_PC,
  output [1:0] pre_num,
  output jmp
);

  wire _1write, _2write, _3write, _4write, add1, add2, add3, add4, and_1_out, and_2_out, and_3_out,
       and_4_out, and_5_out, and_6_out, and_7_out, and_8_out, and_9_out, and_10_out, and_11_out, and_12_out,
       and_13_out, and_14_out, and_15_out, and_16_out, and_17_out, comparator_1_eq, comparator_2_eq,
       comparator_3_eq, comparator_4_eq, comparator_4_gt, comparator_4_lt, comparator_5_eq, comparator_5_gt,
       comparator_5_lt, comparator_6_eq, comparator_6_gt, comparator_6_lt, comparator_7_eq, comparator_7_gt,
       comparator_7_lt, comparator_8_eq, comparator_8_gt, comparator_8_lt, comparator_9_eq, comparator_9_gt,
       comparator_9_lt, comparator_10_eq, comparator_11_eq, comparator_12_eq, comparator_13_eq,
       comparator_14_eq, demultiplexer_1_out0, demultiplexer_1_out1, demultiplexer_1_out2,
       demultiplexer_1_out3, IS_Branch, loss, match, nor_1_out, nor_2_out, nor_3_out, not_1_out, not_2_out,
       not_3_out, not_4_out, not_5_out, not_6_out, not_7_out, not_8_out, not_9_out, or_5_out, or_6_out,
       or_7_out, or_8_out, or_9_out, or_10_out, valid1, valid2, valid3, valid4;
  wire [1:0] compare, state1, state2, state3, state4;
  wire [7:0] count1_q, count2_q, count3_q, count4_q;
  wire [31:0] adder_1_out, multiplexer_1_out, PC1, PC2, PC3, PC4, Pre_PC1, Pre_PC2, Pre_PC3, Pre_PC4;

  not not_1 (not_1_out, pc_update[0]);
  Demultiplexer #(.select(2)) demultiplexer_1 (
    .out0(demultiplexer_1_out0), .out1(demultiplexer_1_out1), .out2(demultiplexer_1_out2),
    .out3(demultiplexer_1_out3), .in(pc_update[0]), .sel(Wrong_num), .en(1'b1));
  Comparator #(.width(32)) comparator_1 (.a(Back_PC), .b(PC1), .eq(comparator_1_eq));  // open: gt, lt
  not not_2 (not_2_out, _1write);
  not not_3 (not_3_out, _2write);
  not not_4 (not_4_out, _3write);
  not not_5 (not_5_out, _4write);
  Register #(.width(32)) u_PC1 (.D(Back_PC), .en(_1write), .Q(PC1), .clk(clk), .clr(clear));
  Register #(.width(1)) u_valid1 (.D(1'b1), .en(_1write), .Q(valid1), .clk(clk), .clr(clear));
  Register #(.width(32)) u_Pre_PC1 (.D(Branch_PC), .en(_1write), .Q(Pre_PC1), .clk(clk), .clr(clear));
  not not_6 (not_6_out, comparator_1_eq);
  and and_1 (and_1_out, not_6_out, valid1);
  Counter #(.ongoal("stay")) count1 (
    .load(_1write), .D({8{1'b0}}), .count(not_2_out), .Q(count1_q), .clk(clk), .clr(clear));  // open: carry
  Counter #(.ongoal("stay")) count2 (
    .load(_2write), .D({8{1'b0}}), .count(not_3_out), .Q(count2_q), .clk(clk), .clr(clear));  // open: carry
  Counter #(.ongoal("stay")) count3 (
    .load(_3write), .D({8{1'b0}}), .count(not_4_out), .Q(count3_q), .clk(clk), .clr(clear));  // open: carry
  Counter #(.ongoal("stay")) count4 (
    .load(_4write), .D({8{1'b0}}), .count(not_5_out), .Q(count4_q), .clk(clk), .clr(clear));  // open: carry
  Comparator #(.width(32), .mode("unsigned")) comparator_2 (
    .a(Current_PC), .b(PC1), .eq(comparator_2_eq));  // open: gt, lt
  _2bit_state_machine u_2bit_state_machine_1 (
    .success(not_1_out), .clk(clk), .enable(_1write), .clear(clear), .state_out(state1));
  and and_2 (and_2_out, pc_update[1], add4);
  and and_3 (and_3_out, pc_update[1], add3);
  and and_4 (and_4_out, pc_update[1], add2);
  and and_5 (and_5_out, pc_update[1], add1);
  or or_1 (_4write, demultiplexer_1_out0, and_2_out);
  or or_2 (_3write, demultiplexer_1_out1, and_3_out);
  or or_3 (_2write, demultiplexer_1_out2, and_4_out);
  or or_4 (_1write, demultiplexer_1_out3, and_5_out);
  and and_6 (and_6_out, comparator_2_eq, valid1, state1[1]);
  Comparator #(.width(32)) comparator_3 (.a(Back_PC), .b(PC2), .eq(comparator_3_eq));  // open: gt, lt
  not not_7 (not_7_out, comparator_3_eq);
  or or_5 (or_5_out, comparator_4_gt, comparator_4_eq);
  Comparator comparator_4 (
    .a(count1_q), .b(count2_q), .gt(comparator_4_gt), .eq(comparator_4_eq), .lt(comparator_4_lt));
  or or_6 (or_6_out, comparator_5_gt, comparator_5_eq);
  Comparator comparator_5 (
    .a(count1_q), .b(count3_q), .gt(comparator_5_gt), .eq(comparator_5_eq), .lt(comparator_5_lt));
  or or_7 (or_7_out, comparator_6_gt, comparator_6_eq);
  Comparator comparator_6 (
    .a(count1_q), .b(count4_q), .gt(comparator_6_gt), .eq(comparator_6_eq), .lt(comparator_6_lt));
  or or_8 (or_8_out, comparator_7_gt, comparator_7_eq);
  Comparator comparator_7 (
    .a(count2_q), .b(count3_q), .gt(comparator_7_gt), .eq(comparator_7_eq), .lt(comparator_7_lt));
  or or_9 (or_9_out, comparator_8_gt, comparator_8_eq);
  Comparator comparator_8 (
    .a(count2_q), .b(count4_q), .gt(comparator_8_gt), .eq(comparator_8_eq), .lt(comparator_8_lt));
  or or_10 (or_10_out, comparator_9_gt, comparator_9_eq);
  Comparator comparator_9 (
    .a(count3_q), .b(count4_q), .gt(comparator_9_gt), .eq(comparator_9_eq), .lt(comparator_9_lt));
  Register #(.width(32)) u_PC2 (.D(Back_PC), .en(_2write), .Q(PC2), .clk(clk), .clr(clear));
  Register #(.width(1)) u_valid2 (.D(1'b1), .en(_2write), .Q(valid2), .clk(clk), .clr(clear));
  _2bit_state_machine u_2bit_state_machine_2 (
    .success(not_1_out), .clk(clk), .enable(_2write), .clear(clear), .state_out(state2));
  Register #(.width(32)) u_Pre_PC2 (.D(Branch_PC), .en(_2write), .Q(Pre_PC2), .clk(clk), .clr(clear));
  and and_7 (and_7_out, not_7_out, valid2);
  Comparator #(.width(32), .mode("unsigned")) comparator_10 (
    .a(Current_PC), .b(PC2), .eq(comparator_10_eq));  // open: gt, lt
  and and_8 (and_8_out, and_1_out, and_7_out, and_14_out, and_16_out);
  and and_9 (and_9_out, and_8_out, or_5_out, or_6_out, or_7_out);
  and and_10 (and_10_out, and_8_out, comparator_4_lt, or_8_out, or_9_out);
  and and_11 (and_11_out, and_8_out, comparator_5_lt, comparator_7_lt, or_10_out);
  and and_12 (and_12_out, comparator_6_lt, comparator_8_lt, and_8_out, comparator_9_lt);
  and and_13 (and_13_out, comparator_10_eq, valid2, state2[1]);
  Comparator #(.width(32)) comparator_11 (.a(Back_PC), .b(PC3), .eq(comparator_11_eq));  // open: gt, lt
  not not_8 (not_8_out, comparator_11_eq);
  or or_11 (add1, ~and_1_out, and_9_out);  // OR_Gate
  Register #(.width(32)) u_PC3 (.D(Back_PC), .en(_3write), .Q(PC3), .clk(clk), .clr(clear));
  Register #(.width(1)) u_valid3 (.D(1'b1), .en(_3write), .Q(valid3), .clk(clk), .clr(clear));
  _2bit_state_machine u_2bit_state_machine_3 (
    .success(not_1_out), .clk(clk), .enable(_3write), .clear(clear), .state_out(state3));
  Register #(.width(32)) u_Pre_PC3 (.D(Branch_PC), .en(_3write), .Q(Pre_PC3), .clk(clk), .clr(clear));
  and and_14 (and_14_out, not_8_out, valid3);
  nor nor_1 (nor_1_out, and_7_out, add1);
  Comparator #(.width(32), .mode("unsigned")) comparator_12 (
    .a(Current_PC), .b(PC3), .eq(comparator_12_eq));  // open: gt, lt
  or or_12 (add2, nor_1_out, and_10_out);
  and and_15 (and_15_out, comparator_12_eq, valid3, state3[1]);
  Comparator #(.width(32)) comparator_13 (.a(Back_PC), .b(PC4), .eq(comparator_13_eq));  // open: gt, lt
  not not_9 (not_9_out, comparator_13_eq);
  nor nor_2 (nor_2_out, and_14_out, add1, add2);
  Register #(.width(32)) u_PC4 (.D(Back_PC), .en(_4write), .Q(PC4), .clk(clk), .clr(clear));
  Register #(.width(1)) u_valid4 (.D(1'b1), .en(_4write), .Q(valid4), .clk(clk), .clr(clear));
  _2bit_state_machine u_2bit_state_machine_4 (
    .success(not_1_out), .clk(clk), .enable(_4write), .clear(clear), .state_out(state4));
  Register #(.width(32)) u_Pre_PC4 (.D(Branch_PC), .en(_4write), .Q(Pre_PC4), .clk(clk), .clr(clear));
  and and_16 (and_16_out, not_9_out, valid4);
  or or_13 (add3, nor_2_out, and_11_out);
  Comparator #(.width(32), .mode("unsigned")) comparator_14 (
    .a(Current_PC), .b(PC4), .eq(comparator_14_eq));  // open: gt, lt
  nor nor_3 (nor_3_out, and_16_out, add1, add2, add3);
  and and_17 (and_17_out, valid4, state4[1], comparator_14_eq);
  or or_14 (add4, nor_3_out, and_12_out);
  assign pre_num = {2{jmp}} & compare;  // AND_Gate and_18, 2 bits wide
  Priority_Encoder #(.select(2)) priority_encoder_1 (
    .in0(and_17_out), .in1(and_15_out), .in2(and_13_out), .in3(and_6_out), .out(compare), .gs(match));  // open: en_out, en_in
  // Probe on compare
  not not_10 (loss, match);
  Branch_IR branch_ir_1 (.Current_IR(Current_IR), .Branch_IR(IS_Branch));
  Adder #(.width(32)) adder_1 (.a(Current_PC), .b(32'h4), .out(adder_1_out), .cin(1'b0));  // open: cout
  Multiplexer #(.select(2), .width(32)) multiplexer_1 (
    .in0(Pre_PC4), .in1(Pre_PC3), .in2(Pre_PC2), .in3(Pre_PC1), .out(multiplexer_1_out), .sel(compare),
    .en(1'b1));
  and and_19 (jmp, IS_Branch, match);
  Multiplexer #(.width(32)) multiplexer_2 (
    .in0(adder_1_out), .in1(multiplexer_1_out), .out(Predict_PC), .sel(jmp), .en(1'b1));

  // Other names for the same wires on the sheet: modify = pc_update[0]; add = pc_update[1]
endmodule

module Branch_IR (
  input  [31:0] Current_IR,
  output Branch_IR
);

  wire and_1_out, comparator_1_eq, comparator_2_eq, comparator_3_eq, comparator_4_eq, comparator_5_eq,
       comparator_6_eq;

  Comparator #(.width(6), .mode("unsigned")) comparator_1 (
    .a(Current_IR[31:26]), .b({6{1'b0}}), .eq(comparator_1_eq));  // open: gt, lt
  Comparator #(.width(6), .mode("unsigned")) comparator_2 (
    .a(Current_IR[5:0]), .b(6'b001000), .eq(comparator_2_eq));  // open: gt, lt
  Comparator #(.width(6), .mode("unsigned")) comparator_3 (
    .a(Current_IR[31:26]), .b(6'b000100), .eq(comparator_3_eq));  // open: gt, lt
  Comparator #(.width(6), .mode("unsigned")) comparator_4 (
    .a(Current_IR[31:26]), .b(6'b000101), .eq(comparator_4_eq));  // open: gt, lt
  Comparator #(.width(6), .mode("unsigned")) comparator_5 (
    .a(Current_IR[31:26]), .b(6'b000010), .eq(comparator_5_eq));  // open: gt, lt
  Comparator #(.width(6), .mode("unsigned")) comparator_6 (
    .a(Current_IR[31:26]), .b(6'b000011), .eq(comparator_6_eq));  // open: gt, lt
  and and_1 (and_1_out, comparator_1_eq, comparator_2_eq);
  or or_1 (Branch_IR, and_1_out, comparator_3_eq, comparator_4_eq, comparator_5_eq, comparator_6_eq);

  // Other names for the same wires on the sheet: funct[5:0] = Current_IR[5:0]; opcode[5:0] = Current_IR[31:26]

  // Notes on the sheet:
  //   jr
  //   beq
  //   bne
  //   j
  //   jal
endmodule

// state4
module _2bit_state_machine (
  input  success,
  input  clk,
  input  enable,
  input  clear,
  output [1:0] state_out
);

  wire and_1_out, and_2_out, and_3_out, or_1_out;

  D_Flip_Flop y2 (.clk(clk), .D(or_1_out), .Q(state_out[1]), .en(enable), .reset(clear));  // open: Qn, preset
  D_Flip_Flop y1 (.clk(clk), .D(success), .Q(state_out[0]), .en(enable), .reset(clear));  // open: Qn, preset
  and and_1 (and_1_out, success, state_out[0]);
  and and_2 (and_2_out, state_out[1], success);
  and and_3 (and_3_out, state_out[1], state_out[0]);
  or or_1 (or_1_out, and_1_out, and_2_out, and_3_out);
endmodule
