// Logisim project accumulate.circ as structural Verilog: 1 circuit, main circuit main
module main (
  input  [31:0] a0,
  input  [31:0] d
);

  wire button, clk_out, comparator_1_gt;
  wire [31:0] ai, multiplexer_1_out, register_2_q, register_3_q, sum, \time ;

  // Probe on button
  // Probe on a0
  // Probe on a0
  Button button_1 (.out(button));
  // Probe on d
  // Probe on d
  Comparator #(.width(32)) comparator_1 (.a(\time ), .b({32{1'b0}}), .gt(comparator_1_gt));  // open: eq, lt
  // Probe on ai
  // Probe on ai
  Multiplexer #(.width(32), .enable("false")) multiplexer_1 (
    .in0(a0), .in1(d), .out(multiplexer_1_out), .sel(comparator_1_gt));
  Register #(.width(32)) register_1 (.D(32'h1), .Q(\time ), .clk(clk_out), .clr(button));  // open: en
  Clock clk (.out(clk_out));
  // Probe on sum
  // Probe on sum
  Register #(.width(32)) register_2 (.D(ai), .en(1'b1), .Q(register_2_q), .clk(clk_out), .clr(button));
  Hex_Digit_Display hex_digit_display_1 (.value(sum[27:24]));  // open: dp
  Hex_Digit_Display hex_digit_display_2 (.value(sum[31:28]));  // open: dp
  ALU alu_1 (
    .AluOP(4'b0101), .X(multiplexer_1_out), .Result(ai), .Y(register_2_q));  // open: Equal, Signed_Overflow, Result_2, UnSigned_Overflow
  Register #(.width(32)) register_3 (.D(sum), .en(1'b1), .Q(register_3_q), .clk(clk_out), .clr(button));
  Hex_Digit_Display hex_digit_display_3 (.value(sum[19:16]));  // open: dp
  Hex_Digit_Display hex_digit_display_4 (.value(sum[23:20]));  // open: dp
  ALU alu_2 (
    .AluOP(4'b0101), .X(register_2_q), .Result(sum), .Y(register_3_q));  // open: Equal, Signed_Overflow, Result_2, UnSigned_Overflow
  Hex_Digit_Display hex_digit_display_5 (.value(sum[15:12]));  // open: dp
  Hex_Digit_Display hex_digit_display_6 (.value(sum[11:8]));  // open: dp
  Hex_Digit_Display hex_digit_display_7 (.value(sum[7:4]));  // open: dp
  Hex_Digit_Display hex_digit_display_8 (.value(sum[3:0]));  // open: dp
endmodule
