// Logisim project alu.backup.circ as structural Verilog: 15 circuits, main circuit ALU
module ALU (
  input  [31:0] X,
  input  [31:0] Y,
  input  [3:0] AluOP,
  output Signed_Overflow,
  output UnSigned_Overflow,
  output Equal,
  output [31:0] Result,
  output [31:0] Result_2
);

  wire CF_0101, CF_0110, OF_0101, OF_0110;
  wire [31:0] addfull_1_result, and_1_result, divide_1_result, multiply_1_result, or_1_result,
       or_not_1_result, Result2_0011, Result2_0100, sar_1_result, shl_1_result, shr_1_result,
       signed_1_rresult, subfull_1_result, unsigned_1_result, xor_1_result;

  // Probe on X
  // Probe on X
  shl shl_1 (.X(X), .Y(Y), .Result(shl_1_result));
  sar sar_1 (.X(X), .Y(Y), .Result(sar_1_result));
  shr shr_1 (.X(X), .Y(Y), .Result(shr_1_result));
  multiply multiply_1 (.X(X), .Y(Y), .Result2(Result2_0011), .Result(multiply_1_result));
  divide divide_1 (.X(X), .Y(Y), .Result2(Result2_0100), .Result(divide_1_result));
  addfull addfull_1 (.X(X), .Y(Y), .Result(addfull_1_result), .OF(OF_0101), .CF(CF_0101));
  subfull subfull_1 (.X(X), .Y(Y), .Result(subfull_1_result), .OF(OF_0110), .CF(CF_0110));
  \and  and_1 (.X(X), .Y(Y), .Result(and_1_result));
  \or  or_1 (.X(X), .Y(Y), .Result(or_1_result));
  \xor  xor_1 (.X(X), .Y(Y), .Result(xor_1_result));
  or_not or_not_1 (.X(X), .Y(Y), .Result(or_not_1_result));
  \signed  signed_1 (.X(X), .Y(Y), .Rresult(signed_1_rresult));
  \unsigned  unsigned_1 (.X(X), .Y(Y), .Result(unsigned_1_result));
  // Probe on Y
  // Probe on Y
  // Probe on AluOP
  // Probe on Result
  // Probe on Result
  Multiplexer #(.select(4), .width(32), .enable("false")) multiplexer_1 (
    .in0(shl_1_result), .in1(sar_1_result), .in2(shr_1_result), .in3(multiply_1_result),
    .in4(divide_1_result), .in5(addfull_1_result), .in6(subfull_1_result), .in7(and_1_result),
    .in8(or_1_result), .in9(xor_1_result), .in10(or_not_1_result), .in11(signed_1_rresult),
    .in12(unsigned_1_result), .in13({32{1'b0}}), .in14({32{1'b0}}), .in15({32{1'b0}}), .out(Result),
    .sel(AluOP));
  // Probe on Result_2
  Comparator #(.width(32), .mode("unsigned")) comparator_1 (.a(X), .b(Y), .eq(Equal));  // open: gt, lt
  Multiplexer #(.select(4), .width(32), .enable("false")) multiplexer_2 (
    .in0({32{1'b0}}), .in1({32{1'b0}}), .in2({32{1'b0}}), .in3(Result2_0011), .in4(Result2_0100),
    .in5({32{1'b0}}), .in6({32{1'b0}}), .in7({32{1'b0}}), .in8({32{1'b0}}), .in9({32{1'b0}}),
    .in10({32{1'b0}}), .in11({32{1'b0}}), .in12({32{1'b0}}), .in13({32{1'b0}}), .in14({32{1'b0}}),
    .in15({32{1'b0}}), .out(Result_2), .sel(AluOP));
  Multiplexer #(.select(4), .enable("false")) multiplexer_3 (
    .in0(1'b0), .in1(1'b0), .in2(1'b0), .in3(1'b0), .in4(1'b0), .in5(OF_0101), .in6(OF_0110), .in7(1'b0),
    .in8(1'b0), .in9(1'b0), .in10(1'b0), .in11(1'b0), .in12(1'b0), .in13(1'b0), .in14(1'b0), .in15(1'b0),
    .out(Signed_Overflow), .sel(AluOP));
  Multiplexer #(.select(4), .enable("false")) multiplexer_4 (
    .in0(1'b0), .in1(1'b0), .in2(1'b0), .in3(1'b0), .in4(1'b0), .in5(CF_0101), .in6(CF_0110), .in7(1'b0),
    .in8(1'b0), .in9(1'b0), .in10(1'b0), .in11(1'b0), .in12(1'b0), .in13(1'b0), .in14(1'b0), .in15(1'b0),
    .out(UnSigned_Overflow), .sel(AluOP));

  // Other names for the same wires on the sheet: CF = UnSigned_Overflow; OF = Signed_Overflow;
  //   Result2[31:0] = Result_2; S[3:0] = AluOP

  // Notes on the sheet:
  //   不要改变此引脚区域内容，也不要改变ALU封装形式
  //   输入引脚
  //   请在下方利用上方输入输出引脚的隧道信号构建ALU电路，ctrl+d复制选择部件
  //   华中科技大学计算机学院 计算机组成原理，鸣谢加州大学伯克利CS61C课程
  //   输出引脚
  //   探测区域
endmodule

module \演示电路  (
  input  [31:0] X,
  input  [31:0] Y,
  input  [3:0] ALUOP,
  output Signed_Overflow,
  output Unsigned_overflow,
  output [31:0] Result,
  output [31:0] Result_2,
  output Equal
);

  // Probe on X
  // Probe on X
  ALU alu_1 (
    .AluOP(ALUOP), .X(X), .Equal(Equal), .Result(Result), .Signed_Overflow(Signed_Overflow), .Y(Y),
    .Result_2(Result_2), .UnSigned_Overflow(Unsigned_overflow));
  // Probe on ALUOP
  // Probe on Y
  // Probe on Y
  // Probe on Result
  // Probe on Result
  // Probe on Result_2
endmodule

module addfull (
  input  [31:0] X,
  input  [31:0] Y,
  output [31:0] Result,
  output OF,
  output CF
);

  wire adder_1_cout;

  Adder #(.width(31)) adder_1 (.a(X[30:0]), .b(Y[30:0]), .out(Result[30:0]), .cin(1'b0), .cout(adder_1_cout));
  Adder #(.width(1)) adder_2 (.a(X[31]), .b(Y[31]), .out(Result[31]), .cin(adder_1_cout), .cout(CF));
  xor xor_1 (OF, adder_1_cout, CF);
endmodule

module subfull (
  input  [31:0] X,
  input  [31:0] Y,
  output [31:0] Result,
  output OF,
  output CF
);

  wire subtractor_1_bout;

  Subtractor #(.width(31)) subtractor_1 (
    .a(X[30:0]), .b(Y[30:0]), .out(Result[30:0]), .bin(1'b0), .bout(subtractor_1_bout));
  Subtractor #(.width(1)) subtractor_2 (.a(X[31]), .b(Y[31]), .out(Result[31]), .bin(subtractor_1_bout), .bout(CF));
  xor xor_1 (OF, subtractor_1_bout, CF);
endmodule

module multiply (
  input  [31:0] X,
  input  [31:0] Y,
  output [31:0] Result2,
  output [31:0] Result
);

  Multiplier #(.width(32)) multiplier_1 (.a(X), .b(Y), .out(Result), .cin({32{1'b0}}), .cout(Result2));
endmodule

module divide (
  input  [31:0] X,
  input  [31:0] Y,
  output [31:0] Result2,
  output [31:0] Result
);

  Divider #(.width(32)) divider_1 (.a(X), .b(Y), .out(Result), .upper({32{1'b0}}), .rem(Result2));
endmodule

module \and  (
  input  [31:0] X,
  input  [31:0] Y,
  output [31:0] Result
);

  assign Result = X & Y;  // AND_Gate and_1, 32 bits wide

  // Notes on the sheet:
  //   X
  //   Y
endmodule

module \or  (
  input  [31:0] X,
  input  [31:0] Y,
  output [31:0] Result
);

  assign Result = X | Y;  // OR_Gate or_1, 32 bits wide
endmodule

module \xor  (
  input  [31:0] X,
  input  [31:0] Y,
  output [31:0] Result
);

  assign Result = X ^ Y;  // XOR_Gate xor_1, 32 bits wide
endmodule

module or_not (
  input  [31:0] X,
  input  [31:0] Y,
  output [31:0] Result
);

  assign Result = ~(X | Y);  // NOR_Gate nor_1, 32 bits wide
endmodule

module \signed  (
  input  [31:0] X,
  input  [31:0] Y,
  output [31:0] Rresult
);

  wire comparator_1_lt;

  Comparator #(.width(32)) comparator_1 (.a(X), .b(Y), .lt(comparator_1_lt));  // open: gt, eq
  assign Rresult = {{31{1'b0}}, comparator_1_lt};  // Bit_Extender bit_extender_1
endmodule

module \unsigned  (
  input  [31:0] X,
  input  [31:0] Y,
  output [31:0] Result
);

  wire comparator_1_lt;

  Comparator #(.width(32), .mode("unsigned")) comparator_1 (.a(X), .b(Y), .lt(comparator_1_lt));  // open: gt, eq
  assign Result = {{31{1'b0}}, comparator_1_lt};  // Bit_Extender bit_extender_1
endmodule

module shl (
  input  [31:0] X,
  input  [31:0] Y,
  output [31:0] Result
);

  Shifter #(.width(32)) shifter_1 (.in(X), .\dist (Y[4:0]), .out(Result));
endmodule

module shr (
  input  [31:0] X,
  input  [31:0] Y,
  output [31:0] Result
);

  Shifter #(.width(32), .shift("lr")) shifter_1 (.in(X), .\dist (Y[4:0]), .out(Result));
endmodule

module sar (
  input  [31:0] X,
  input  [31:0] Y,
  output [31:0] Result
);

  Shifter #(.width(32), .shift("ar")) shifter_1 (.in(X), .\dist (Y[4:0]), .out(Result));
endmodule
