// Logisim project regfile.circ as structural Verilog: 2 circuits, main circuit main
module main (
  input  [4:0] Reg1_num,
  input  [4:0] Reg2_num,
  input  [4:0] Write_Reg_num,
  input  [31:0] Din,
  input  Write_Enable,
  input  Clock,
  output [31:0] Reg1,
  output [31:0] s0_Value,
  output [31:0] s1_Value,
  output [31:0] s2_Value,
  output [31:0] ra_Value,
  output [31:0] Reg2,
  output [31:0] v0_Value,
  output [31:0] a0_Value
);

  wire r0, r1, r2, r3, r4, r5, r6, r7, r8, r9, r10, r11, r12, r13, r14, r15, r16, r17, r18, r19, r20, r21,
       r22, r23, r24, r25, r26, r27, r28, r29, r30, r31;
  wire [31:0] ri0, ri1, ri3, ri5, ri6, ri7, ri8, ri9, ri10, ri11, ri12, ri13, ri14, ri15, ri19, ri20, ri21,
       ri22, ri23, ri24, ri25, ri26, ri27, ri28, ri29, ri30;

  Demultiplexer #(.select(5), .enable("false")) demultiplexer_1 (
    .out0(r0), .out1(r1), .out2(r2), .out3(r3), .out4(r4), .out5(r5), .out6(r6), .out7(r7), .out8(r8),
    .out9(r9), .out10(r10), .out11(r11), .out12(r12), .out13(r13), .out14(r14), .out15(r15), .out16(r16),
    .out17(r17), .out18(r18), .out19(r19), .out20(r20), .out21(r21), .out22(r22), .out23(r23), .out24(r24),
    .out25(r25), .out26(r26), .out27(r27), .out28(r28), .out29(r29), .out30(r30), .out31(r31),
    .in(Write_Enable), .sel(Write_Reg_num));
  Multiplexer #(.select(5), .width(32), .enable("false")) multiplexer_1 (
    .in0(ri0), .in1(ri1), .in2(v0_Value), .in3(ri3), .in4(a0_Value), .in5(ri5), .in6(ri6), .in7(ri7),
    .in8(ri8), .in9(ri9), .in10(ri10), .in11(ri11), .in12(ri12), .in13(ri13), .in14(ri14), .in15(ri15),
    .in16(s0_Value), .in17(s1_Value), .in18(s2_Value), .in19(ri19), .in20(ri20), .in21(ri21), .in22(ri22),
    .in23(ri23), .in24(ri24), .in25(ri25), .in26(ri26), .in27(ri27), .in28(ri28), .in29(ri29), .in30(ri30),
    .in31(ra_Value), .out(Reg1), .sel(Reg1_num));
  Register #(.width(32)) reg16 (.D(Din), .en(r16), .Q(s0_Value), .clk(Clock));  // open: clr
  Register #(.width(32)) reg24 (.D(Din), .en(r24), .Q(ri24), .clk(Clock));  // open: clr
  Register #(.width(32)) reg0 (.D({32{1'b0}}), .en(1'b0), .Q(ri0), .clk(Clock));  // open: clr
  Register #(.width(32)) reg8 (.D(Din), .en(r8), .Q(ri8), .clk(Clock));  // open: clr
  Register #(.width(32)) u_reg1 (.D(Din), .en(r1), .Q(ri1), .clk(Clock));  // open: clr
  Register #(.width(32)) reg9 (.D(Din), .en(r9), .Q(ri9), .clk(Clock));  // open: clr
  Register #(.width(32)) reg17 (.D(Din), .en(r17), .Q(s1_Value), .clk(Clock));  // open: clr
  Register #(.width(32)) reg25 (.D(Din), .en(r25), .Q(ri25), .clk(Clock));  // open: clr
  Register #(.width(32)) u_reg2 (.D(Din), .en(r2), .Q(v0_Value), .clk(Clock));  // open: clr
  Register #(.width(32)) reg10 (.D(Din), .en(r10), .Q(ri10), .clk(Clock));  // open: clr
  Register #(.width(32)) reg18 (.D(Din), .en(r18), .Q(s2_Value), .clk(Clock));  // open: clr
  Register #(.width(32)) reg26 (.D(Din), .en(r26), .Q(ri26), .clk(Clock));  // open: clr
  Register #(.width(32)) reg3 (.D(Din), .en(r3), .Q(ri3), .clk(Clock));  // open: clr
  Register #(.width(32)) reg11 (.D(Din), .en(r11), .Q(ri11), .clk(Clock));  // open: clr
  Register #(.width(32)) reg19 (.D(Din), .en(r19), .Q(ri19), .clk(Clock));  // open: clr
  Register #(.width(32)) reg27 (.D(Din), .en(r27), .Q(ri27), .clk(Clock));  // open: clr
  Register #(.width(32)) reg4 (.D(Din), .en(r4), .Q(a0_Value), .clk(Clock));  // open: clr
  Register #(.width(32)) reg12 (.D(Din), .en(r12), .Q(ri12), .clk(Clock));  // open: clr
  Register #(.width(32)) reg20 (.D(Din), .en(r20), .Q(ri20), .clk(Clock));  // open: clr
  Register #(.width(32)) reg28 (.D(Din), .en(r28), .Q(ri28), .clk(Clock));  // open: clr
  Multiplexer #(.select(5), .width(32), .enable("false")) multiplexer_2 (
    .in0(ri0), .in1(ri1), .in2(v0_Value), .in3(ri3), .in4(a0_Value), .in5(ri5), .in6(ri6), .in7(ri7),
    .in8(ri8), .in9(ri9), .in10(ri10), .in11(ri11), .in12(ri12), .in13(ri13), .in14(ri14), .in15(ri15),
    .in16(s0_Value), .in17(s1_Value), .in18(s2_Value), .in19(ri19), .in20(ri20), .in21(ri21), .in22(ri22),
    .in23(ri23), .in24(ri24), .in25(ri25), .in26(ri26), .in27(ri27), .in28(ri28), .in29(ri29), .in30(ri30),
    .in31(ra_Value), .out(Reg2), .sel(Reg2_num));
  Register #(.width(32)) reg5 (.D(Din), .en(r5), .Q(ri5), .clk(Clock));  // open: clr
  Register #(.width(32)) reg21 (.D(Din), .en(r21), .Q(ri21), .clk(Clock));  // open: clr
  Register #(.width(32)) reg29 (.D(Din), .en(r29), .Q(ri29), .clk(Clock));  // open: clr
  Register #(.width(32)) reg13 (.D(Din), .en(r13), .Q(ri13), .clk(Clock));  // open: clr
  Register #(.width(32)) reg6 (.D(Din), .en(r6), .Q(ri6), .clk(Clock));  // open: clr
  Register #(.width(32)) reg14 (.D(Din), .en(r14), .Q(ri14), .clk(Clock));  // open: clr
  Register #(.width(32)) reg22 (.D(Din), .en(r22), .Q(ri22), .clk(Clock));  // open: clr
  Register #(.width(32)) reg30 (.D(Din), .en(r30), .Q(ri30), .clk(Clock));  // open: clr
  Register #(.width(32)) reg15 (.D(Din), .en(r15), .Q(ri15), .clk(Clock));  // open: clr
  Register #(.width(32)) reg23 (.D(Din), .en(r23), .Q(ri23), .clk(Clock));  // open: clr
  Register #(.width(32)) reg31 (.D(Din), .en(r31), .Q(ra_Value), .clk(Clock));  // open: clr
  Register #(.width(32)) reg7 (.D(Din), .en(r7), .Q(ri7), .clk(Clock));  // open: clr

  // Other names for the same wires on the sheet: clk = Clock; ri2[31:0] = v0_Value; v0[31:0] = v0_Value;
  //   a0[31:0] = a0_Value; ri4[31:0] = a0_Value; ri16[31:0] = s0_Value; s0[31:0] = s0_Value; ri17[31:0] = s1_Value;
  //   s1[31:0] = s1_Value; ri18[31:0] = s2_Value; s2[31:0] = s2_Value; ra[31:0] = ra_Value; ri31[31:0] = ra_Value;
  //   WE = Write_Enable; write_data[31:0] = Din

  // Notes on the sheet:
  //   输入引脚
  //   输出引脚
  //   Debug引脚，便于观测寄存器值
  //   请勿修改引脚以及封装，直接使用隧道连接电路
endmodule

module test (
);

  wire [31:0] main_1_v0_value;

  main main_1 (.v0_Value(main_1_v0_value));  // open: Reg1_num, Reg2_num, Write_Reg_num, Din, Write_Enable, Clock, Reg1, Reg2, s0_Value, s1_Value, s2_Value, ra_Value, a0_Value
endmodule
