// Logisim project single_cpu.circ as structural Verilog: 1 circuit, main circuit main
module main (
  output [15:0] \步数 
);

  wire clear, Clock, clock_1_out, comparator_1_eq, equal, halt, Hi_Lo, main_2_branch, main_2_memwrite,
       main_2_regwrite, main_2_rf_r1, multiplexer_1_out, not_1_out, not_2_out, syscall;
  wire [1:0] main_2_alu_b, main_2_pc, main_2_rf_w;
  wire [2:0] main_2_rf_din;
  wire [3:0] ALU_OP;
  wire [4:0] main_1_rd, main_1_rs, main_1_rt, main_1_shamt, multiplexer_5_out, multiplexer_6_out;
  wire [5:0] main_1_funct, main_1_op;
  wire [15:0] counter_1_q, main_1_imm, multiplexer_4_out;
  wire [25:0] Addr;
  wire [31:0] a0, alu_1_result, alu_1_result_2, bit_extender_3_out, Hi, Lo, main_3_reg2, multiplexer_2_out,
       multiplexer_3_out, multiplexer_7_out, multiplexer_8_out, PC2, PC_4, PC_q, ra, ram_1_data, RF_R1,
       rom_1_data, s0, s1, s2, S_EXT, S_EXT__2, v0, Z_EXT;

  Button button_1 (.out(clear));
  Clock clock_1 (.out(clock_1_out));
  Multiplexer multiplexer_1 (.in0(equal), .in1(not_1_out), .out(multiplexer_1_out), .sel(main_2_branch), .en(1'b1));
  not not_1 (not_1_out, equal);
  Multiplexer #(.width(32)) multiplexer_2 (
    .in0(PC_4), .in1(PC2), .out(multiplexer_2_out), .sel(multiplexer_1_out), .en(1'b1));
  Counter #(.width(16), .max('hffff)) counter_1 (
    .load(1'b0), .D({16{1'b0}}), .count(1'b1), .Q(counter_1_q), .clk(Clock), .clr(clear));  // open: carry
  and and_1 (Clock, ~halt, clock_1_out);  // AND_Gate
  Multiplexer #(.select(2), .width(32)) multiplexer_3 (
    .in0(PC_4), .in1(multiplexer_2_out), .in2({PC_4[31:28], Addr, 2'b00}), .in3(RF_R1),
    .out(multiplexer_3_out), .sel(main_2_pc), .en(1'b1));
  not not_2 (not_2_out, halt);
  Comparator #(.width(32)) comparator_1 (.a(v0), .b(32'ha), .eq(comparator_1_eq));  // open: gt, lt
  Register #(.width(32)) PC (.D(multiplexer_3_out), .en(not_2_out), .Q(PC_q), .clk(Clock), .clr(clear));
  and and_2 (halt, syscall, comparator_1_eq);
  Adder #(.width(32)) adder_1 (.a(32'h4), .b(PC_q), .out(PC_4), .cin(1'b0));  // open: cout
  Multiplexer #(.width(16)) multiplexer_4 (
    .in0({16{1'b0}}), .in1(16'h1), .out(multiplexer_4_out), .sel(halt), .en(1'b1));
  Shifter #(.width(32)) shifter_1 (.in(S_EXT), .\dist (5'b00010), .out(S_EXT__2));
  Adder #(.width(16)) adder_2 (.a(counter_1_q), .b(multiplexer_4_out), .out(\步数 ));  // open: cin, cout
  Adder #(.width(32)) adder_3 (.a(S_EXT__2), .b(PC_4), .out(PC2), .cin(1'b0));  // open: cout
  ROM #(.addrWidth(10), .dataWidth(32)) rom_1 (.addr(PC_q[11:2]), .data(rom_1_data), .sel(1'b1));
  assign S_EXT = {{16{main_1_imm[15]}}, main_1_imm};  // Bit_Extender bit_extender_1
  assign Z_EXT = {{16{1'b0}}, main_1_imm};  // Bit_Extender bit_extender_2
  // Probe on \步数 
  Hex_Digit_Display hex_digit_display_1 (.value(a0[31:28]));  // open: dp
  decode_main main_1 (
    .in_1(rom_1_data), .OP(main_1_op), .rs(main_1_rs), .rt(main_1_rt), .rd(main_1_rd), .shamt(main_1_shamt),
    .funct(main_1_funct), .imm(main_1_imm), .addr(Addr));
  Hex_Digit_Display hex_digit_display_2 (.value(a0[23:20]));  // open: dp
  Hex_Digit_Display hex_digit_display_3 (.value(a0[27:24]));  // open: dp
  control_unit_main main_2 (
    .OP(main_1_op), .funct(main_1_funct), .Rf_R1(main_2_rf_r1), .PC(main_2_pc), .RF_Din(main_2_rf_din),
    .RF_W(main_2_rf_w), .MemWrite(main_2_memwrite), .ALU_B(main_2_alu_b), .RegWrite(main_2_regwrite),
    .ALU_OP(ALU_OP), .Branch(main_2_branch), .Hi_Lo(Hi_Lo), .syscall(syscall));
  assign bit_extender_3_out = {{27{1'b0}}, main_1_shamt};  // Bit_Extender bit_extender_3
  Hex_Digit_Display hex_digit_display_4 (.value(a0[19:16]));  // open: dp
  Hex_Digit_Display hex_digit_display_5 (.value(a0[15:12]));  // open: dp
  Multiplexer #(.width(5)) multiplexer_5 (
    .in0(main_1_rs), .in1(main_1_rt), .out(multiplexer_5_out), .sel(main_2_rf_r1), .en(1'b1));
  Multiplexer #(.select(2), .width(5)) multiplexer_6 (
    .in0(main_1_rd), .in1(main_1_rt), .in2({5{1'b1}}), .out(multiplexer_6_out), .sel(main_2_rf_w), .en(1'b1));  // open: in3
  Hex_Digit_Display hex_digit_display_6 (.value(a0[11:8]));  // open: dp
  Hex_Digit_Display hex_digit_display_7 (.value(a0[7:4]));  // open: dp
  // Probe on main_2_rf_din
  Multiplexer #(.select(3), .width(32)) multiplexer_7 (
    .in0(alu_1_result), .in1(Lo), .in2(Hi), .in3(ram_1_data), .in4(PC_4), .in5(PC_4), .in6(PC_4), .in7(PC_4),
    .out(multiplexer_7_out), .sel(main_2_rf_din), .en(1'b1));
  Hex_Digit_Display hex_digit_display_8 (.value(a0[3:0]));  // open: dp
  regfile_main main_3 (
    .Reg1_num(multiplexer_5_out), .Reg2_num(main_1_rt), .Write_Reg_num(multiplexer_6_out),
    .Din(multiplexer_7_out), .Write_Enable(main_2_regwrite), .Clock(Clock), .Reg1(RF_R1), .Reg2(main_3_reg2),
    .s0_Value(s0), .s1_Value(s1), .s2_Value(s2), .ra_Value(ra), .v0_Value(v0), .a0_Value(a0));
  Multiplexer #(.select(2), .width(32)) multiplexer_8 (
    .in0(main_3_reg2), .in1(S_EXT), .in2(Z_EXT), .in3(bit_extender_3_out), .out(multiplexer_8_out),
    .sel(main_2_alu_b), .en(1'b1));
  // Probe on s0
  // Probe on s1
  // Probe on s2
  // Probe on v0
  // Probe on a0
  // Probe on Hi
  // Probe on Lo
  ALU alu_1 (
    .AluOP(ALU_OP), .X(RF_R1), .Equal(equal), .Result(alu_1_result), .Y(multiplexer_8_out),
    .Result_2(alu_1_result_2));  // open: Signed_Overflow, UnSigned_Overflow
  Register #(.width(32)) register_1 (.D(alu_1_result_2), .en(Hi_Lo), .Q(Hi), .clk(Clock), .clr(clear));
  Register #(.width(32)) register_2 (.D(alu_1_result), .en(Hi_Lo), .Q(Lo), .clk(Clock), .clr(clear));
  RAM #(.addrWidth(10), .dataWidth(32), .bus("separate")) ram_1 (
    .addr(alu_1_result[11:2]), .din(main_3_reg2), .data(ram_1_data), .str(main_2_memwrite), .clk(Clock),
    .ld(1'b1));  // open: sel, clr

  // Notes on the sheet:
  //   contents of rom_1 (hex, n*v repeats v):
  //   20110001 8000c05 20110001 20120002 20130003 8000c09 20110001 20120002 20130003 8000c0d 20110001
  //   20120002 20130003 8000c11 20110001 20120002 20130003 c000cce 20110001 20120010 112020 20020022 c
  //   2320018 4810 8812 112020 20020022 c 1120fff9 20110001 20120010 118fc0 112020 20020022 c 232001b 4810
  //   8812 1620fff9 20100001 20110001 118fc0 112020 20020022 c 118882 12200001 8000c2b 112020 20020022 c
  //   20110001 118880 112020 20020022 c 12200001 8000c35 20110001 118fc0 112020 20020022 c 1188c3 112020
  //   20020022 c 118903 112020 20020022 c 118903 112020 20020022 c 118903 112020 20020022 c 118903 112020
  //   20020022 c 118903 112020 20020022 c 118903 112020 20020022 c 118903 112020 20020022 c 20100001
  //   109fc0 139fc3 8021 2012000c 24160003 26100001 3210000f 20080008 20090001 139900 2709825 132020
  //   20020022 c 1094022 1500fff9 22100001 2018000f 2188024 108700 20080008 20090001 139902 2709825 132021
  //   20020022 c 1094022 1500fff9 108702 2c9b022 12c00001 8000c66 4020 1084027 84400 3508ffff 82021
  //   20020022 c 2010ffff 20110000 ae300000 22100001 22310004 ae300000 22100001 22310004 ae300000 22100001
  //   22310004 ae300000 22100001 22310004 ae300000 22100001 22310004 ae300000 22100001 22310004 ae300000
  //   22100001 22310004 ae300000 22100001 22310004 ae300000 22100001 22310004 ae300000 22100001 22310004
  //   ae300000 22100001 22310004 ae300000 22100001 22310004 ae300000 22100001 22310004 ae300000 22100001
  //   22310004 ae300000 22100001 22310004 ae300000 22100001 22310004 22100001 8020 2011003c 8e130000
  //   8e340000 274402a 11000002 ae330000 ae140000 2231fffc 1611fff8 102020 20020022 c 22100004 2011003c
  //   1611fff2 2002000a c 20100000 22100001 102020 20020022 c 22100002 102020 20020022 c 22100003 102020
  //   20020022 c 22100004 102020 20020022 c 22100005 102020 20020022 c 22100006 102020 20020022 c 22100007
  //   102020 20020022 c 22100008 102020 20020022 20020022 c 3e00008
endmodule
