// Logisim project test.circ as structural Verilog: 1 circuit, main circuit main
module main (
  input  [31:0] a0,
  input  [31:0] d
);

  wire button, clk_out;
  wire [31:0] ai, alu_3_result, alu_4_result, alu_5_result, bit_extender_1_out, bit_extender_2_out, \reg ,
       register_1_q, register_2_q, sum;

  // Probe on \reg 
  // Probe on a0
  // Probe on a0
  Clock clk (.out(clk_out));
  // Probe on button
  Register #(.width(32)) register_1 (.D(\reg ), .en(1'b1), .Q(register_1_q), .clk(clk_out), .clr(1'b0));
  // Probe on d
  // Probe on d
  Button button_1 (.out(button));
  ALU alu_1 (
    .AluOP(4'b0101), .X(d), .Result(ai), .Y(register_1_q));  // open: Equal, Signed_Overflow, Result_2, UnSigned_Overflow
  Register #(.width(32)) register_2 (.D(sum), .en(1'b1), .Q(register_2_q), .clk(clk_out), .clr(button));
  ALU alu_2 (
    .AluOP(4'b0101), .X(register_1_q), .Result(sum), .Y(register_2_q));  // open: Equal, Signed_Overflow, Result_2, UnSigned_Overflow
  // Probe on ai
  // Probe on ai
  // Probe on sum
  // Probe on sum
  assign bit_extender_1_out = {{31{1'b0}}, button};  // Bit_Extender bit_extender_1
  Hex_Digit_Display hex_digit_display_1 (.value(sum[31:28]));  // open: dp
  Hex_Digit_Display hex_digit_display_2 (.value(sum[27:24]));  // open: dp
  // Probe on bit_extender_1_out
  ALU alu_3 (
    .AluOP(4'b1001), .X(bit_extender_1_out), .Result(alu_3_result), .Y({32{1'b1}}));  // open: Equal, Signed_Overflow, Result_2, UnSigned_Overflow
  Hex_Digit_Display hex_digit_display_3 (.value(sum[23:20]));  // open: dp
  Hex_Digit_Display hex_digit_display_4 (.value(sum[19:16]));  // open: dp
  // Probe on bit_extender_2_out
  assign bit_extender_2_out = {{31{button}}, button};  // Bit_Extender bit_extender_2
  // Probe on alu_3_result
  // Probe on ai
  Hex_Digit_Display hex_digit_display_5 (.value(sum[15:12]));  // open: dp
  Hex_Digit_Display hex_digit_display_6 (.value(sum[11:8]));  // open: dp
  ALU alu_4 (
    .AluOP(4'b0111), .X(bit_extender_2_out), .Result(alu_4_result), .Y(a0));  // open: Equal, Signed_Overflow, Result_2, UnSigned_Overflow
  ALU alu_5 (
    .AluOP(4'b0111), .X(alu_3_result), .Result(alu_5_result), .Y(ai));  // open: Equal, Signed_Overflow, Result_2, UnSigned_Overflow
  Hex_Digit_Display hex_digit_display_7 (.value(sum[7:4]));  // open: dp
  Hex_Digit_Display hex_digit_display_8 (.value(sum[3:0]));  // open: dp
  // Probe on alu_4_result
  ALU alu_6 (
    .AluOP(4'b1000), .X(alu_4_result), .Result(\reg ), .Y(alu_5_result));  // open: Equal, Signed_Overflow, Result_2, UnSigned_Overflow
  // Probe on alu_5_result
endmodule
