// Logisim project 奇偶校验.circ as structural Verilog: 1 circuit, main circuit main
module main (
  input  [7:0] \数据 ,
  input  [8:0] \传输噪音 ,
  output \校验位P ,
  output \检测函数 
);

  wire [8:0] xor_1_out;

  // Probe on \数据 
  assign xor_1_out = {\数据 , \校验位P } ^ \传输噪音 ;  // XOR_Gate xor_1, 9 bits wide
  // Probe on xor_1_out[8:1]
  xor xor_2 (\校验位P , \数据 [0], \数据 [1], \数据 [2], \数据 [3], \数据 [4], \数据 [5], \数据 [6], \数据 [7]);
  xor xor_3 (\检测函数 , xor_1_out[0], xor_1_out[1], xor_1_out[2], xor_1_out[3], xor_1_out[4], xor_1_out[5], xor_1_out[6], xor_1_out[7], xor_1_out[8]);

  // Notes on the sheet:
  //   传输噪音可以将对应数据位翻转
  //   数据
  //   发送数据   校验码
  //   校验位
  //   接收数据
  //   接收数据，不含校验位
  //   为零表示数据正常
endmodule
