// Logisim project Data_Redirection.circ as structural Verilog: 7 circuits, main circuit main
module main (
  output [15:0] \步数 
);

  wire and_2_out, and_3_out, and_4_out, Branch, clear, clear1, clear2, clear3, clear4, clk, clock_1_out,
       comparator_1_eq, equal, EX_MEM_halt_out, EX_MEM_memread_2, EX_MEM_memwrite_out, EX_MEM_regwrite_out,
       halt, halt_bubble, ID_EX_lohi_out, ID_EX_memread_2, ID_EX_memwrite_out, ID_EX_regwrite_out,
       ID_EX_syscall_out, jmp_detect_1_jmp_signal, main_1_bubble, main_2_branch, main_2_hi_lo,
       main_2_memread, main_2_memwrite, main_2_regwrite, main_2_rf_r1, main_2_syscall, multiplexer_1_out,
       not_1_out, not_2_out, not_3_out, not_4_out, not_5_out, or_1_out, or_2_out, or_3_out, WE;
  wire [1:0] EX_MEM_selpc_out, ID_EX_alu_b_out, main_1_sel_a0, main_1_sel_r1, main_1_sel_r2, main_1_sel_v0,
       main_2_alu_b, main_2_pc, main_2_rf_w, selPC;
  wire [2:0] EX_MEM_rf_din_out, ID_EX_rf_din_out, main_2_rf_din, RF_Din;
  wire [3:0] ID_EX_alu_op_out, main_2_alu_op, register_1_q_2, register_1_q_3, register_1_q_4;
  wire [4:0] decode_rd, decode_rs, decode_rt, decode_shamt, EX_MEM_rw__out, ID_EX_rw__out, ID_EX_shamt_out,
       multiplexer_5_out, multiplexer_6_out, RW_num;
  wire [5:0] decode_funct, decode_op;
  wire [15:0] counter_2_q, counter_3_q, decode_imm, ID_EX_imm_out, multiplexer_4_out, PCcount;
  wire [19:0] register_1_q;
  wire [25:0] Addr, decode_addr;
  wire [31:0] adder_1_out, adder_2_out, alu_1_result, alu_1_result_2, ALU_out, bit_extender_1_out,
       bit_extender_3_out, DM_out, EX_BACK, EX_MEM_alu_out_out, EX_MEM_hi_out, EX_MEM_ir_out, EX_MEM_lo_out,
       EX_MEM_pc_4_out, EX_MEM_pc_out, EX_MEM_rf_r2_out, Hi, Hi_q, ID_EX_a0_out, ID_EX_ir_out, ID_EX_pc_out,
       ID_EX_rf_r2_out, ID_EX_v0_out, IF_ID_ir_out, IF_ID_pc_4_out, IF_ID_pc_out, Lo, Lo_q, main_3_a0_value,
       main_3_ra_value, main_3_reg1, main_3_reg2, main_3_s0_value, main_3_s1_value, main_3_s2_value,
       main_3_v0_value, MEM_BACK, MEM_WB_ir_out, MEM_WB_pc_4_out, MEM_WB_pc_out, multiplexer_2_out,
       multiplexer_3_out, multiplexer_7_out, multiplexer_8_out, multiplexer_9_out, multiplexer_10_out,
       multiplexer_11_out, multiplexer_12_out, PC_4, PC_q, ram_1_data, RF_R1, rom_1_data, S_EXT,
       shifter_1_out;

  Button button_1 (.out(clear));
  Button button_2 (.out(clear1));
  Button button_3 (.out(clear2));
  Button button_4 (.out(clear3));
  Button button_5 (.out(clear4));
  Multiplexer multiplexer_1 (.in0(equal), .in1(not_1_out), .out(multiplexer_1_out), .sel(Branch), .en(1'b1));
  not not_1 (not_1_out, equal);
  Shifter #(.width(32)) shifter_1 (.in(S_EXT), .\dist (5'b00010), .out(shifter_1_out));
  Clock clock_1 (.out(clock_1_out));
  Multiplexer #(.width(32)) multiplexer_2 (
    .in0(adder_2_out), .in1(adder_1_out), .out(multiplexer_2_out), .sel(multiplexer_1_out), .en(1'b1));
  Adder #(.width(32)) adder_1 (.a(shifter_1_out), .b(PC_4), .out(adder_1_out), .cin(1'b0));  // open: cout
  Counter #(.width(16), .max('hffff)) counter_1 (.Q(PCcount), .clk(clk), .clr(clear));  // open: load, D, count, carry
  and and_1 (clk, ~halt, clock_1_out);  // AND_Gate
  Multiplexer #(.select(2), .width(32)) multiplexer_3 (
    .in0(adder_2_out), .in1(multiplexer_2_out), .in2({PC_4[31:28], Addr, 2'b00}), .in3(RF_R1),
    .out(multiplexer_3_out), .sel(selPC), .en(1'b1));
  and and_2 (and_2_out, or_1_out, not_2_out);
  not not_2 (not_2_out, halt);
  or or_1 (or_1_out, jmp_detect_1_jmp_signal, not_3_out);
  not not_3 (not_3_out, main_1_bubble);
  Multiplexer #(.width(16)) multiplexer_4 (
    .in0({16{1'b0}}), .in1(16'h1), .out(multiplexer_4_out), .sel(halt), .en(1'b1));
  Adder #(.width(32)) adder_2 (.a(32'h4), .b(PC_q), .out(adder_2_out), .cin(1'b0));  // open: cout
  Register #(.width(32)) PC (.D(multiplexer_3_out), .en(and_2_out), .Q(PC_q), .clk(clk), .clr(clear));
  not not_4 (not_4_out, main_1_bubble);
  Hex_Digit_Display hex_digit_display_1 (.value(register_1_q_4));  // open: dp
  Hex_Digit_Display hex_digit_display_2 (.value(register_1_q_3));  // open: dp
  Adder #(.width(16)) adder_3 (.a(PCcount), .b(multiplexer_4_out), .out(\步数 ));  // open: cin, cout
  Hex_Digit_Display hex_digit_display_3 (.value(register_1_q_2));  // open: dp
  Hex_Digit_Display hex_digit_display_4 (.value(register_1_q[19:16]));  // open: dp
  Register #(.width(32)) register_1 (
    .D(ID_EX_a0_out), .en(ID_EX_syscall_out),
    .Q({register_1_q_4, register_1_q_3, register_1_q_2, register_1_q}), .clk(clk));  // open: clr
  and and_3 (and_3_out, clk, ~halt_bubble);  // AND_Gate
  and and_4 (and_4_out, clk, ~halt_bubble);  // AND_Gate
  // Probe on \步数 
  or or_2 (or_2_out, not_4_out, jmp_detect_1_jmp_signal);
  Hex_Digit_Display hex_digit_display_5 (.value(register_1_q[15:12]));  // open: dp
  Hex_Digit_Display hex_digit_display_6 (.value(register_1_q[11:8]));  // open: dp
  Counter #(.width(16), .max('hffff)) counter_2 (
    .count(main_1_bubble), .Q(counter_2_q), .clk(and_3_out));  // open: load, D, carry, clr
  Counter #(.width(16), .max('hffff)) counter_3 (
    .count(jmp_detect_1_jmp_signal), .Q(counter_3_q), .clk(and_4_out));  // open: load, D, carry, clr
  ROM #(.addrWidth(10), .dataWidth(32)) rom_1 (.addr(PC_q[11:2]), .data(rom_1_data), .sel(1'b1));
  Hex_Digit_Display hex_digit_display_7 (.value(register_1_q[3:0]));  // open: dp
  Hex_Digit_Display hex_digit_display_8 (.value(register_1_q[7:4]));  // open: dp
  // Probe on counter_2_q
  // Probe on counter_3_q
  // Probe on IF_ID_pc_out
  // Probe on IF_ID_ir_out
  IF_ID IF_ID (
    .PC_in(PC_q), .PC_out(IF_ID_pc_out), .PC_4_in(adder_2_out), .PC_4_out(IF_ID_pc_4_out),
    .IR_in(rom_1_data), .IR_out(IF_ID_ir_out), .E(or_2_out), .in_5(jmp_detect_1_jmp_signal), .clk(clk),
    .clear(clear1));
  decode_main decode (
    .in_1(IF_ID_ir_out), .OP(decode_op), .rs(decode_rs), .rt(decode_rt), .rd(decode_rd),
    .shamt(decode_shamt), .funct(decode_funct), .imm(decode_imm), .addr(decode_addr));
  reg_read_detect_main main_1 (
    .OP(decode_op), .funct(decode_funct), .syscall(main_2_syscall), .WE1(ID_EX_regwrite_out),
    .WE2(EX_MEM_regwrite_out), .MemRead(ID_EX_memread_2), .RW_1(ID_EX_rw__out), .RW_2(EX_MEM_rw__out),
    .R1_num(multiplexer_5_out), .R2_num(decode_rt), .PCcount(PCcount), .bubble(main_1_bubble),
    .sel_R1(main_1_sel_r1), .sel_R2(main_1_sel_r2), .sel_v0(main_1_sel_v0), .sel_a0(main_1_sel_a0));
  Multiplexer #(.width(5)) multiplexer_5 (
    .in0(decode_rs), .in1(decode_rt), .out(multiplexer_5_out), .sel(main_2_rf_r1), .en(1'b1));
  Multiplexer #(.select(2), .width(5)) multiplexer_6 (
    .in0(decode_rd), .in1(decode_rt), .in2({5{1'b1}}), .out(multiplexer_6_out), .sel(main_2_rf_w), .en(1'b1));  // open: in3
  // Probe on main_3_s0_value
  // Probe on main_3_s1_value
  // Probe on main_3_s2_value
  // Probe on main_3_ra_value
  // Probe on main_3_v0_value
  // Probe on main_3_a0_value
  control_unit_main main_2 (
    .OP(decode_op), .funct(decode_funct), .Rf_R1(main_2_rf_r1), .PC(main_2_pc), .RF_Din(main_2_rf_din),
    .RF_W(main_2_rf_w), .MemWrite(main_2_memwrite), .ALU_B(main_2_alu_b), .RegWrite(main_2_regwrite),
    .ALU_OP(main_2_alu_op), .Branch(main_2_branch), .Hi_Lo(main_2_hi_lo), .syscall(main_2_syscall),
    .MemRead(main_2_memread));
  not not_5 (not_5_out, clk);
  Multiplexer #(.select(3), .width(32)) multiplexer_7 (
    .in0(ALU_out), .in1(Lo), .in2(Hi), .in3(DM_out), .in4(MEM_WB_pc_4_out), .out(multiplexer_7_out),
    .sel(RF_Din), .en(1'b1));  // open: in5, in6, in7
  regfile_main main_3 (
    .Reg1_num(multiplexer_5_out), .Reg2_num(decode_rt), .Write_Reg_num(RW_num), .Din(multiplexer_7_out),
    .Write_Enable(WE), .Clock(not_5_out), .Reg1(main_3_reg1), .Reg2(main_3_reg2), .s0_Value(main_3_s0_value),
    .s1_Value(main_3_s1_value), .s2_Value(main_3_s2_value), .ra_Value(main_3_ra_value),
    .v0_Value(main_3_v0_value), .a0_Value(main_3_a0_value));
  ID_EX ID_EX (
    .PC_in(IF_ID_pc_out), .selPC_in(main_2_pc), .RW__in(multiplexer_6_out), .RF_Din_in(main_2_rf_din),
    .ALU_B_in(main_2_alu_b), .ALU_OP_in(main_2_alu_op), .MemWrite_in(main_2_memwrite),
    .RegWrite_in(main_2_regwrite), .Branch_in(main_2_branch), .LOHI_in(main_2_hi_lo),
    .Syscall_in(main_2_syscall), .IMM_in(decode_imm), .Addr_in(decode_addr), .shamt_in(decode_shamt),
    .v0_in(multiplexer_11_out), .a0_in(multiplexer_10_out), .RF_R1_in(multiplexer_9_out),
    .RF_R2_in(multiplexer_8_out), .PC_out(ID_EX_pc_out), .PC_4_out(PC_4), .selPC_out(selPC),
    .RW__out(ID_EX_rw__out), .RF_Din_out(ID_EX_rf_din_out), .ALU_B_out(ID_EX_alu_b_out),
    .ALU_OP_out(ID_EX_alu_op_out), .MemWrite_out(ID_EX_memwrite_out), .RegWrite_out(ID_EX_regwrite_out),
    .Branch_out(Branch), .LOHI_out(ID_EX_lohi_out), .Syscall_out(ID_EX_syscall_out), .IMM_out(ID_EX_imm_out),
    .Addr_out(Addr), .shamt_out(ID_EX_shamt_out), .v0_out(ID_EX_v0_out), .a0_out(ID_EX_a0_out),
    .RF_R1_out(RF_R1), .RF_R2_out(ID_EX_rf_r2_out), .clk(clk), .clear(clear2), .IR_in(IF_ID_ir_out),
    .IR_out(ID_EX_ir_out), .PC_4_in(IF_ID_pc_4_out), .in_22(or_3_out), .MemRead(main_2_memread),
    .MemRead_2(ID_EX_memread_2));
  Multiplexer #(.select(2), .width(32)) multiplexer_8 (
    .in0(main_3_reg2), .in1(EX_BACK), .in2(MEM_BACK), .in3(EX_BACK), .out(multiplexer_8_out),
    .sel(main_1_sel_r2), .en(1'b1));
  Multiplexer #(.select(2), .width(32)) multiplexer_9 (
    .in0(main_3_reg1), .in1(EX_BACK), .in2(MEM_BACK), .in3(EX_BACK), .out(multiplexer_9_out),
    .sel(main_1_sel_r1), .en(1'b1));
  Multiplexer #(.select(2), .width(32)) multiplexer_10 (
    .in0(main_3_a0_value), .in1(EX_BACK), .in2(MEM_BACK), .in3(EX_BACK), .out(multiplexer_10_out),
    .sel(main_1_sel_a0), .en(1'b1));
  Multiplexer #(.select(2), .width(32)) multiplexer_11 (
    .in0(main_3_v0_value), .in1(EX_BACK), .in2(MEM_BACK), .in3(EX_BACK), .out(multiplexer_11_out),
    .sel(main_1_sel_v0), .en(1'b1));
  // Probe on ID_EX_pc_out
  // Probe on ID_EX_ir_out
  assign bit_extender_1_out = {{27{1'b0}}, ID_EX_shamt_out};  // Bit_Extender bit_extender_1
  assign S_EXT = {{16{ID_EX_imm_out[15]}}, ID_EX_imm_out};  // Bit_Extender bit_extender_2
  assign bit_extender_3_out = {{16{1'b0}}, ID_EX_imm_out};  // Bit_Extender bit_extender_3
  or or_3 (or_3_out, main_1_bubble, jmp_detect_1_jmp_signal);
  Multiplexer #(.select(2), .width(32)) multiplexer_12 (
    .in0(ID_EX_rf_r2_out), .in1(S_EXT), .in2(bit_extender_3_out), .in3(bit_extender_1_out),
    .out(multiplexer_12_out), .sel(ID_EX_alu_b_out), .en(1'b1));
  Comparator #(.width(32), .mode("unsigned")) comparator_1 (
    .a(ID_EX_v0_out), .b(32'ha), .eq(comparator_1_eq));  // open: gt, lt
  ALU alu_1 (
    .AluOP(ID_EX_alu_op_out), .X(RF_R1), .Equal(equal), .Result(alu_1_result), .Y(multiplexer_12_out),
    .Result_2(alu_1_result_2));  // open: Signed_Overflow, UnSigned_Overflow
  Register #(.width(32), .trigger("falling")) u_Hi (
    .D(alu_1_result_2), .en(ID_EX_lohi_out), .Q(Hi_q), .clk(clk), .clr(clear));
  and and_5 (halt_bubble, ID_EX_syscall_out, comparator_1_eq);
  jmp_detect jmp_detect_1 (.selPC(selPC), .Branch(Branch), .equal(equal), .jmp_signal(jmp_detect_1_jmp_signal));
  Register #(.width(32), .trigger("falling")) u_Lo (
    .D(alu_1_result), .en(ID_EX_lohi_out), .Q(Lo_q), .clk(clk), .clr(clear));
  EX_MEM EX_MEM (
    .PC_in(ID_EX_pc_out), .PC_4_in(PC_4), .IR_in(ID_EX_ir_out), .selPC_in(selPC), .RW__in(ID_EX_rw__out),
    .RF_Din_in(ID_EX_rf_din_out), .MemWrite_in(ID_EX_memwrite_out), .RegWrite_in(ID_EX_regwrite_out),
    .Lo_in(Lo_q), .Hi_in(Hi_q), .halt_in(halt_bubble), .ALU_out_in(alu_1_result), .RF_R2_in(ID_EX_rf_r2_out),
    .PC_out(EX_MEM_pc_out), .PC_4_out(EX_MEM_pc_4_out), .IR_out(EX_MEM_ir_out), .selPC_out(EX_MEM_selpc_out),
    .RW__out(EX_MEM_rw__out), .RF_Din_out(EX_MEM_rf_din_out), .MemWrite_out(EX_MEM_memwrite_out),
    .RegWrite_out(EX_MEM_regwrite_out), .Lo_out(EX_MEM_lo_out), .Hi_out(EX_MEM_hi_out),
    .halt_out(EX_MEM_halt_out), .ALU_out_out(EX_MEM_alu_out_out), .RF_R2_out(EX_MEM_rf_r2_out), .clk(clk),
    .clear(clear3), .MemRead(ID_EX_memread_2), .MemRead_2(EX_MEM_memread_2));  // open: Branch_in, equal_in, S_EXT_in, Addr_in, RF_R1_in, Branch_out, equal_out, S_EXT_out, Addr_out, RF_R1_out
  data_redirection data_redirection_1 (
    .ALU_R1(alu_1_result), .Lo(Lo_q), .Hi(Hi_q), .PC_4(PC_4), .RF_Din(ID_EX_rf_din_out), .out_7(EX_BACK));  // open: DM_out
  // Probe on EX_MEM_pc_out
  // Probe on EX_MEM_ir_out
  RAM #(.addrWidth(10), .dataWidth(32), .bus("separate")) ram_1 (
    .addr(EX_MEM_alu_out_out[11:2]), .din(EX_MEM_rf_r2_out), .data(ram_1_data), .str(EX_MEM_memwrite_out),
    .clk(clk), .ld(EX_MEM_memread_2));  // open: sel, clr
  MEM_WB MEM_WB (
    .PC_in(EX_MEM_pc_out), .PC_4_in(EX_MEM_pc_4_out), .IR_in(EX_MEM_ir_out), .selPC_in(EX_MEM_selpc_out),
    .RW__in(EX_MEM_rw__out), .RF_Din_in(EX_MEM_rf_din_out), .DM_out_in(ram_1_data),
    .RegWrite_in(EX_MEM_regwrite_out), .Lo_in(EX_MEM_lo_out), .Hi_in(EX_MEM_hi_out),
    .halt_in(EX_MEM_halt_out), .ALU_out_in(EX_MEM_alu_out_out), .PC_out(MEM_WB_pc_out),
    .PC_4_out(MEM_WB_pc_4_out), .IR_out(MEM_WB_ir_out), .RW__out(RW_num), .RF_Din_out(RF_Din),
    .DM_out_out(DM_out), .RegWrite_out(WE), .Lo_out(Lo), .Hi_out(Hi), .halt_out(halt), .ALU_out_out(ALU_out),
    .clk(clk), .clear(clear4));  // open: Branch_in, equal_in, S_EXT_in, Addr_in, RF_R1_in, selPC_out, Branch_out, equal_out, S_EXT_out, Addr_out, RF_R1_out
  data_redirection data_redirection_2 (
    .ALU_R1(EX_MEM_alu_out_out), .Lo(EX_MEM_lo_out), .Hi(EX_MEM_hi_out), .DM_out(ram_1_data),
    .PC_4(EX_MEM_pc_4_out), .RF_Din(EX_MEM_rf_din_out), .out_7(MEM_BACK));
  // Probe on MEM_WB_pc_out
  // Probe on MEM_WB_ir_out

  // Notes on the sheet:
  //   contents of rom_1 (hex, n*v repeats v):
  //   20110001 8000c05 20110001 20120002 20130003 8000c09 20110001 20120002 20130003 8000c0d 20110001
  //   20120002 20130003 8000c11 20110001 20120002 20130003 c000cce 20110001 20120010 112020 20020022 c
  //   2320018 4810 8812 112020 20020022 c 1120fff9 20110001 20120010 118fc0 112020 20020022 c 232001b 4810
  //   8812 1620fff9 20100001 20110001 118fc0 112020 20020022 c 118882 12200001 8000c2b 112020 20020022 c
  //   20110001 118880 112020 20020022 c 12200001 8000c35 20110001 118fc0 112020 20020022 c 1188c3 112020
  //   20020022 c 118903 112020 20020022 c 118903 112020 20020022 c 118903 112020 20020022 c 118903 112020
  //   20020022 c 118903 112020 20020022 c 118903 112020 20020022 c 118903 112020 20020022 c 20100001
  //   109fc0 139fc3 8021 2012000c 24160003 26100001 3210000f 20080008 20090001 139900 2709825 132020
  //   20020022 c 1094022 1500fff9 22100001 2018000f 2188024 108700 20080008 20090001 139902 2709825 132021
  //   20020022 c 1094022 1500fff9 108702 2c9b022 12c00001 8000c66 4020 1084027 84400 3508ffff 82021
  //   20020022 c 2010ffff 20110000 ae300000 22100001 22310004 ae300000 22100001 22310004 ae300000 22100001
  //   22310004 ae300000 22100001 22310004 ae300000 22100001 22310004 ae300000 22100001 22310004 ae300000
  //   22100001 22310004 ae300000 22100001 22310004 ae300000 22100001 22310004 ae300000 22100001 22310004
  //   ae300000 22100001 22310004 ae300000 22100001 22310004 ae300000 22100001 22310004 ae300000 22100001
  //   22310004 ae300000 22100001 22310004 ae300000 22100001 22310004 22100001 8020 2011003c 8e130000
  //   8e340000 274402a 11000002 ae330000 ae140000 2231fffc 1611fff8 102020 20020022 c 22100004 2011003c
  //   1611fff2 2002000a c 20100000 22100001 102020 20020022 c 22100002 102020 20020022 c 22100003 102020
  //   20020022 c 22100004 102020 20020022 c 22100005 102020 20020022 c 22100006 102020 20020022 c 22100007
  //   102020 20020022 c 22100008 102020 20020022 20020022 c 3e00008
  //   R2
  //   R1
  //   a0
  //   v0
endmodule

module IF_ID (
  input  [31:0] PC_in,
  input  [31:0] PC_4_in,
  input  [31:0] IR_in,
  input  E,
  input  in_5,
  input  clk,
  input  clear,
  output [31:0] PC_out,
  output [31:0] PC_4_out,
  output [31:0] IR_out
);

  wire [31:0] multiplexer_1_out, multiplexer_2_out, multiplexer_3_out;

  Multiplexer #(.width(32)) multiplexer_1 (
    .in0(PC_in), .in1({32{1'b0}}), .out(multiplexer_1_out), .sel(in_5), .en(1'b1));
  Multiplexer #(.width(32)) multiplexer_2 (
    .in0(PC_4_in), .in1({32{1'b0}}), .out(multiplexer_2_out), .sel(in_5), .en(1'b1));
  Multiplexer #(.width(32)) multiplexer_3 (
    .in0(IR_in), .in1({32{1'b0}}), .out(multiplexer_3_out), .sel(in_5), .en(1'b1));
  Register #(.width(32)) register_1 (.D(multiplexer_1_out), .en(E), .Q(PC_out), .clk(clk), .clr(clear));
  Register #(.width(32)) register_2 (.D(multiplexer_2_out), .en(E), .Q(PC_4_out), .clk(clk), .clr(clear));
  Register #(.width(32)) register_3 (.D(multiplexer_3_out), .en(E), .Q(IR_out), .clk(clk), .clr(clear));
endmodule

module ID_EX (
  input  [31:0] PC_in,
  input  [31:0] PC_4_in,
  input  [31:0] IR_in,
  input  [1:0] selPC_in,
  input  [4:0] RW__in,
  input  [2:0] RF_Din_in,
  input  [1:0] ALU_B_in,
  input  [3:0] ALU_OP_in,
  input  MemWrite_in,
  input  RegWrite_in,
  input  Branch_in,
  input  LOHI_in,
  input  Syscall_in,
  input  [15:0] IMM_in,
  input  [25:0] Addr_in,
  input  [4:0] shamt_in,
  input  [31:0] v0_in,
  input  [31:0] a0_in,
  input  [31:0] RF_R1_in,
  input  [31:0] RF_R2_in,
  input  MemRead,
  input  in_22,
  input  clk,
  input  clear,
  output [31:0] PC_out,
  output [31:0] PC_4_out,
  output [31:0] IR_out,
  output [1:0] selPC_out,
  output [4:0] RW__out,
  output [2:0] RF_Din_out,
  output [1:0] ALU_B_out,
  output [3:0] ALU_OP_out,
  output MemWrite_out,
  output RegWrite_out,
  output Branch_out,
  output LOHI_out,
  output Syscall_out,
  output [15:0] IMM_out,
  output [25:0] Addr_out,
  output [4:0] shamt_out,
  output [31:0] v0_out,
  output [31:0] a0_out,
  output [31:0] RF_R1_out,
  output [31:0] RF_R2_out,
  output MemRead_2
);

  wire multiplexer_9_out, multiplexer_10_out, multiplexer_11_out, multiplexer_12_out, multiplexer_13_out,
       multiplexer_21_out;
  wire [1:0] multiplexer_4_out, multiplexer_7_out;
  wire [2:0] multiplexer_6_out;
  wire [3:0] multiplexer_8_out;
  wire [4:0] multiplexer_5_out, multiplexer_16_out;
  wire [15:0] multiplexer_14_out;
  wire [25:0] multiplexer_15_out;
  wire [31:0] multiplexer_1_out, multiplexer_2_out, multiplexer_3_out, multiplexer_17_out,
       multiplexer_18_out, multiplexer_19_out, multiplexer_20_out;

  Multiplexer #(.width(32)) multiplexer_1 (
    .in0(PC_in), .in1({32{1'b0}}), .out(multiplexer_1_out), .sel(in_22), .en(1'b1));
  Multiplexer #(.width(32)) multiplexer_2 (
    .in0(PC_4_in), .in1({32{1'b0}}), .out(multiplexer_2_out), .sel(in_22), .en(1'b1));
  Multiplexer #(.width(32)) multiplexer_3 (
    .in0(IR_in), .in1({32{1'b0}}), .out(multiplexer_3_out), .sel(in_22), .en(1'b1));
  Multiplexer #(.width(2)) multiplexer_4 (.in0(selPC_in), .in1(2'b00), .out(multiplexer_4_out), .sel(in_22), .en(1'b1));
  Multiplexer #(.width(5)) multiplexer_5 (
    .in0(RW__in), .in1({5{1'b0}}), .out(multiplexer_5_out), .sel(in_22), .en(1'b1));
  Multiplexer #(.width(3)) multiplexer_6 (
    .in0(RF_Din_in), .in1(3'b000), .out(multiplexer_6_out), .sel(in_22), .en(1'b1));
  Multiplexer #(.width(2)) multiplexer_7 (.in0(ALU_B_in), .in1(2'b00), .out(multiplexer_7_out), .sel(in_22), .en(1'b1));
  Multiplexer #(.width(4)) multiplexer_8 (
    .in0(ALU_OP_in), .in1(4'b0000), .out(multiplexer_8_out), .sel(in_22), .en(1'b1));
  Multiplexer multiplexer_9 (.in0(MemWrite_in), .in1(1'b0), .out(multiplexer_9_out), .sel(in_22), .en(1'b1));
  Multiplexer multiplexer_10 (.in0(RegWrite_in), .in1(1'b0), .out(multiplexer_10_out), .sel(in_22), .en(1'b1));
  Multiplexer multiplexer_11 (.in0(Branch_in), .in1(1'b0), .out(multiplexer_11_out), .sel(in_22), .en(1'b1));
  Multiplexer multiplexer_12 (.in0(LOHI_in), .in1(1'b0), .out(multiplexer_12_out), .sel(in_22), .en(1'b1));
  Multiplexer multiplexer_13 (.in0(Syscall_in), .in1(1'b0), .out(multiplexer_13_out), .sel(in_22), .en(1'b1));
  Multiplexer #(.width(16)) multiplexer_14 (
    .in0(IMM_in), .in1({16{1'b0}}), .out(multiplexer_14_out), .sel(in_22), .en(1'b1));
  Multiplexer #(.width(26)) multiplexer_15 (
    .in0(Addr_in), .in1({26{1'b0}}), .out(multiplexer_15_out), .sel(in_22), .en(1'b1));
  Multiplexer #(.width(5)) multiplexer_16 (
    .in0(shamt_in), .in1({5{1'b0}}), .out(multiplexer_16_out), .sel(in_22), .en(1'b1));
  Multiplexer #(.width(32)) multiplexer_17 (
    .in0(v0_in), .in1({32{1'b0}}), .out(multiplexer_17_out), .sel(in_22), .en(1'b1));
  Multiplexer #(.width(32)) multiplexer_18 (
    .in0(a0_in), .in1({32{1'b0}}), .out(multiplexer_18_out), .sel(in_22), .en(1'b1));
  Multiplexer #(.width(32)) multiplexer_19 (
    .in0(RF_R1_in), .in1({32{1'b0}}), .out(multiplexer_19_out), .sel(in_22), .en(1'b1));
  Multiplexer #(.width(32)) multiplexer_20 (
    .in0(RF_R2_in), .in1({32{1'b0}}), .out(multiplexer_20_out), .sel(in_22), .en(1'b1));
  Multiplexer multiplexer_21 (.in0(MemRead), .in1(1'b0), .out(multiplexer_21_out), .sel(in_22), .en(1'b1));
  Register #(.width(32)) register_1 (.D(multiplexer_1_out), .en(1'b1), .Q(PC_out), .clk(clk), .clr(clear));
  Register #(.width(32)) register_2 (.D(multiplexer_2_out), .en(1'b1), .Q(PC_4_out), .clk(clk), .clr(clear));
  Register #(.width(32)) register_3 (.D(multiplexer_3_out), .en(1'b1), .Q(IR_out), .clk(clk), .clr(clear));
  Register #(.width(2)) register_4 (.D(multiplexer_4_out), .en(1'b1), .Q(selPC_out), .clk(clk), .clr(clear));
  Register #(.width(5)) register_5 (.D(multiplexer_5_out), .en(1'b1), .Q(RW__out), .clk(clk), .clr(clear));
  Register #(.width(3)) register_6 (.D(multiplexer_6_out), .en(1'b1), .Q(RF_Din_out), .clk(clk), .clr(clear));
  Register #(.width(2)) register_7 (.D(multiplexer_7_out), .en(1'b1), .Q(ALU_B_out), .clk(clk), .clr(clear));
  Register #(.width(4)) register_8 (.D(multiplexer_8_out), .en(1'b1), .Q(ALU_OP_out), .clk(clk), .clr(clear));
  Register #(.width(1)) register_9 (.D(multiplexer_9_out), .en(1'b1), .Q(MemWrite_out), .clk(clk), .clr(clear));
  Register #(.width(1)) register_10 (.D(multiplexer_10_out), .en(1'b1), .Q(RegWrite_out), .clk(clk), .clr(clear));
  Register #(.width(1)) register_11 (.D(multiplexer_11_out), .en(1'b1), .Q(Branch_out), .clk(clk), .clr(clear));
  Register #(.width(1)) register_12 (.D(multiplexer_12_out), .en(1'b1), .Q(LOHI_out), .clk(clk), .clr(clear));
  Register #(.width(1)) register_13 (.D(multiplexer_13_out), .en(1'b1), .Q(Syscall_out), .clk(clk), .clr(clear));
  Register #(.width(16)) register_14 (.D(multiplexer_14_out), .en(1'b1), .Q(IMM_out), .clk(clk), .clr(clear));
  Register #(.width(26)) register_15 (.D(multiplexer_15_out), .en(1'b1), .Q(Addr_out), .clk(clk), .clr(clear));
  Register #(.width(5)) register_16 (.D(multiplexer_16_out), .en(1'b1), .Q(shamt_out), .clk(clk), .clr(clear));
  Register #(.width(32)) register_17 (.D(multiplexer_17_out), .en(1'b1), .Q(v0_out), .clk(clk), .clr(clear));
  Register #(.width(32)) register_18 (.D(multiplexer_18_out), .en(1'b1), .Q(a0_out), .clk(clk), .clr(clear));
  Register #(.width(32)) register_19 (.D(multiplexer_19_out), .en(1'b1), .Q(RF_R1_out), .clk(clk), .clr(clear));
  Register #(.width(32)) register_20 (.D(multiplexer_20_out), .en(1'b1), .Q(RF_R2_out), .clk(clk), .clr(clear));
  Register #(.width(1)) register_21 (.D(multiplexer_21_out), .en(1'b1), .Q(MemRead_2), .clk(clk), .clr(clear));
endmodule

module EX_MEM (
  input  [31:0] PC_in,
  input  [31:0] PC_4_in,
  input  [31:0] IR_in,
  input  [1:0] selPC_in,
  input  [4:0] RW__in,
  input  [2:0] RF_Din_in,
  input  MemWrite_in,
  input  RegWrite_in,
  input  [31:0] Lo_in,
  input  [31:0] Hi_in,
  input  Branch_in,
  input  equal_in,
  input  [31:0] S_EXT_in,
  input  halt_in,
  input  [31:0] ALU_out_in,
  input  [25:0] Addr_in,
  input  [31:0] RF_R1_in,
  input  [31:0] RF_R2_in,
  input  MemRead,
  input  clk,
  input  clear,
  output [31:0] PC_out,
  output [31:0] PC_4_out,
  output [31:0] IR_out,
  output [1:0] selPC_out,
  output [4:0] RW__out,
  output [2:0] RF_Din_out,
  output MemWrite_out,
  output RegWrite_out,
  output [31:0] Lo_out,
  output [31:0] Hi_out,
  output Branch_out,
  output equal_out,
  output [31:0] S_EXT_out,
  output halt_out,
  output [31:0] ALU_out_out,
  output [25:0] Addr_out,
  output [31:0] RF_R1_out,
  output [31:0] RF_R2_out,
  output MemRead_2
);

  Register #(.width(32)) register_1 (.D(PC_in), .en(1'b1), .Q(PC_out), .clk(clk), .clr(clear));
  Register #(.width(32)) register_2 (.D(PC_4_in), .en(1'b1), .Q(PC_4_out), .clk(clk), .clr(clear));
  Register #(.width(32)) register_3 (.D(IR_in), .en(1'b1), .Q(IR_out), .clk(clk), .clr(clear));
  Register #(.width(2)) register_4 (.D(selPC_in), .en(1'b1), .Q(selPC_out), .clk(clk), .clr(clear));
  Register #(.width(5)) register_5 (.D(RW__in), .en(1'b1), .Q(RW__out), .clk(clk), .clr(clear));
  Register #(.width(3)) register_6 (.D(RF_Din_in), .en(1'b1), .Q(RF_Din_out), .clk(clk), .clr(clear));
  Register #(.width(1)) register_7 (.D(MemWrite_in), .en(1'b1), .Q(MemWrite_out), .clk(clk), .clr(clear));
  Register #(.width(1)) register_8 (.D(RegWrite_in), .en(1'b1), .Q(RegWrite_out), .clk(clk), .clr(clear));
  Register #(.width(32)) register_9 (.D(Lo_in), .en(1'b1), .Q(Lo_out), .clk(clk), .clr(clear));
  Register #(.width(32)) register_10 (.D(Hi_in), .en(1'b1), .Q(Hi_out), .clk(clk), .clr(clear));
  Register #(.width(1)) register_11 (.D(Branch_in), .en(1'b1), .Q(Branch_out), .clk(clk), .clr(clear));
  Register #(.width(1)) register_12 (.D(equal_in), .en(1'b1), .Q(equal_out), .clk(clk), .clr(clear));
  Register #(.width(32)) register_13 (.D(S_EXT_in), .en(1'b1), .Q(S_EXT_out), .clk(clk), .clr(clear));
  Register #(.width(1)) register_14 (.D(halt_in), .en(1'b1), .Q(halt_out), .clk(clk), .clr(clear));
  Register #(.width(32)) register_15 (.D(ALU_out_in), .en(1'b1), .Q(ALU_out_out), .clk(clk), .clr(clear));
  Register #(.width(26)) register_16 (.D(Addr_in), .en(1'b1), .Q(Addr_out), .clk(clk), .clr(clear));
  Register #(.width(32)) register_17 (.D(RF_R1_in), .en(1'b1), .Q(RF_R1_out), .clk(clk), .clr(clear));
  Register #(.width(32)) register_18 (.D(RF_R2_in), .en(1'b1), .Q(RF_R2_out), .clk(clk), .clr(clear));
  Register #(.width(1)) register_19 (.D(MemRead), .en(1'b1), .Q(MemRead_2), .clk(clk), .clr(clear));
endmodule

module MEM_WB (
  input  [31:0] PC_in,
  input  [31:0] PC_4_in,
  input  [31:0] IR_in,
  input  [1:0] selPC_in,
  input  [4:0] RW__in,
  input  [2:0] RF_Din_in,
  input  [31:0] DM_out_in,
  input  RegWrite_in,
  input  [31:0] Lo_in,
  input  [31:0] Hi_in,
  input  Branch_in,
  input  equal_in,
  input  [31:0] S_EXT_in,
  input  halt_in,
  input  [31:0] ALU_out_in,
  input  [25:0] Addr_in,
  input  [31:0] RF_R1_in,
  input  clk,
  input  clear,
  output [31:0] PC_out,
  output [31:0] PC_4_out,
  output [31:0] IR_out,
  output [1:0] selPC_out,
  output [4:0] RW__out,
  output [2:0] RF_Din_out,
  output [31:0] DM_out_out,
  output RegWrite_out,
  output [31:0] Lo_out,
  output [31:0] Hi_out,
  output Branch_out,
  output equal_out,
  output [31:0] S_EXT_out,
  output halt_out,
  output [31:0] ALU_out_out,
  output [25:0] Addr_out,
  output [31:0] RF_R1_out
);

  Register #(.width(32)) register_1 (.D(PC_in), .en(1'b1), .Q(PC_out), .clk(clk), .clr(clear));
  Register #(.width(32)) register_2 (.D(PC_4_in), .en(1'b1), .Q(PC_4_out), .clk(clk), .clr(clear));
  Register #(.width(32)) register_3 (.D(IR_in), .en(1'b1), .Q(IR_out), .clk(clk), .clr(clear));
  Register #(.width(2)) register_4 (.D(selPC_in), .en(1'b1), .Q(selPC_out), .clk(clk), .clr(clear));
  Register #(.width(5)) register_5 (.D(RW__in), .en(1'b1), .Q(RW__out), .clk(clk), .clr(clear));
  Register #(.width(3)) register_6 (.D(RF_Din_in), .en(1'b1), .Q(RF_Din_out), .clk(clk), .clr(clear));
  Register #(.width(32)) register_7 (.D(DM_out_in), .en(1'b1), .Q(DM_out_out), .clk(clk), .clr(clear));
  Register #(.width(1)) register_8 (.D(RegWrite_in), .en(1'b1), .Q(RegWrite_out), .clk(clk), .clr(clear));
  Register #(.width(32)) register_9 (.D(Lo_in), .en(1'b1), .Q(Lo_out), .clk(clk), .clr(clear));
  Register #(.width(32)) register_10 (.D(Hi_in), .en(1'b1), .Q(Hi_out), .clk(clk), .clr(clear));
  Register #(.width(1)) register_11 (.D(Branch_in), .en(1'b1), .Q(Branch_out), .clk(clk), .clr(clear));
  Register #(.width(1)) register_12 (.D(equal_in), .en(1'b1), .Q(equal_out), .clk(clk), .clr(clear));
  Register #(.width(32)) register_13 (.D(S_EXT_in), .en(1'b1), .Q(S_EXT_out), .clk(clk), .clr(clear));
  Register #(.width(1)) register_14 (.D(halt_in), .en(1'b1), .Q(halt_out), .clk(clk), .clr(clear));
  Register #(.width(32)) register_15 (.D(ALU_out_in), .en(1'b1), .Q(ALU_out_out), .clk(clk), .clr(clear));
  Register #(.width(26)) register_16 (.D(Addr_in), .en(1'b1), .Q(Addr_out), .clk(clk), .clr(clear));
  Register #(.width(32)) register_17 (.D(RF_R1_in), .en(1'b1), .Q(RF_R1_out), .clk(clk), .clr(clear));
endmodule

module jmp_detect (
  input  [1:0] selPC,
  input  Branch,
  input  equal,
  output jmp_signal
);

  wire and_1_out, comparator_1_eq, comparator_2_eq, multiplexer_1_out, not_1_out, or_1_out;

  not not_1 (not_1_out, equal);
  Comparator #(.width(2)) comparator_1 (.a(selPC), .b(2'b00), .eq(comparator_1_eq));  // open: gt, lt
  Comparator #(.width(2)) comparator_2 (.a(selPC), .b(2'b01), .eq(comparator_2_eq));  // open: gt, lt
  Multiplexer multiplexer_1 (.in0(equal), .in1(not_1_out), .out(multiplexer_1_out), .sel(Branch), .en(1'b1));
  and and_1 (and_1_out, comparator_2_eq, ~multiplexer_1_out);  // AND_Gate
  or or_1 (or_1_out, comparator_1_eq, and_1_out);
  not not_2 (jmp_signal, or_1_out);
endmodule

module data_redirection (
  input  [31:0] ALU_R1,
  input  [31:0] Lo,
  input  [31:0] Hi,
  input  [31:0] DM_out,
  input  [31:0] PC_4,
  input  [2:0] RF_Din,
  output [31:0] out_7
);

  Multiplexer #(.select(3), .width(32), .enable("false")) multiplexer_1 (
    .in0(ALU_R1), .in1(Lo), .in2(Hi), .in3(DM_out), .in4(PC_4), .out(out_7), .sel(RF_Din));  // open: in5, in6, in7
endmodule
