// Logisim project reg_read_detect.circ as structural Verilog: 3 circuits, main circuit main
module main (
  input  [5:0] OP,
  input  [5:0] funct,
  input  syscall,
  input  WE1,
  input  WE2,
  input  MemRead,
  input  [4:0] RW_1,
  input  [4:0] RW_2,
  input  [4:0] R1_num,
  input  [4:0] R2_num,
  input  [15:0] PCcount,
  output bubble,
  output [1:0] sel_R1,
  output [1:0] sel_R2,
  output [1:0] sel_v0,
  output [1:0] sel_a0
);

  wire and_1_out, and_2_out, and_3_out, and_4_out, and_5_out, and_6_out, and_8_out, and_9_out, and_10_out,
       and_11_out, and_12_out, and_13_out, and_14_out, and_15_out, and_16_out, and_17_out, and_18_out,
       and_19_out, and_20_out, and_21_out, and_22_out, and_23_out, comparator_1_eq, comparator_2_eq,
       comparator_3_eq, comparator_4_eq, comparator_5_eq, comparator_6_eq, comparator_7_eq, comparator_8_eq,
       comparator_9_eq, comparator_10_eq, comparator_11_eq, comparator_12_eq, comparator_13_eq,
       comparator_14_eq, comparator_15_eq, EX_RW_____0, MEM_RW_____0, not_3_out, not_4_out, not_5_out,
       not_6_out, not_7_out, or_1_out, or_2_out, or_3_out, or_4_out, or_5_out, or_6_out, R1_read, R2_read;

  Comparator #(.width(5), .mode("unsigned")) comparator_1 (
    .a(RW_1), .b({5{1'b0}}), .eq(comparator_1_eq));  // open: gt, lt
  Comparator #(.width(5), .mode("unsigned")) comparator_2 (
    .a(RW_2), .b({5{1'b0}}), .eq(comparator_2_eq));  // open: gt, lt
  Comparator #(.width(5), .mode("unsigned")) comparator_3 (
    .a(RW_1), .b(5'b00010), .eq(comparator_3_eq));  // open: gt, lt
  Comparator #(.width(5), .mode("unsigned")) comparator_4 (
    .a(RW_1), .b(5'b00100), .eq(comparator_4_eq));  // open: gt, lt
  not not_1 (EX_RW_____0, comparator_1_eq);
  not not_2 (MEM_RW_____0, comparator_2_eq);
  Comparator #(.width(5), .mode("unsigned")) comparator_5 (.a(R1_num), .b(RW_1), .eq(comparator_5_eq));  // open: gt, lt
  Comparator #(.width(5), .mode("unsigned")) comparator_6 (.a(R2_num), .b(RW_1), .eq(comparator_6_eq));  // open: gt, lt
  or or_1 (or_1_out, comparator_3_eq, comparator_4_eq);
  R1_read u_R1_read (
    .o1(OP[5]), .o2(OP[4]), .o3(OP[3]), .o4(OP[2]), .o5(OP[1]), .o6(OP[0]), .f1(funct[5]), .f2(funct[4]),
    .f3(funct[3]), .f4(funct[2]), .f5(funct[1]), .f6(funct[0]), .R1_Read(R1_read));
  and and_1 (and_1_out, comparator_5_eq, WE1, MemRead, EX_RW_____0);
  and and_2 (and_2_out, comparator_6_eq, WE1, MemRead, EX_RW_____0);
  and and_3 (and_3_out, or_1_out, WE1, MemRead);
  Comparator #(.width(16), .mode("unsigned")) comparator_7 (
    .a(PCcount), .b(16'h1), .eq(comparator_7_eq));  // open: gt, lt
  not not_3 (not_3_out, comparator_7_eq);
  and and_4 (and_4_out, R1_read, and_1_out);
  and and_5 (and_5_out, R2_read, and_2_out);
  and and_6 (and_6_out, syscall, and_3_out);
  or or_2 (or_2_out, and_4_out, and_5_out, and_6_out);
  R2_read u_R2_read (
    .o1(OP[5]), .o2(OP[4]), .o3(OP[3]), .o4(OP[2]), .o5(OP[1]), .o6(OP[0]), .f1(funct[5]), .f2(funct[4]),
    .f3(funct[3]), .f4(funct[2]), .f5(funct[1]), .f6(funct[0]), .R2_read(R2_read));
  and and_7 (bubble, or_2_out, not_3_out);
  Comparator #(.width(5), .mode("unsigned")) comparator_8 (.a(R1_num), .b(RW_1), .eq(comparator_8_eq));  // open: gt, lt
  Comparator #(.width(5), .mode("unsigned")) comparator_9 (.a(R1_num), .b(RW_2), .eq(comparator_9_eq));  // open: gt, lt
  Comparator #(.width(5), .mode("unsigned")) comparator_10 (
    .a(R2_num), .b(RW_1), .eq(comparator_10_eq));  // open: gt, lt
  Comparator #(.width(5), .mode("unsigned")) comparator_11 (
    .a(R2_num), .b(RW_2), .eq(comparator_11_eq));  // open: gt, lt
  Comparator #(.width(5), .mode("unsigned")) comparator_12 (
    .a(5'b00010), .b(RW_1), .eq(comparator_12_eq));  // open: gt, lt
  Comparator #(.width(5), .mode("unsigned")) comparator_13 (
    .a(5'b00010), .b(RW_2), .eq(comparator_13_eq));  // open: gt, lt
  Comparator #(.width(5), .mode("unsigned")) comparator_14 (
    .a(5'b00100), .b(RW_1), .eq(comparator_14_eq));  // open: gt, lt
  Comparator #(.width(5), .mode("unsigned")) comparator_15 (
    .a(5'b00100), .b(RW_2), .eq(comparator_15_eq));  // open: gt, lt
  and and_8 (and_8_out, comparator_8_eq, WE1, EX_RW_____0);
  and and_9 (and_9_out, comparator_9_eq, WE2, MEM_RW_____0);
  and and_10 (and_10_out, comparator_10_eq, WE1, EX_RW_____0);
  and and_11 (and_11_out, comparator_11_eq, WE2, MEM_RW_____0);
  and and_12 (and_12_out, comparator_12_eq, WE1);
  and and_13 (and_13_out, comparator_13_eq, WE2);
  and and_14 (and_14_out, comparator_14_eq, WE1);
  and and_15 (and_15_out, comparator_15_eq, WE2);
  and and_16 (and_16_out, R1_read, and_8_out);
  and and_17 (and_17_out, R1_read, and_9_out);
  and and_18 (and_18_out, R2_read, and_10_out);
  and and_19 (and_19_out, R2_read, and_11_out);
  and and_20 (and_20_out, syscall, and_12_out);
  and and_21 (and_21_out, syscall, and_13_out);
  and and_22 (and_22_out, syscall, and_14_out);
  and and_23 (and_23_out, syscall, and_15_out);
  not not_4 (not_4_out, bubble);
  or or_3 (or_3_out, and_16_out, and_17_out);
  not not_5 (not_5_out, bubble);
  or or_4 (or_4_out, and_18_out, and_19_out);
  not not_6 (not_6_out, bubble);
  or or_5 (or_5_out, and_20_out, and_21_out);
  not not_7 (not_7_out, bubble);
  or or_6 (or_6_out, and_22_out, and_23_out);
  and and_24 (sel_R1[0], not_4_out, and_16_out);
  and and_25 (sel_R1[1], not_4_out, or_3_out);
  and and_26 (sel_R2[0], not_5_out, and_18_out);
  and and_27 (sel_R2[1], not_5_out, or_4_out);
  and and_28 (sel_v0[0], not_6_out, and_20_out);
  and and_29 (sel_v0[1], not_6_out, or_5_out);
  and and_30 (sel_a0[0], not_7_out, and_22_out);
  and and_31 (sel_a0[1], not_7_out, or_6_out);
endmodule

module R1_read (
  input  o1,
  input  o2,
  input  o3,
  input  o4,
  input  o5,
  input  o6,
  input  f1,
  input  f2,
  input  f3,
  input  f4,
  input  f5,
  input  f6,
  output R1_Read
);

  wire and_1_out, and_2_out, and_3_out, and_4_out, and_5_out, not_1_out, not_2_out, not_3_out, not_4_out,
       not_5_out, not_6_out, not_7_out, not_8_out, not_9_out, not_10_out, not_11_out, not_12_out, not_13_out,
       not_14_out, not_15_out, not_16_out, not_17_out, not_18_out, not_19_out, or_1_out;

  not not_1 (not_1_out, f3);
  not not_2 (not_2_out, f4);
  not not_3 (not_3_out, f5);
  not not_4 (not_4_out, f3);
  not not_5 (not_5_out, f4);
  not not_6 (not_6_out, f2);
  not not_7 (not_7_out, f5);
  not not_8 (not_8_out, o1);
  not not_9 (not_9_out, o2);
  not not_10 (not_10_out, o3);
  not not_11 (not_11_out, o4);
  not not_12 (not_12_out, o5);
  not not_13 (not_13_out, o6);
  not not_14 (not_14_out, f1);
  not not_15 (not_15_out, f6);
  and and_1 (and_1_out, f2, not_1_out, not_2_out, not_3_out);
  or or_1 (or_1_out, and_1_out, and_2_out, and_3_out);
  and and_2 (and_2_out, f2, not_4_out, not_5_out, f5);
  and and_3 (and_3_out, not_6_out, f3, f4, not_7_out);
  not not_16 (not_16_out, o1);
  not not_17 (not_17_out, o2);
  not not_18 (not_18_out, o3);
  not not_19 (not_19_out, o4);
  and and_4 (and_4_out, not_8_out, not_9_out, not_10_out, not_11_out, not_12_out, not_13_out, not_14_out, not_15_out, or_1_out);
  and and_5 (and_5_out, not_16_out, not_17_out, not_18_out, not_19_out, o5);
  nor nor_1 (R1_Read, and_4_out, and_5_out);
endmodule

module R2_read (
  input  o1,
  input  o2,
  input  o3,
  input  o4,
  input  o5,
  input  o6,
  input  f1,
  input  f2,
  input  f3,
  input  f4,
  input  f5,
  input  f6,
  output R2_read
);

  wire and_1_out, and_2_out, and_3_out, and_4_out, and_5_out, and_6_out, and_7_out, and_8_out, and_9_out,
       not_1_out, not_2_out, not_3_out, not_4_out, not_5_out, not_6_out, not_7_out, not_8_out, not_9_out,
       not_10_out, not_11_out, not_12_out, not_13_out, not_14_out, not_15_out, not_16_out, not_17_out,
       not_18_out, not_19_out, not_20_out, not_21_out, not_22_out, not_23_out, not_24_out, not_25_out,
       not_26_out, or_1_out, or_2_out, or_3_out, or_4_out;

  not not_1 (not_1_out, f5);
  not not_2 (not_2_out, f6);
  not not_3 (not_3_out, f5);
  not not_4 (not_4_out, f5);
  and and_1 (and_1_out, not_4_out, not_5_out);
  not not_5 (not_5_out, f6);
  and and_2 (and_2_out, f5, f6);
  not not_6 (not_6_out, f2);
  not not_7 (not_7_out, f3);
  not not_8 (not_8_out, f4);
  or or_1 (or_1_out, not_1_out, not_2_out);
  not not_9 (not_9_out, f2);
  not not_10 (not_10_out, f3);
  or or_2 (or_2_out, not_3_out, f6);
  not not_11 (not_11_out, f1);
  not not_12 (not_12_out, f4);
  or or_3 (or_3_out, and_1_out, and_2_out);
  not not_13 (not_13_out, f2);
  not not_14 (not_14_out, f4);
  and and_3 (and_3_out, f1, not_6_out, not_7_out, not_8_out, or_1_out);
  and and_4 (and_4_out, f1, not_9_out, not_10_out, f4, or_2_out);
  and and_5 (and_5_out, not_11_out, f2, f3, not_12_out, or_3_out);
  and and_6 (and_6_out, f1, not_13_out, f3, not_14_out, f5);
  not not_15 (not_15_out, o1);
  not not_16 (not_16_out, o2);
  not not_17 (not_17_out, o3);
  not not_18 (not_18_out, o4);
  not not_19 (not_19_out, o5);
  not not_20 (not_20_out, o6);
  or or_4 (or_4_out, and_3_out, and_4_out, and_5_out, and_6_out);
  not not_21 (not_21_out, o2);
  not not_22 (not_22_out, o4);
  not not_23 (not_23_out, o1);
  not not_24 (not_24_out, o2);
  not not_25 (not_25_out, o3);
  not not_26 (not_26_out, o5);
  and and_7 (and_7_out, not_15_out, not_16_out, not_17_out, not_18_out, not_19_out, not_20_out, or_4_out);
  and and_8 (and_8_out, o1, not_21_out, o3, not_22_out, o5, o6);
  and and_9 (and_9_out, not_23_out, not_24_out, not_25_out, o4, not_26_out);
  or or_5 (R2_read, and_7_out, and_8_out, and_9_out);
endmodule
