// Logisim project control_unit.circ as structural Verilog: 21 circuits, main circuit main
module main (
  input  [5:0] OP,
  input  [5:0] funct,
  output Rf_R1,
  output [1:0] PC,
  output [2:0] RF_Din,
  output [1:0] RF_W,
  output MemWrite,
  output [1:0] ALU_B,
  output RegWrite,
  output Branch,
  output Hi_Lo,
  output [3:0] ALU_OP,
  output syscall,
  output MemRead
);

  PC2 pc2_1 (
    .o1(OP[5]), .o2(OP[4]), .o3(OP[3]), .o4(OP[2]), .o5(OP[1]), .o6(OP[0]), .f1(funct[5]), .f2(funct[4]),
    .f3(funct[3]), .f4(funct[2]), .f5(funct[1]), .f6(funct[0]), .pc2(PC[1]));
  PC1 pc1_1 (
    .o1(OP[5]), .o2(OP[4]), .o3(OP[3]), .o4(OP[2]), .o5(OP[1]), .o6(OP[0]), .f1(funct[5]), .f2(funct[4]),
    .f3(funct[3]), .f4(funct[2]), .f5(funct[1]), .f6(funct[0]), .pc1(PC[0]));
  RF_W2 rf_w2_1 (
    .o1(OP[5]), .o2(OP[4]), .o3(OP[3]), .o4(OP[2]), .o5(OP[1]), .o6(OP[0]), .f1(funct[5]), .f2(funct[4]),
    .f3(funct[3]), .f4(funct[2]), .f5(funct[1]), .f6(funct[0]), .RF_W2(RF_W[1]));
  RF_W1 rf_w1_1 (
    .o1(OP[5]), .o2(OP[4]), .o3(OP[3]), .o4(OP[2]), .o5(OP[1]), .o6(OP[0]), .f1(funct[5]), .f2(funct[4]),
    .f3(funct[3]), .f4(funct[2]), .f5(funct[1]), .f6(funct[0]), .RF_W1(RF_W[0]));
  ALU_B2 alu_b2_1 (
    .o1(OP[5]), .o2(OP[4]), .o3(OP[3]), .o4(OP[2]), .o5(OP[1]), .o6(OP[0]), .f1(funct[5]), .f2(funct[4]),
    .f3(funct[3]), .f4(funct[2]), .f5(funct[1]), .f6(funct[0]), .ALU_B2(ALU_B[1]));
  ALU_B1 alu_b1_1 (
    .o1(OP[5]), .o2(OP[4]), .o3(OP[3]), .o4(OP[2]), .o5(OP[1]), .o6(OP[0]), .f1(funct[5]), .f2(funct[4]),
    .f3(funct[3]), .f4(funct[2]), .f5(funct[1]), .f6(funct[0]), .ALU_B1(ALU_B[0]));
  ALU_OP1 alu_op1_1 (
    .o1(OP[5]), .o2(OP[4]), .o3(OP[3]), .o4(OP[2]), .o5(OP[1]), .o6(OP[0]), .f1(funct[5]), .f2(funct[4]),
    .f3(funct[3]), .f4(funct[2]), .f5(funct[1]), .f6(funct[0]), .ALU_OP1(ALU_OP[3]));
  ALU_OP2 alu_op2_1 (
    .o1(OP[5]), .o2(OP[4]), .o3(OP[3]), .o4(OP[2]), .o5(OP[1]), .o6(OP[0]), .f1(funct[5]), .f2(funct[4]),
    .f3(funct[3]), .f4(funct[2]), .f5(funct[1]), .f6(funct[0]), .ALU_OP2(ALU_OP[2]));
  ALU_OP3 alu_op3_1 (
    .o1(OP[5]), .o2(OP[4]), .o3(OP[3]), .o4(OP[2]), .o5(OP[1]), .o6(OP[0]), .f1(funct[5]), .f2(funct[4]),
    .f3(funct[3]), .f4(funct[2]), .f5(funct[1]), .f6(funct[0]), .ALU_OP3(ALU_OP[1]));
  ALU_OP4 alu_op4_1 (
    .o1(OP[5]), .o2(OP[4]), .o3(OP[3]), .o4(OP[2]), .o5(OP[1]), .o6(OP[0]), .f1(funct[5]), .f2(funct[4]),
    .f3(funct[3]), .f4(funct[2]), .f5(funct[1]), .f6(funct[0]), .ALU_OP4(ALU_OP[0]));
  MemRead memread_1 (
    .o1(OP[5]), .o2(OP[4]), .o3(OP[3]), .o4(OP[2]), .o5(OP[1]), .o6(OP[0]), .f1(funct[5]), .f2(funct[4]),
    .f3(funct[3]), .f4(funct[2]), .f5(funct[1]), .f6(funct[0]), .MemRead(MemRead));
  RF_R1 rf_r1_1 (
    .o1(OP[5]), .o2(OP[4]), .o3(OP[3]), .o4(OP[2]), .o5(OP[1]), .o6(OP[0]), .f1(funct[5]), .f2(funct[4]),
    .f3(funct[3]), .f4(funct[2]), .f5(funct[1]), .f6(funct[0]), .RF_R1(Rf_R1));
  RF_Din3 rf_din3_1 (
    .o1(OP[5]), .o2(OP[4]), .o3(OP[3]), .o4(OP[2]), .o5(OP[1]), .o6(OP[0]), .f1(funct[5]), .f2(funct[4]),
    .f3(funct[3]), .f4(funct[2]), .f5(funct[1]), .f6(funct[0]), .RF_Din3(RF_Din[2]));
  RF_Din2 rf_din2_1 (
    .o1(OP[5]), .o2(OP[4]), .o3(OP[3]), .o4(OP[2]), .o5(OP[1]), .o6(OP[0]), .f1(funct[5]), .f2(funct[4]),
    .f3(funct[3]), .f4(funct[2]), .f5(funct[1]), .f6(funct[0]), .RF_Din2(RF_Din[1]));
  RF_Din1 rf_din1_1 (
    .o1(OP[5]), .o2(OP[4]), .o3(OP[3]), .o4(OP[2]), .o5(OP[1]), .o6(OP[0]), .f1(funct[5]), .f2(funct[4]),
    .f3(funct[3]), .f4(funct[2]), .f5(funct[1]), .f6(funct[0]), .RF_Din1(RF_Din[0]));
  MemWrite memwrite_1 (
    .o1(OP[5]), .o2(OP[4]), .o3(OP[3]), .o4(OP[2]), .o5(OP[1]), .o6(OP[0]), .f1(funct[5]), .f2(funct[4]),
    .f3(funct[3]), .f4(funct[2]), .f5(funct[1]), .f6(funct[0]), .MemWrite(MemWrite));
  RegWrite regwrite_1 (
    .o1(OP[5]), .o2(OP[4]), .o3(OP[3]), .o4(OP[2]), .o5(OP[1]), .o6(OP[0]), .f1(funct[5]), .f2(funct[4]),
    .f3(funct[3]), .f4(funct[2]), .f5(funct[1]), .f6(funct[0]), .RegWrite(RegWrite));
  Branch branch_1 (
    .o1(OP[5]), .o2(OP[4]), .o3(OP[3]), .o4(OP[2]), .o5(OP[1]), .o6(OP[0]), .f1(funct[5]), .f2(funct[4]),
    .f3(funct[3]), .f4(funct[2]), .f5(funct[1]), .f6(funct[0]), .Branch(Branch));
  Hi_Lo hi_lo_1 (
    .o1(OP[5]), .o2(OP[4]), .o3(OP[3]), .o4(OP[2]), .o5(OP[1]), .o6(OP[0]), .f1(funct[5]), .f2(funct[4]),
    .f3(funct[3]), .f4(funct[2]), .f5(funct[1]), .f6(funct[0]), .Hi_Lo(Hi_Lo));
  syscall syscall_1 (
    .o1(OP[5]), .o2(OP[4]), .o3(OP[3]), .o4(OP[2]), .o5(OP[1]), .o6(OP[0]), .f1(funct[5]), .f2(funct[4]),
    .f3(funct[3]), .f4(funct[2]), .f5(funct[1]), .f6(funct[0]), .syscall(syscall));
endmodule

module PC2 (
  input  o1,
  input  o2,
  input  o3,
  input  o4,
  input  o5,
  input  o6,
  input  f1,
  input  f2,
  input  f3,
  input  f4,
  input  f5,
  input  f6,
  output pc2
);

  wire and_1_out, not_1_out, not_2_out, not_3_out, not_4_out, not_5_out, not_6_out, not_7_out, not_8_out,
       not_9_out, not_10_out, not_11_out, or_1_out;

  not not_1 (not_1_out, o5);
  not not_2 (not_2_out, o6);
  not not_3 (not_3_out, f1);
  not not_4 (not_4_out, f2);
  not not_5 (not_5_out, f4);
  not not_6 (not_6_out, f5);
  not not_7 (not_7_out, f6);
  and and_1 (and_1_out, not_1_out, not_2_out, not_3_out, not_4_out, f3, not_5_out, not_6_out, not_7_out);
  not not_8 (not_8_out, o1);
  not not_9 (not_9_out, o2);
  not not_10 (not_10_out, o3);
  not not_11 (not_11_out, o4);
  or or_1 (or_1_out, o5, and_1_out);
  and and_2 (pc2, not_8_out, not_9_out, not_10_out, not_11_out, or_1_out);
endmodule

module PC1 (
  input  o1,
  input  o2,
  input  o3,
  input  o4,
  input  o5,
  input  o6,
  input  f1,
  input  f2,
  input  f3,
  input  f4,
  input  f5,
  input  f6,
  output pc1
);

  wire and_1_out, not_1_out, not_2_out, not_3_out, not_4_out, not_5_out, not_6_out, not_7_out, not_8_out,
       not_9_out, not_10_out, not_11_out, or_1_out;

  not not_1 (not_1_out, o4);
  not not_2 (not_2_out, o6);
  not not_3 (not_3_out, f1);
  not not_4 (not_4_out, f2);
  not not_5 (not_5_out, f4);
  not not_6 (not_6_out, f5);
  not not_7 (not_7_out, f6);
  and and_1 (and_1_out, not_1_out, not_2_out, not_3_out, not_4_out, f3, not_5_out, not_6_out, not_7_out);
  not not_8 (not_8_out, o1);
  not not_9 (not_9_out, o2);
  not not_10 (not_10_out, o3);
  not not_11 (not_11_out, o5);
  or or_1 (or_1_out, o4, and_1_out);
  and and_2 (pc1, not_8_out, not_9_out, not_10_out, not_11_out, or_1_out);
endmodule

module RF_R1 (
  input  o1,
  input  o2,
  input  o3,
  input  o4,
  input  o5,
  input  o6,
  input  f1,
  input  f2,
  input  f3,
  input  f4,
  input  f5,
  input  f6,
  output RF_R1
);

  wire and_1_out, and_2_out, and_3_out, not_1_out, not_2_out, not_3_out, not_4_out, not_5_out, not_6_out,
       not_7_out, not_8_out, not_9_out, not_10_out, not_11_out, not_12_out, not_13_out, or_1_out;

  not not_1 (not_1_out, f5);
  and and_1 (and_1_out, not_1_out, not_2_out);
  not not_2 (not_2_out, f6);
  and and_2 (and_2_out, f5, f6);
  and and_3 (and_3_out, f5, not_3_out);
  not not_3 (not_3_out, f6);
  not not_4 (not_4_out, o1);
  not not_5 (not_5_out, o2);
  not not_6 (not_6_out, o3);
  not not_7 (not_7_out, o4);
  not not_8 (not_8_out, o5);
  not not_9 (not_9_out, o6);
  not not_10 (not_10_out, f1);
  not not_11 (not_11_out, f2);
  not not_12 (not_12_out, f3);
  not not_13 (not_13_out, f4);
  or or_1 (or_1_out, and_1_out, and_2_out, and_3_out);
  and and_4 (RF_R1, not_4_out, not_5_out, not_6_out, not_7_out, not_8_out, not_9_out, not_10_out, not_11_out, not_12_out, not_13_out, or_1_out);
endmodule

module RF_W2 (
  input  o1,
  input  o2,
  input  o3,
  input  o4,
  input  o5,
  input  o6,
  input  f1,
  input  f2,
  input  f3,
  input  f4,
  input  f5,
  input  f6,
  output RF_W2
);

  wire not_1_out, not_2_out, not_3_out, not_4_out;

  not not_1 (not_1_out, o1);
  not not_2 (not_2_out, o2);
  not not_3 (not_3_out, o3);
  not not_4 (not_4_out, o4);
  and and_1 (RF_W2, not_1_out, not_2_out, not_3_out, not_4_out, o5, o6);
endmodule

module RF_W1 (
  input  o1,
  input  o2,
  input  o3,
  input  o4,
  input  o5,
  input  o6,
  input  f1,
  input  f2,
  input  f3,
  input  f4,
  input  f5,
  input  f6,
  output RF_W1
);

  wire and_1_out, and_2_out, and_3_out, and_4_out, and_5_out, and_6_out, and_7_out, not_1_out, not_2_out,
       not_3_out, not_4_out, not_5_out, not_6_out, not_7_out, not_8_out, not_9_out, not_10_out, not_11_out,
       not_12_out, not_13_out, not_14_out, not_15_out, or_1_out;

  not not_1 (not_1_out, o4);
  not not_2 (not_2_out, o5);
  and and_1 (and_1_out, not_1_out, not_2_out, not_3_out);
  not not_3 (not_3_out, o6);
  not not_4 (not_4_out, o4);
  and and_2 (and_2_out, not_4_out, not_5_out, o6);
  not not_5 (not_5_out, o5);
  not not_6 (not_6_out, o5);
  and and_3 (and_3_out, o4, not_6_out, not_7_out);
  not not_7 (not_7_out, o6);
  and and_4 (and_4_out, o4, not_8_out, o6);
  not not_8 (not_8_out, o5);
  not not_9 (not_9_out, o4);
  and and_5 (and_5_out, not_9_out, o5, not_10_out);
  not not_10 (not_10_out, o6);
  not not_11 (not_11_out, o1);
  not not_12 (not_12_out, o2);
  or or_1 (or_1_out, and_1_out, and_2_out, and_3_out, and_4_out, and_5_out);
  not not_13 (not_13_out, o2);
  not not_14 (not_14_out, o3);
  not not_15 (not_15_out, o4);
  and and_6 (and_6_out, not_11_out, not_12_out, o3, or_1_out);
  and and_7 (and_7_out, o1, not_13_out, not_14_out, not_15_out, o5, o6);
  or or_2 (RF_W1, and_6_out, and_7_out);
endmodule

module RF_Din3 (
  input  o1,
  input  o2,
  input  o3,
  input  o4,
  input  o5,
  input  o6,
  input  f1,
  input  f2,
  input  f3,
  input  f4,
  input  f5,
  input  f6,
  output RF_Din3
);

  wire not_1_out, not_2_out, not_3_out, not_4_out;

  not not_1 (not_1_out, o1);
  not not_2 (not_2_out, o2);
  not not_3 (not_3_out, o3);
  not not_4 (not_4_out, o4);
  and and_1 (RF_Din3, not_1_out, not_2_out, not_3_out, not_4_out, o5, o6);
endmodule

module RF_Din2 (
  input  o1,
  input  o2,
  input  o3,
  input  o4,
  input  o5,
  input  o6,
  input  f1,
  input  f2,
  input  f3,
  input  f4,
  input  f5,
  input  f6,
  output RF_Din2
);

  wire and_1_out, and_2_out, not_1_out, not_2_out, not_3_out, not_4_out, not_5_out, not_6_out, not_7_out,
       not_8_out, not_9_out, not_10_out, not_11_out, or_1_out;

  not not_1 (not_1_out, o1);
  not not_2 (not_2_out, o5);
  not not_3 (not_3_out, o6);
  not not_4 (not_4_out, f1);
  not not_5 (not_5_out, f3);
  not not_6 (not_6_out, f4);
  not not_7 (not_7_out, f5);
  not not_8 (not_8_out, f6);
  and and_1 (and_1_out, not_1_out, not_2_out, not_3_out, not_4_out, f2, not_5_out, not_6_out, not_7_out, not_8_out);
  and and_2 (and_2_out, o1, o5, o6);
  not not_9 (not_9_out, o2);
  not not_10 (not_10_out, o3);
  not not_11 (not_11_out, o4);
  or or_1 (or_1_out, and_1_out, and_2_out);
  and and_3 (RF_Din2, not_9_out, not_10_out, not_11_out, or_1_out);
endmodule

module RF_Din1 (
  input  o1,
  input  o2,
  input  o3,
  input  o4,
  input  o5,
  input  o6,
  input  f1,
  input  f2,
  input  f3,
  input  f4,
  input  f5,
  input  f6,
  output RF_Din1
);

  wire and_1_out, and_2_out, not_1_out, not_2_out, not_3_out, not_4_out, not_5_out, not_6_out, not_7_out,
       not_8_out, not_9_out, not_10_out, or_1_out;

  not not_1 (not_1_out, o1);
  not not_2 (not_2_out, o5);
  not not_3 (not_3_out, o6);
  not not_4 (not_4_out, f1);
  not not_5 (not_5_out, f3);
  not not_6 (not_6_out, f4);
  not not_7 (not_7_out, f6);
  and and_1 (and_1_out, not_1_out, not_2_out, not_3_out, not_4_out, f2, not_5_out, not_6_out, f5, not_7_out);
  and and_2 (and_2_out, o1, o5, o6);
  not not_8 (not_8_out, o2);
  not not_9 (not_9_out, o3);
  not not_10 (not_10_out, o4);
  or or_1 (or_1_out, and_1_out, and_2_out);
  and and_3 (RF_Din1, not_8_out, not_9_out, not_10_out, or_1_out);
endmodule

module ALU_B2 (
  input  o1,
  input  o2,
  input  o3,
  input  o4,
  input  o5,
  input  o6,
  input  f1,
  input  f2,
  input  f3,
  input  f4,
  input  f5,
  input  f6,
  output ALU_B2
);

  wire and_1_out, and_2_out, and_3_out, and_4_out, and_5_out, not_1_out, not_2_out, not_3_out, not_4_out,
       not_5_out, not_6_out, not_7_out, not_8_out, not_9_out, not_10_out, not_11_out, not_12_out, not_13_out,
       not_14_out, not_15_out, not_16_out, or_1_out;

  not not_1 (not_1_out, f5);
  and and_1 (and_1_out, not_1_out, not_2_out);
  not not_2 (not_2_out, f6);
  and and_2 (and_2_out, f5, f6);
  and and_3 (and_3_out, f5, not_3_out);
  not not_3 (not_3_out, f6);
  not not_4 (not_4_out, o1);
  not not_5 (not_5_out, o2);
  not not_6 (not_6_out, o3);
  not not_7 (not_7_out, o4);
  not not_8 (not_8_out, o5);
  not not_9 (not_9_out, o6);
  not not_10 (not_10_out, f1);
  not not_11 (not_11_out, f2);
  not not_12 (not_12_out, f3);
  not not_13 (not_13_out, f4);
  or or_1 (or_1_out, and_1_out, and_2_out, and_3_out);
  not not_14 (not_14_out, o1);
  not not_15 (not_15_out, o2);
  not not_16 (not_16_out, o5);
  and and_4 (and_4_out, not_4_out, not_5_out, not_6_out, not_7_out, not_8_out, not_9_out, not_10_out, not_11_out, not_12_out, not_13_out, or_1_out);
  and and_5 (and_5_out, not_14_out, not_15_out, o3, o4, not_16_out);
  or or_2 (ALU_B2, and_4_out, and_5_out);
endmodule

module ALU_B1 (
  input  o1,
  input  o2,
  input  o3,
  input  o4,
  input  o5,
  input  o6,
  input  f1,
  input  f2,
  input  f3,
  input  f4,
  input  f5,
  input  f6,
  output ALU_B1
);

  wire and_1_out, and_2_out, and_3_out, and_4_out, and_5_out, and_6_out, and_7_out, and_8_out, not_1_out,
       not_2_out, not_3_out, not_4_out, not_5_out, not_6_out, not_7_out, not_8_out, not_9_out, not_10_out,
       not_11_out, not_12_out, not_13_out, not_14_out, not_15_out, not_16_out, not_17_out, not_18_out,
       not_19_out, or_1_out, or_2_out;

  not not_1 (not_1_out, f5);
  and and_1 (and_1_out, not_1_out, not_2_out);
  not not_2 (not_2_out, f6);
  and and_2 (and_2_out, f5, f6);
  and and_3 (and_3_out, f5, not_3_out);
  not not_3 (not_3_out, f6);
  not not_4 (not_4_out, o1);
  not not_5 (not_5_out, o5);
  not not_6 (not_6_out, o1);
  not not_7 (not_7_out, o6);
  not not_8 (not_8_out, o1);
  not not_9 (not_9_out, o2);
  not not_10 (not_10_out, o3);
  not not_11 (not_11_out, o4);
  not not_12 (not_12_out, o5);
  not not_13 (not_13_out, o6);
  not not_14 (not_14_out, f1);
  not not_15 (not_15_out, f2);
  not not_16 (not_16_out, f3);
  not not_17 (not_17_out, f4);
  or or_1 (or_1_out, and_1_out, and_2_out, and_3_out);
  and and_4 (and_4_out, not_4_out, o3, not_5_out);
  and and_5 (and_5_out, o1, o5, o6);
  and and_6 (and_6_out, not_6_out, o3, o5, not_7_out);
  not not_18 (not_18_out, o2);
  not not_19 (not_19_out, o4);
  or or_2 (or_2_out, and_4_out, and_5_out, and_6_out);
  and and_7 (and_7_out, not_8_out, not_9_out, not_10_out, not_11_out, not_12_out, not_13_out, not_14_out, not_15_out, not_16_out, not_17_out, or_1_out);
  and and_8 (and_8_out, not_18_out, not_19_out, or_2_out);
  or or_3 (ALU_B1, and_7_out, and_8_out);
endmodule

module ALU_OP1 (
  input  o1,
  input  o2,
  input  o3,
  input  o4,
  input  o5,
  input  o6,
  input  f1,
  input  f2,
  input  f3,
  input  f4,
  input  f5,
  input  f6,
  output ALU_OP1
);

  wire and_1_out, and_2_out, and_3_out, and_4_out, and_5_out, and_6_out, and_7_out, not_1_out, not_2_out,
       not_3_out, not_4_out, not_5_out, not_6_out, not_7_out, not_8_out, not_9_out, not_10_out, not_11_out,
       not_12_out, not_13_out, not_14_out, not_15_out, not_16_out, not_17_out, not_18_out, or_1_out, or_2_out;

  not not_1 (not_1_out, o5);
  not not_2 (not_2_out, o4);
  not not_3 (not_3_out, o6);
  not not_4 (not_4_out, f2);
  not not_5 (not_5_out, f3);
  not not_6 (not_6_out, f5);
  not not_7 (not_7_out, f2);
  not not_8 (not_8_out, f3);
  not not_9 (not_9_out, f2);
  not not_10 (not_10_out, f4);
  and and_1 (and_1_out, o4, not_1_out, o6);
  and and_2 (and_2_out, not_2_out, o5, not_3_out);
  and and_3 (and_3_out, f1, not_4_out, not_5_out, f4, not_6_out, f6);
  and and_4 (and_4_out, f1, not_7_out, not_8_out, f4, f5, f6);
  and and_5 (and_5_out, f1, not_9_out, f3, not_10_out, f5);
  not not_11 (not_11_out, o1);
  not not_12 (not_12_out, o2);
  or or_1 (or_1_out, and_1_out, and_2_out);
  not not_13 (not_13_out, o1);
  not not_14 (not_14_out, o2);
  not not_15 (not_15_out, o3);
  not not_16 (not_16_out, o4);
  not not_17 (not_17_out, o5);
  not not_18 (not_18_out, o6);
  or or_2 (or_2_out, and_3_out, and_4_out, and_5_out);
  and and_6 (and_6_out, not_11_out, not_12_out, o3, or_1_out);
  and and_7 (and_7_out, not_13_out, not_14_out, not_15_out, not_16_out, not_17_out, not_18_out, or_2_out);
  or or_3 (ALU_OP1, and_6_out, and_7_out);
endmodule

module ALU_OP2 (
  input  o1,
  input  o2,
  input  o3,
  input  o4,
  input  o5,
  input  o6,
  input  f1,
  input  f2,
  input  f3,
  input  f4,
  input  f5,
  input  f6,
  output ALU_OP2
);

  wire and_1_out, and_2_out, and_3_out, and_4_out, and_5_out, and_6_out, and_7_out, and_8_out, and_9_out,
       and_10_out, not_1_out, not_2_out, not_3_out, not_4_out, not_5_out, not_6_out, not_7_out, not_8_out,
       not_9_out, not_10_out, not_11_out, not_12_out, not_13_out, not_14_out, not_15_out, not_16_out,
       not_17_out, not_18_out, not_19_out, not_20_out, not_21_out, not_22_out, not_23_out, not_24_out,
       not_25_out, not_26_out, not_27_out, not_28_out, not_29_out, not_30_out, or_1_out, or_2_out;

  not not_1 (not_1_out, f2);
  not not_2 (not_2_out, f3);
  not not_3 (not_3_out, f4);
  not not_4 (not_4_out, f5);
  not not_5 (not_5_out, f2);
  not not_6 (not_6_out, f3);
  not not_7 (not_7_out, f5);
  not not_8 (not_8_out, f6);
  not not_9 (not_9_out, f2);
  not not_10 (not_10_out, f3);
  not not_11 (not_11_out, f4);
  not not_12 (not_12_out, f6);
  not not_13 (not_13_out, f1);
  not not_14 (not_14_out, f4);
  not not_15 (not_15_out, f2);
  not not_16 (not_16_out, f4);
  not not_17 (not_17_out, o4);
  not not_18 (not_18_out, o5);
  not not_19 (not_19_out, o5);
  not not_20 (not_20_out, o6);
  and and_1 (and_1_out, f1, not_1_out, not_2_out, not_3_out, not_4_out);
  and and_2 (and_2_out, f1, not_5_out, not_6_out, f4, not_7_out, not_8_out);
  and and_3 (and_3_out, f1, not_9_out, not_10_out, not_11_out, f5, not_12_out);
  and and_4 (and_4_out, not_13_out, f2, f3, not_14_out, f5, f6);
  and and_5 (and_5_out, f1, not_15_out, f3, not_16_out, f5, f6);
  and and_6 (and_6_out, not_17_out, not_18_out);
  and and_7 (and_7_out, o4, not_19_out, not_20_out);
  not not_21 (not_21_out, o1);
  not not_22 (not_22_out, o2);
  not not_23 (not_23_out, o3);
  not not_24 (not_24_out, o4);
  not not_25 (not_25_out, o5);
  not not_26 (not_26_out, o6);
  or or_1 (or_1_out, and_1_out, and_2_out, and_3_out, and_4_out, and_5_out);
  not not_27 (not_27_out, o1);
  not not_28 (not_28_out, o2);
  or or_2 (or_2_out, and_6_out, and_7_out);
  not not_29 (not_29_out, o2);
  not not_30 (not_30_out, o4);
  and and_8 (and_8_out, not_21_out, not_22_out, not_23_out, not_24_out, not_25_out, not_26_out, or_1_out);
  and and_9 (and_9_out, not_27_out, not_28_out, o3, or_2_out);
  and and_10 (and_10_out, o1, not_29_out, not_30_out, o5, o6);
  or or_3 (ALU_OP2, and_8_out, and_9_out, and_10_out);
endmodule

module ALU_OP3 (
  input  o1,
  input  o2,
  input  o3,
  input  o4,
  input  o5,
  input  o6,
  input  f1,
  input  f2,
  input  f3,
  input  f4,
  input  f5,
  input  f6,
  output ALU_OP3
);

  wire and_1_out, and_2_out, and_3_out, and_4_out, and_5_out, and_6_out, and_7_out, and_8_out, and_9_out,
       and_10_out, and_11_out, not_1_out, not_2_out, not_3_out, not_4_out, not_5_out, not_6_out, not_7_out,
       not_8_out, not_9_out, not_10_out, not_11_out, not_12_out, not_13_out, not_14_out, not_15_out,
       not_16_out, not_17_out, not_18_out, not_19_out, not_20_out, not_21_out, not_22_out, not_23_out,
       not_24_out, or_1_out, or_2_out, or_3_out, or_4_out;

  not not_1 (not_1_out, f5);
  and and_1 (and_1_out, not_1_out, not_2_out);
  not not_2 (not_2_out, f6);
  and and_2 (and_2_out, f5, f6);
  not not_3 (not_3_out, f2);
  and and_3 (and_3_out, not_3_out, not_4_out, f5);
  not not_4 (not_4_out, f3);
  and and_4 (and_4_out, f2, f3, not_5_out);
  not not_5 (not_5_out, f5);
  not not_6 (not_6_out, f2);
  not not_7 (not_7_out, f4);
  not not_8 (not_8_out, f6);
  not not_9 (not_9_out, f2);
  not not_10 (not_10_out, f3);
  or or_1 (or_1_out, and_1_out, and_2_out);
  not not_11 (not_11_out, f1);
  not not_12 (not_12_out, f4);
  not not_13 (not_13_out, f6);
  or or_2 (or_2_out, and_3_out, and_4_out);
  and and_5 (and_5_out, o4, not_14_out);
  not not_14 (not_14_out, o5);
  not not_15 (not_15_out, o4);
  and and_6 (and_6_out, not_15_out, o5);
  and and_7 (and_7_out, f1, not_6_out, not_7_out, f5, not_8_out);
  and and_8 (and_8_out, f1, not_9_out, not_10_out, f4, or_1_out);
  and and_9 (and_9_out, not_11_out, not_12_out, not_13_out, or_2_out);
  not not_16 (not_16_out, o1);
  not not_17 (not_17_out, o2);
  not not_18 (not_18_out, o6);
  or or_3 (or_3_out, and_5_out, and_6_out);
  not not_19 (not_19_out, o1);
  not not_20 (not_20_out, o2);
  not not_21 (not_21_out, o3);
  not not_22 (not_22_out, o4);
  not not_23 (not_23_out, o5);
  not not_24 (not_24_out, o6);
  or or_4 (or_4_out, and_7_out, and_8_out, and_9_out);
  and and_10 (and_10_out, not_16_out, not_17_out, o3, not_18_out, or_3_out);
  and and_11 (and_11_out, not_19_out, not_20_out, not_21_out, not_22_out, not_23_out, not_24_out, or_4_out);
  or or_5 (ALU_OP3, and_10_out, and_11_out);
endmodule

module ALU_OP4 (
  input  o1,
  input  o2,
  input  o3,
  input  o4,
  input  o5,
  input  o6,
  input  f1,
  input  f2,
  input  f3,
  input  f4,
  input  f5,
  input  f6,
  output ALU_OP4
);

  wire and_1_out, and_2_out, and_3_out, and_4_out, and_5_out, and_6_out, and_7_out, and_8_out, and_9_out,
       and_10_out, and_11_out, and_12_out, and_13_out, not_1_out, not_2_out, not_3_out, not_4_out, not_5_out,
       not_6_out, not_7_out, not_8_out, not_9_out, not_10_out, not_11_out, not_12_out, not_13_out,
       not_14_out, not_15_out, not_16_out, not_17_out, not_18_out, not_19_out, not_20_out, not_21_out,
       not_22_out, not_23_out, not_24_out, not_25_out, not_26_out, not_27_out, not_28_out, not_29_out,
       not_30_out, not_31_out, or_1_out, or_2_out, or_3_out, or_4_out;

  not not_1 (not_1_out, f3);
  and and_1 (and_1_out, not_1_out, f4, not_2_out);
  not not_2 (not_2_out, f5);
  not not_3 (not_3_out, f4);
  and and_2 (and_2_out, f3, not_3_out, f5);
  not not_4 (not_4_out, f2);
  not not_5 (not_5_out, f3);
  not not_6 (not_6_out, f5);
  not not_7 (not_7_out, f6);
  not not_8 (not_8_out, f2);
  not not_9 (not_9_out, f3);
  not not_10 (not_10_out, f4);
  not not_11 (not_11_out, f5);
  not not_12 (not_12_out, f2);
  not not_13 (not_13_out, f6);
  or or_1 (or_1_out, and_1_out, and_2_out);
  not not_14 (not_14_out, f1);
  not not_15 (not_15_out, f4);
  and and_3 (and_3_out, not_4_out, not_5_out, f5, f6);
  or or_2 (or_2_out, and_3_out, and_4_out);
  and and_4 (and_4_out, f2, f3, not_6_out, not_7_out);
  and and_5 (and_5_out, f1, not_8_out, not_9_out, not_10_out, not_11_out);
  and and_6 (and_6_out, f1, not_12_out, not_13_out, or_1_out);
  and and_7 (and_7_out, not_14_out, not_15_out, or_2_out);
  not not_16 (not_16_out, o4);
  and and_8 (and_8_out, not_16_out, not_17_out);
  not not_17 (not_17_out, o5);
  and and_9 (and_9_out, o4, not_18_out, not_19_out);
  not not_18 (not_18_out, o5);
  not not_19 (not_19_out, o6);
  not not_20 (not_20_out, o4);
  and and_10 (and_10_out, not_20_out, o5, not_21_out);
  not not_21 (not_21_out, o6);
  not not_22 (not_22_out, o1);
  not not_23 (not_23_out, o2);
  not not_24 (not_24_out, o3);
  not not_25 (not_25_out, o4);
  not not_26 (not_26_out, o5);
  not not_27 (not_27_out, o6);
  or or_3 (or_3_out, and_5_out, and_6_out, and_7_out);
  not not_28 (not_28_out, o1);
  not not_29 (not_29_out, o2);
  or or_4 (or_4_out, and_8_out, and_9_out, and_10_out);
  not not_30 (not_30_out, o2);
  not not_31 (not_31_out, o4);
  and and_11 (and_11_out, not_22_out, not_23_out, not_24_out, not_25_out, not_26_out, not_27_out, or_3_out);
  and and_12 (and_12_out, not_28_out, not_29_out, o3, or_4_out);
  and and_13 (and_13_out, o1, not_30_out, not_31_out, o5, o6);
  or or_5 (ALU_OP4, and_11_out, and_12_out, and_13_out);
endmodule

module MemWrite (
  input  o1,
  input  o2,
  input  o3,
  input  o4,
  input  o5,
  input  o6,
  input  f1,
  input  f2,
  input  f3,
  input  f4,
  input  f5,
  input  f6,
  output MemWrite
);

  wire not_1_out, not_2_out;

  not not_1 (not_1_out, o2);
  not not_2 (not_2_out, o4);
  and and_1 (MemWrite, o1, not_1_out, o3, not_2_out, o5, o6);
endmodule

module RegWrite (
  input  o1,
  input  o2,
  input  o3,
  input  o4,
  input  o5,
  input  o6,
  input  f1,
  input  f2,
  input  f3,
  input  f4,
  input  f5,
  input  f6,
  output RegWrite
);

  wire and_1_out, and_2_out, and_3_out, and_4_out, and_5_out, and_6_out, and_7_out, and_8_out, and_9_out,
       and_10_out, and_11_out, and_12_out, and_13_out, and_14_out, not_1_out, not_2_out, not_3_out,
       not_4_out, not_5_out, not_6_out, not_7_out, not_8_out, not_9_out, not_10_out, not_11_out, not_12_out,
       not_13_out, not_14_out, not_15_out, not_16_out, not_17_out, not_18_out, not_19_out, not_20_out,
       not_21_out, not_22_out, not_23_out, not_24_out, not_25_out, not_26_out, not_27_out, not_28_out,
       not_29_out, not_30_out, not_31_out, not_32_out, not_33_out, not_34_out, not_35_out, not_36_out,
       not_37_out, or_1_out, or_2_out, or_3_out, or_4_out;

  not not_1 (not_1_out, f5);
  not not_2 (not_2_out, f6);
  not not_3 (not_3_out, f4);
  and and_1 (and_1_out, not_3_out, not_4_out);
  not not_4 (not_4_out, f5);
  not not_5 (not_5_out, f5);
  and and_2 (and_2_out, f4, not_5_out, not_6_out);
  not not_6 (not_6_out, f6);
  not not_7 (not_7_out, f4);
  and and_3 (and_3_out, not_7_out, f5, not_8_out);
  not not_8 (not_8_out, f6);
  and and_4 (and_4_out, f4, f6);
  not not_9 (not_9_out, f1);
  not not_10 (not_10_out, f2);
  not not_11 (not_11_out, f3);
  not not_12 (not_12_out, f4);
  and and_5 (and_5_out, not_1_out, not_2_out);
  or or_1 (or_1_out, and_5_out, f5);
  not not_13 (not_13_out, f2);
  not not_14 (not_14_out, f3);
  or or_2 (or_2_out, and_1_out, and_2_out, and_3_out, and_4_out);
  not not_15 (not_15_out, f1);
  not not_16 (not_16_out, f3);
  not not_17 (not_17_out, f4);
  not not_18 (not_18_out, f6);
  not not_19 (not_19_out, f2);
  not not_20 (not_20_out, f4);
  not not_21 (not_21_out, f6);
  not not_22 (not_22_out, f2);
  not not_23 (not_23_out, f4);
  not not_24 (not_24_out, o4);
  not not_25 (not_25_out, o6);
  and and_6 (and_6_out, not_9_out, not_10_out, not_11_out, not_12_out, or_1_out);
  and and_7 (and_7_out, f1, not_13_out, not_14_out, or_2_out);
  and and_8 (and_8_out, not_15_out, f2, not_16_out, not_17_out, not_18_out);
  and and_9 (and_9_out, f1, not_19_out, f3, not_20_out, f5, not_21_out);
  and and_10 (and_10_out, f1, not_22_out, f3, not_23_out, f5, f6);
  not not_26 (not_26_out, o5);
  and and_11 (and_11_out, not_24_out, o5, not_25_out);
  not not_27 (not_27_out, o1);
  not not_28 (not_28_out, o2);
  not not_29 (not_29_out, o3);
  not not_30 (not_30_out, o4);
  not not_31 (not_31_out, o5);
  not not_32 (not_32_out, o6);
  or or_3 (or_3_out, and_6_out, and_7_out, and_8_out, and_9_out, and_10_out);
  not not_33 (not_33_out, o1);
  not not_34 (not_34_out, o2);
  or or_4 (or_4_out, not_26_out, and_11_out);
  not not_35 (not_35_out, o2);
  not not_36 (not_36_out, o3);
  not not_37 (not_37_out, o4);
  and and_12 (and_12_out, not_33_out, not_34_out, o3, or_4_out);
  and and_13 (and_13_out, not_35_out, not_36_out, not_37_out, o5, o6);
  or or_5 (RegWrite, and_12_out, and_13_out, and_14_out);
  and and_14 (and_14_out, not_27_out, not_28_out, not_29_out, not_30_out, not_31_out, not_32_out, or_3_out);
endmodule

module Branch (
  input  o1,
  input  o2,
  input  o3,
  input  o4,
  input  o5,
  input  o6,
  input  f1,
  input  f2,
  input  f3,
  input  f4,
  input  f5,
  input  f6,
  output Branch
);

  wire not_1_out, not_2_out, not_3_out, not_4_out;

  not not_1 (not_1_out, o1);
  not not_2 (not_2_out, o2);
  not not_3 (not_3_out, o3);
  not not_4 (not_4_out, o5);
  and and_1 (Branch, not_1_out, not_2_out, not_3_out, o4, not_4_out, o6);
endmodule

module Hi_Lo (
  input  o1,
  input  o2,
  input  o3,
  input  o4,
  input  o5,
  input  o6,
  input  f1,
  input  f2,
  input  f3,
  input  f4,
  input  f5,
  input  f6,
  output Hi_Lo
);

  wire and_1_out, and_2_out, not_1_out, not_2_out, not_3_out, not_4_out, not_5_out, not_6_out, not_7_out,
       not_8_out, not_9_out, not_10_out, or_1_out;

  not not_1 (not_1_out, f5);
  and and_1 (and_1_out, not_1_out, not_2_out);
  not not_2 (not_2_out, f6);
  and and_2 (and_2_out, f5, f6);
  not not_3 (not_3_out, o1);
  not not_4 (not_4_out, o2);
  not not_5 (not_5_out, o3);
  not not_6 (not_6_out, o4);
  not not_7 (not_7_out, o5);
  not not_8 (not_8_out, o6);
  not not_9 (not_9_out, f1);
  not not_10 (not_10_out, f4);
  or or_1 (or_1_out, and_1_out, and_2_out);
  and and_3 (Hi_Lo, not_3_out, not_4_out, not_5_out, not_6_out, not_7_out, not_8_out, not_9_out, f2, f3, not_10_out, or_1_out);
endmodule

module syscall (
  input  o1,
  input  o2,
  input  o3,
  input  o4,
  input  o5,
  input  o6,
  input  f1,
  input  f2,
  input  f3,
  input  f4,
  input  f5,
  input  f6,
  output syscall
);

  wire not_1_out, not_2_out, not_3_out, not_4_out, not_5_out, not_6_out, not_7_out, not_8_out, not_9_out,
       not_10_out;

  not not_1 (not_1_out, o1);
  not not_2 (not_2_out, o2);
  not not_3 (not_3_out, o3);
  not not_4 (not_4_out, o4);
  not not_5 (not_5_out, o5);
  not not_6 (not_6_out, o6);
  not not_7 (not_7_out, f1);
  not not_8 (not_8_out, f2);
  not not_9 (not_9_out, f5);
  not not_10 (not_10_out, f6);
  and and_1 (syscall, not_1_out, not_2_out, not_3_out, not_4_out, not_5_out, not_6_out, not_7_out, not_8_out, f3, f4, not_9_out, not_10_out);
endmodule

module MemRead (
  input  o1,
  input  o2,
  input  o3,
  input  o4,
  input  o5,
  input  o6,
  input  f1,
  input  f2,
  input  f3,
  input  f4,
  input  f5,
  input  f6,
  output MemRead
);

  wire not_1_out, not_2_out, not_3_out;

  not not_1 (not_1_out, o2);
  not not_2 (not_2_out, o3);
  not not_3 (not_3_out, o4);
  and and_1 (MemRead, o1, not_1_out, not_2_out, not_3_out, o5, o6);
endmodule
