// Logisim project single_cpu(backup).circ as structural Verilog: 2 circuits, main circuit main
module main (
);

  wire clk;
  wire [4:0] decode_1_rd, decode_1_rs, decode_1_rt, decode_1_shamt, multiplexer_1_out, multiplexer_2_out;
  wire [15:0] decode_1_imm;
  wire [31:0] adder_1_out, alu_1_result, bit_extender_1_out, bit_extender_2_out, bit_extender_3_out, Din,
       main_1_p7, main_1_p8, multiplexer_3_out, ram_1_data, register_1_q, rom_1_data;

  Clock clock_1 (.out(clk));
  Register #(.width(32)) register_1 (.D(adder_1_out), .en(1'b1), .Q(register_1_q), .clk(clk));  // open: clr
  Adder #(.width(32)) adder_1 (.a(register_1_q), .b(32'h4), .out(adder_1_out), .cin(1'b0));  // open: cout
  ROM #(.dataWidth(32)) rom_1 (.addr(register_1_q[9:2]), .data(rom_1_data));  // open: sel
  decode decode_1 (
    .in_1(rom_1_data), .rs(decode_1_rs), .rt(decode_1_rt), .rd(decode_1_rd), .shamt(decode_1_shamt),
    .imm(decode_1_imm));  // open: OP, funct, addr
  Multiplexer #(.width(5)) multiplexer_1 (
    .in0(decode_1_rs), .in1(decode_1_rt), .out(multiplexer_1_out));  // open: sel, en
  Multiplexer #(.width(5)) multiplexer_2 (
    .in0(decode_1_rt), .in1(decode_1_rd), .out(multiplexer_2_out));  // open: sel, en
  assign bit_extender_1_out = {{27{1'b0}}, decode_1_shamt};  // Bit_Extender bit_extender_1
  assign bit_extender_2_out = {{16{1'b0}}, decode_1_imm};  // Bit_Extender bit_extender_2
  assign bit_extender_3_out = {{16{decode_1_imm[15]}}, decode_1_imm};  // Bit_Extender bit_extender_3
  // regfile_main main_1: pin names not known; wires that end beside it: Din, multiplexer_1_out, decode_1_rt, multiplexer_2_out, 1'b1, clk, main_1_p7, main_1_p8
  Multiplexer #(.select(2), .width(32)) multiplexer_3 (
    .in0(main_1_p8), .in1(bit_extender_1_out), .in2(bit_extender_2_out), .in3(bit_extender_3_out),
    .out(multiplexer_3_out));  // open: sel, en
  ALU alu_1 (
    .X(main_1_p7), .Result(alu_1_result), .Y(multiplexer_3_out));  // open: AluOP, Equal, Signed_Overflow, Result_2, UnSigned_Overflow
  RAM #(.dataWidth(32), .bus("separate")) ram_1 (
    .addr(alu_1_result[9:2]), .din(main_1_p8), .data(ram_1_data));  // open: str, sel, clk, ld, clr

  // Notes on the sheet:
  //   contents of rom_1 (hex, n*v repeats v):
  //   18027
endmodule

module decode (
  input  [31:0] in_1,
  output [5:0] OP,
  output [4:0] rs,
  output [4:0] rt,
  output [4:0] rd,
  output [4:0] shamt,
  output [5:0] funct,
  output [15:0] imm,
  output [25:0] addr
);


  assign addr = in_1[25:0];
  assign funct = in_1[5:0];
  assign imm = in_1[15:0];
  assign OP = in_1[31:26];
  assign rd = in_1[15:11];
  assign rs = in_1[25:21];
  assign rt = in_1[20:16];
  assign shamt = in_1[10:6];
endmodule
