// Logisim project _alu_benchmarkV2.0.circ as structural Verilog: 4 circuits, main circuit main
module main (
  output Signed_Overflow,
  output [31:0] Result,
  output Unsigned_overflow,
  output [7:0] Test_num,
  output [31:0] Result_2,
  output Equal
);

  wire ADD, AND, CF_OK, CF_S, CLK, clock_1_out, comparator_1_eq, comparator_2_eq, comparator_3_eq, DIV,
       EQ_OK, EQ_S, grade_1_right, grade_2_right, grade_3_right, grade_4_right, grade_5_right, grade_6_right,
       grade_7_right, grade_8_right, grade_9_right, grade_10_right, grade_11_right, grade_12_right,
       grade_13_right, grade_14_right, grade_15_right, grade_16_right, grade_17_right, grade_18_right, MUL,
       NOR, not_1_out, OF_OK, OR, ROK, SAR, SCMP, SLL, SLR, SUB, tunnel, UCMP, XOR;
  wire [2:2] FLAG_Standard;
  wire [3:0] ALUOP, High, Low, Mid;
  wire [7:0] add_1_result, adder_1_out, grade_1_total, \grade_1_得分 , \grade_1_正确条数 , grade_2_total,
       \grade_2_得分 , \grade_2_正确条数 , grade_3_total, \grade_3_得分 , \grade_3_正确条数 , grade_4_total,
       \grade_4_得分 , \grade_4_正确条数 , grade_5_total, \grade_5_得分 , \grade_5_正确条数 , grade_6_total,
       \grade_6_得分 , \grade_6_正确条数 , grade_7_total, \grade_7_得分 , \grade_7_正确条数 , grade_8_total,
       \grade_8_得分 , \grade_8_正确条数 , grade_9_total, \grade_9_得分 , \grade_9_正确条数 , grade_10_total,
       \grade_10_得分 , \grade_10_正确条数 , grade_11_total, \grade_11_得分 , \grade_11_正确条数 , grade_12_total,
       \grade_12_得分 , \grade_12_正确条数 , grade_13_total, \grade_13_得分 , \grade_13_正确条数 , grade_14_total,
       \grade_14_得分 , \grade_14_正确条数 , grade_15_total, \grade_15_得分 , \grade_15_正确条数 , grade_16_total,
       \grade_16_得分 , \grade_16_正确条数 , grade_17_total, \grade_17_得分 , \grade_17_正确条数 , grade_18_total,
       \grade_18_得分 , \grade_18_正确条数 ;
  wire [31:0] R2_Standard, R_Standard, X, Y;

  Clock clock_1 (.out(clock_1_out));
  LED #(.active("false")) led_1 (.in(grade_1_right));
  // Probe on grade_1_total
  // Probe on \grade_1_正确条数 
  Adder adder_1 (.a(8'h1), .b(Test_num), .out(adder_1_out));  // open: cin, cout
  Register register_1 (.D(adder_1_out), .Q(Test_num), .clk(CLK));  // open: en, clr
  Comparator #(.width(4)) comparator_1 (.a(ALUOP), .b(4'b1111), .eq(comparator_1_eq));  // open: gt, lt
  Hex_Digit_Display hex_digit_display_1 (.value(Mid));  // open: dp
  Hex_Digit_Display hex_digit_display_2 (.value(High));  // open: dp
  LED #(.active("false")) led_2 (.in(grade_2_right));
  grade grade_1 (
    .EQ(ROK), .CLK(CLK), .\分值 (5'b00110), .\正确条数 (\grade_1_正确条数 ), .\得分 (\grade_1_得分 ), .ALU_SWITCH(SLL),
    .Total(grade_1_total), .Right(grade_1_right));
  // Probe on grade_2_total
  // Probe on \grade_2_正确条数 
  // Probe on \grade_2_得分 
  // Probe on \grade_1_得分 
  not not_1 (not_1_out, comparator_1_eq);
  Hex_Digit_Display hex_digit_display_3 (.value(Low));  // open: dp
  LED #(.active("false")) led_3 (.in(grade_3_right));
  grade grade_2 (
    .EQ(ROK), .CLK(CLK), .\分值 (5'b00110), .\正确条数 (\grade_2_正确条数 ), .\得分 (\grade_2_得分 ), .ALU_SWITCH(SAR),
    .Total(grade_2_total), .Right(grade_2_right));
  // Probe on grade_3_total
  // Probe on \grade_3_正确条数 
  // Probe on \grade_3_得分 
  trace trace_1 (
    .in_1(Test_num), .X(X), .Y(Y), .AluOP(ALUOP), .R(R_Standard), .R2(R2_Standard),
    .FLAGS({FLAG_Standard[2], CF_S, EQ_S}));
  and and_1 (CLK, not_1_out, clock_1_out);
  LED #(.active("false")) led_4 (.in(grade_4_right));
  grade grade_3 (
    .EQ(ROK), .CLK(CLK), .\分值 (5'b00110), .\正确条数 (\grade_3_正确条数 ), .\得分 (\grade_3_得分 ), .ALU_SWITCH(SLR),
    .Total(grade_3_total), .Right(grade_3_right));
  grade grade_4 (
    .EQ(ROK), .CLK(CLK), .\分值 (5'b01000), .\正确条数 (\grade_4_正确条数 ), .\得分 (\grade_4_得分 ), .ALU_SWITCH(MUL),
    .Total(grade_4_total), .Right(grade_4_right));
  // Probe on \grade_4_正确条数 
  // Probe on \grade_4_正确条数 
  // Probe on \grade_4_得分 
  LED #(.active("false")) led_5 (.in(grade_5_right));
  grade grade_5 (
    .EQ(ROK), .CLK(CLK), .\分值 (5'b01000), .\正确条数 (\grade_5_正确条数 ), .\得分 (\grade_5_得分 ), .ALU_SWITCH(DIV),
    .Total(grade_5_total), .Right(grade_5_right));
  // Probe on grade_5_total
  // Probe on \grade_5_正确条数 
  // Probe on \grade_5_得分 
  LED #(.active("false")) led_6 (.in(grade_6_right));
  grade grade_6 (
    .EQ(ROK), .CLK(CLK), .\分值 (5'b00110), .\正确条数 (\grade_6_正确条数 ), .\得分 (\grade_6_得分 ), .ALU_SWITCH(ADD),
    .Total(grade_6_total), .Right(grade_6_right));
  // Probe on grade_6_total
  // Probe on \grade_6_正确条数 
  // Probe on \grade_6_得分 
  ALU alu_1 (
    .AluOP(ALUOP), .X(X), .Equal(Equal), .Result(Result), .Signed_Overflow(Signed_Overflow), .Y(Y),
    .Result_2(Result_2), .UnSigned_Overflow(Unsigned_overflow));
  // Probe on ALUOP
  LED #(.active("false")) led_7 (.in(grade_7_right));
  grade grade_7 (
    .EQ(ROK), .CLK(CLK), .\分值 (5'b00110), .\正确条数 (\grade_7_正确条数 ), .\得分 (\grade_7_得分 ), .ALU_SWITCH(SUB),
    .Total(grade_7_total), .Right(grade_7_right));
  // Probe on grade_7_total
  // Probe on grade_8_total
  // Probe on \grade_7_正确条数 
  // Probe on \grade_7_得分 
  ADD add_1 (
    .in_1(\grade_1_得分 ), .in_2(\grade_16_得分 ), .in_3(\grade_2_得分 ), .in_4(\grade_3_得分 ), .in_5(\grade_6_得分 ),
    .in_6(\grade_7_得分 ), .in_7(\grade_8_得分 ), .in_8(\grade_9_得分 ), .in_9(\grade_11_得分 ),
    .in_10(\grade_10_得分 ), .in_11(\grade_12_得分 ), .in_12(\grade_13_得分 ), .in_13(\grade_15_得分 ),
    .in_14(\grade_5_得分 ), .in_15(\grade_4_得分 ), .in_16(\grade_14_得分 ), .Result(add_1_result),
    .in_17(\grade_17_得分 ), .in_18(\grade_18_得分 ), .High(High), .Low(Low), .Mid(Mid));
  // Probe on add_1_result
  LED #(.active("false")) led_8 (.in(grade_9_right));
  LED #(.active("false")) led_9 (.in(grade_8_right));
  grade grade_8 (
    .EQ(ROK), .CLK(CLK), .\分值 (5'b00101), .\正确条数 (\grade_8_正确条数 ), .\得分 (\grade_8_得分 ), .ALU_SWITCH(AND),
    .Total(grade_8_total), .Right(grade_8_right));
  // Probe on grade_9_total
  // Probe on \grade_8_正确条数 
  // Probe on \grade_9_正确条数 
  // Probe on \grade_8_得分 
  // Probe on \grade_9_得分 
  Decoder #(.select(4), .enable("false")) decoder_1 (
    .out0(SLL), .out1(SAR), .out2(SLR), .out3(MUL), .out4(DIV), .out5(ADD), .out6(SUB), .out7(AND),
    .out8(OR), .out9(XOR), .out10(NOR), .out11(SCMP), .out12(UCMP), .sel(ALUOP));  // open: out13, out14, out15
  LED #(.active("false")) led_10 (.in(grade_11_right));
  grade grade_9 (
    .EQ(ROK), .CLK(CLK), .\分值 (5'b00101), .\正确条数 (\grade_9_正确条数 ), .\得分 (\grade_9_得分 ), .ALU_SWITCH(OR),
    .Total(grade_9_total), .Right(grade_9_right));
  // Probe on grade_11_total
  // Probe on \grade_11_正确条数 
  // Probe on \grade_11_得分 
  LED #(.active("false")) led_11 (.in(grade_10_right));
  grade grade_10 (
    .EQ(ROK), .CLK(CLK), .\分值 (5'b00101), .\正确条数 (\grade_10_正确条数 ), .\得分 (\grade_10_得分 ), .ALU_SWITCH(NOR),
    .Total(grade_10_total), .Right(grade_10_right));
  grade grade_11 (
    .EQ(ROK), .CLK(CLK), .\分值 (5'b00101), .\正确条数 (\grade_11_正确条数 ), .\得分 (\grade_11_得分 ), .ALU_SWITCH(XOR),
    .Total(grade_11_total), .Right(grade_11_right));
  // Probe on grade_10_total
  // Probe on \grade_10_正确条数 
  // Probe on \grade_10_得分 
  LED #(.active("false")) led_12 (.in(grade_12_right));
  grade grade_12 (
    .EQ(ROK), .CLK(CLK), .\分值 (5'b00110), .\正确条数 (\grade_12_正确条数 ), .\得分 (\grade_12_得分 ), .ALU_SWITCH(SCMP),
    .Total(grade_12_total), .Right(grade_12_right));
  // Probe on grade_12_total
  // Probe on \grade_12_正确条数 
  // Probe on \grade_12_得分 
  xnor xnor_1 (EQ_OK, EQ_S, Equal);
  LED #(.active("false")) led_13 (.in(grade_13_right));
  grade grade_13 (
    .EQ(ROK), .CLK(CLK), .\分值 (5'b00110), .\正确条数 (\grade_13_正确条数 ), .\得分 (\grade_13_得分 ), .ALU_SWITCH(UCMP),
    .Total(grade_13_total), .Right(grade_13_right));
  // Probe on grade_14_total
  // Probe on grade_13_total
  // Probe on \grade_13_正确条数 
  // Probe on \grade_13_得分 
  xnor xnor_2 (OF_OK, FLAG_Standard[2], Signed_Overflow);
  xnor xnor_3 (CF_OK, CF_S, Unsigned_overflow);
  Comparator #(.width(32)) comparator_2 (.a(R_Standard), .b(Result), .eq(comparator_2_eq));  // open: gt, lt
  Comparator #(.width(32)) comparator_3 (.a(R2_Standard), .b(Result_2), .eq(comparator_3_eq));  // open: gt, lt
  LED #(.active("false")) led_14 (.in(grade_14_right));
  grade grade_14 (
    .EQ(EQ_OK), .CLK(CLK), .\分值 (5'b00010), .\正确条数 (\grade_14_正确条数 ), .\得分 (\grade_14_得分 ),
    .ALU_SWITCH(EQ_OK), .Total(grade_14_total), .Right(grade_14_right));
  // Probe on grade_15_total
  // Probe on \grade_14_正确条数 
  // Probe on \grade_15_正确条数 
  // Probe on \grade_14_得分 
  // Probe on \grade_15_得分 
  and and_2 (ROK, comparator_2_eq, comparator_3_eq);
  or or_1 (tunnel, ADD, SUB);
  LED #(.active("false")) led_15 (.in(grade_16_right));
  LED #(.active("false")) led_16 (.in(grade_15_right));
  grade grade_15 (
    .EQ(OF_OK), .CLK(CLK), .\分值 (5'b00010), .\正确条数 (\grade_15_正确条数 ), .\得分 (\grade_15_得分 ),
    .ALU_SWITCH(1'b1), .Total(grade_15_total), .Right(grade_15_right));
  grade grade_16 (
    .EQ(CF_OK), .CLK(CLK), .\分值 (5'b00010), .\正确条数 (\grade_16_正确条数 ), .\得分 (\grade_16_得分 ),
    .ALU_SWITCH(1'b1), .Total(grade_16_total), .Right(grade_16_right));
  // Probe on grade_16_total
  // Probe on \grade_16_正确条数 
  // Probe on \grade_16_得分 
  LED #(.active("false")) led_17 (.in(grade_17_right));
  grade grade_17 (
    .EQ(OF_OK), .CLK(CLK), .\分值 (5'b01000), .\正确条数 (\grade_17_正确条数 ), .\得分 (\grade_17_得分 ),
    .ALU_SWITCH(tunnel), .Total(grade_17_total), .Right(grade_17_right));
  // Probe on grade_18_total
  // Probe on grade_17_total
  // Probe on \grade_17_正确条数 
  // Probe on \grade_17_得分 
  LED #(.active("false")) led_18 (.in(grade_18_right));
  grade grade_18 (
    .EQ(CF_OK), .CLK(CLK), .\分值 (5'b01000), .\正确条数 (\grade_18_正确条数 ), .\得分 (\grade_18_得分 ),
    .ALU_SWITCH(tunnel), .Total(grade_18_total), .Right(grade_18_right));
  // Probe on \grade_18_正确条数 
  // Probe on \grade_18_得分 

  // Other names for the same wires on the sheet: CF = Unsigned_overflow; EQ = Equal;
  //   FLAG_Standard[1:0] = {CF_S, EQ_S}; OF_S = FLAG_Standard[2]; OF = Signed_Overflow; R[31:0] = Result;
  //   R2[31:0] = Result_2

  // Notes on the sheet:
  //   操作码为F停止
  //   最终分数
  //   各部分分值
  //   各部分得分
endmodule

// Trace
module trace (
  input  [7:0] in_1,
  output [31:0] X,
  output [31:0] Y,
  output [3:0] AluOP,
  output [31:0] R,
  output [31:0] R2,
  output [2:0] FLAGS
);

  ROM #(.dataWidth(32)) rom_1 (.addr(in_1), .data(X));  // open: sel
  ROM #(.dataWidth(32)) rom_2 (.addr(in_1), .data(Y));  // open: sel
  ROM #(.dataWidth(4)) rom_3 (.addr(in_1), .data(AluOP));  // open: sel
  ROM #(.dataWidth(32)) rom_4 (.addr(in_1), .data(R));  // open: sel
  ROM #(.dataWidth(32)) rom_5 (.addr(in_1), .data(R2));  // open: sel
  ROM #(.dataWidth(3)) rom_6 (.addr(in_1), .data(FLAGS));  // open: sel

  // Notes on the sheet:
  //   X trace
  //   Y trace
  //   ALU OP Trace
  //   Result Benchmark
  //   Result2 Benchmark
  //   FLAGS Benchmark
  //   contents of rom_1 (hex, n*v repeats v):
  //   ff00ffff ff00ffff ff000000 ff00ffff 7fffffff fffffffe ffff ffffffff 7fffffff 80000000 7ff00000 7c
  //   80000000 7fffffff ff00ffff 7fffffff 18*fffffffe
  //   contents of rom_2 (hex, n*v repeats v):
  //   7 ff00ffff 18 18 10 10 80 ffffffff c 80000000 7c 7ff00000 1 fffffffe 18 74 fffffffe 88 10 ffffffff
  //   10 ffffffff 12*10
  //   contents of rom_3 (hex, n*v repeats v):
  //   0 0 1 2 3 4 4*5 4*6 7 8 9 a b b c c f 11*9 f
  //   contents of rom_4 (hex, n*v repeats v):
  //   807fff80 80000000 ffffffff ff fffffff0 fffffff 1007f fffffffe 8000000b 0 7fefff84 8010007c 7fffffff
  //   80000001 18 7fffffff 0 1 1 1 0 1 300000 11*ffffffee 1
  //   contents of rom_5 (hex, n*v repeats v):
  //   4*0 7 e
  //   contents of rom_6 (hex, n*v repeats v):
  //   0 1 5*0 3 4 7 0 2 4 6 0 0 1 17*0 66*1
endmodule

// 统计评分
module grade (
  input  ALU_SWITCH,
  input  EQ,
  input  CLK,
  input  [4:0] \分值 ,
  output [7:0] \正确条数 ,
  output [7:0] \得分 ,
  output [7:0] Total,
  output Right
);

  wire and_1_out, priority_encoder_1_gs, priority_encoder_1_out;
  wire [7:0] bit_extender_1_out, multiplier_1_out;

  Priority_Encoder #(.select(1)) priority_encoder_1 (
    .in0(EQ), .in1(EQ), .out(priority_encoder_1_out), .gs(priority_encoder_1_gs));  // open: en_out, en_in
  Counter counter_1 (.count(ALU_SWITCH), .Q(Total), .clk(CLK));  // open: load, D, carry, clr
  and and_1 (and_1_out, ALU_SWITCH, priority_encoder_1_out, priority_encoder_1_gs);
  Counter counter_2 (.count(and_1_out), .Q(\正确条数 ), .clk(CLK));  // open: load, D, carry, clr
  assign bit_extender_1_out = {{3{1'b0}}, \分值 };  // Bit_Extender bit_extender_1
  Multiplier multiplier_1 (.a(\正确条数 ), .b(bit_extender_1_out), .out(multiplier_1_out));  // open: cin, cout
  Divider divider_1 (.a(multiplier_1_out), .b(Total), .out(\得分 ));  // open: upper, rem
  Comparator comparator_1 (.a(\得分 ), .b(bit_extender_1_out), .eq(Right));  // open: gt, lt

  // Notes on the sheet:
  //   只有使用优先编码器才能屏蔽掉位置状态
endmodule

// 16路加法器
module ADD (
  input  [7:0] in_1,
  input  [7:0] in_2,
  input  [7:0] in_3,
  input  [7:0] in_4,
  input  [7:0] in_5,
  input  [7:0] in_6,
  input  [7:0] in_7,
  input  [7:0] in_8,
  input  [7:0] in_9,
  input  [7:0] in_10,
  input  [7:0] in_11,
  input  [7:0] in_12,
  input  [7:0] in_13,
  input  [7:0] in_14,
  input  [7:0] in_15,
  input  [7:0] in_16,
  input  [7:0] in_17,
  input  [7:0] in_18,
  output [7:0] Result,
  output [3:0] High,
  output [3:0] Low,
  output [3:0] Mid
);

  wire [7:0] adder_1_out, adder_2_out, adder_3_out, adder_4_out, adder_5_out, adder_6_out, adder_7_out,
       adder_8_out, adder_9_out, adder_10_out, adder_11_out, adder_12_out, adder_13_out, adder_14_out,
       adder_15_out, adder_16_out, divider_1_out;
  wire [7:4] divider_1_rem, divider_2_out, divider_2_rem;

  Adder adder_1 (.a(in_1), .b(in_2), .out(adder_1_out));  // open: cin, cout
  Adder adder_2 (.a(in_3), .b(in_4), .out(adder_2_out));  // open: cin, cout
  Adder adder_3 (.a(in_5), .b(in_6), .out(adder_3_out));  // open: cin, cout
  Adder adder_4 (.a(in_7), .b(in_8), .out(adder_4_out));  // open: cin, cout
  Adder adder_5 (.a(in_9), .b(in_10), .out(adder_5_out));  // open: cin, cout
  Adder adder_6 (.a(in_11), .b(in_12), .out(adder_6_out));  // open: cin, cout
  Adder adder_7 (.a(in_13), .b(in_14), .out(adder_7_out));  // open: cin, cout
  Adder adder_8 (.a(in_15), .b(in_16), .out(adder_8_out));  // open: cin, cout
  Adder adder_9 (.a(in_17), .b(in_18), .out(adder_9_out));  // open: cin, cout
  Adder adder_10 (.a(adder_1_out), .b(adder_2_out), .out(adder_10_out));  // open: cin, cout
  Adder adder_11 (.a(adder_3_out), .b(adder_4_out), .out(adder_11_out));  // open: cin, cout
  Adder adder_12 (.a(adder_5_out), .b(adder_6_out), .out(adder_12_out));  // open: cin, cout
  Adder adder_13 (.a(adder_7_out), .b(adder_8_out), .out(adder_13_out));  // open: cin, cout
  Adder adder_14 (.a(adder_10_out), .b(adder_11_out), .out(adder_14_out));  // open: cin, cout
  Adder adder_15 (.a(adder_12_out), .b(adder_13_out), .out(adder_15_out));  // open: cin, cout
  Adder adder_16 (.a(adder_14_out), .b(adder_15_out), .out(adder_16_out));  // open: cin, cout
  Adder adder_17 (.a(adder_16_out), .b(adder_9_out), .out(Result));  // open: cin, cout
  Divider divider_1 (.a(Result), .b(8'ha), .out(divider_1_out), .rem({divider_1_rem, Low}));  // open: upper
  Divider divider_2 (
    .a(divider_1_out), .b(8'ha), .out({divider_2_out, High}), .rem({divider_2_rem, Mid}));  // open: upper
endmodule
