// Logisim project _regfile_benchmarkV2.0.circ as structural Verilog: 2 circuits, main circuit main
module main (
  output [9:0] test_num,
  output [31:0] Reg_0_Value,
  output [31:0] Reg_1_Value,
  output [31:0] Reg_2_Value,
  output [31:0] Reg_3_Value,
  output [31:0] Reg1,
  output [31:0] Reg2
);

  wire CLK, clock_1_out, comparator_1_eq, comparator_2_eq, comparator_3_eq, comparator_4_eq, Equal, Halt,
       NEQ, R1_NEQ, R2_NEQ;
  wire [3:0] grade_1_high, grade_1_low, grade_1_mid;
  wire [4:0] multiplexer_1_out, multiplexer_2_out;
  wire [9:0] adder_1_out, counter_1_q;
  wire [15:0] otherinput;
  wire [31:0] grade_1_total, \grade_1_正确条数 , R1_Ref, R2_Ref, WriteData;

  Register #(.width(10)) register_1 (.D(adder_1_out), .en(1'b1), .Q(test_num), .clk(CLK));  // open: clr
  Adder #(.width(10)) adder_1 (.a(10'h1), .b(test_num), .out(adder_1_out));  // open: cin, cout
  // Probe on grade_1_total
  grade grade_1 (
    .EQ(Equal), .CLK(CLK), .\正确条数 (\grade_1_正确条数 ), .High(grade_1_high), .Low(grade_1_low),
    .Mid(grade_1_mid), .Total(grade_1_total));  // open: Right
  // Probe on \grade_1_正确条数 
  ROM #(.addrWidth(10), .dataWidth(32)) rom_1 (.addr(test_num), .data(WriteData));  // open: sel
  ROM #(.addrWidth(10), .dataWidth(16)) rom_2 (.addr(test_num), .data(otherinput), .sel(1'b1));
  ROM #(.addrWidth(10), .dataWidth(32)) rom_3 (.addr(test_num), .data(R1_Ref));  // open: sel
  Hex_Digit_Display hex_digit_display_1 (.value(grade_1_high));  // open: dp
  Hex_Digit_Display hex_digit_display_2 (.value(grade_1_mid));  // open: dp
  Hex_Digit_Display hex_digit_display_3 (.value(grade_1_low));  // open: dp
  regfile_main main_1 (
    .Reg1_num(otherinput[4:0]), .Reg2(otherinput[9:5]), .Write_Reg_num(otherinput[14:10]), .Din(WriteData),
    .Write_Enable(otherinput[15]), .Clock(CLK), .Reg1(Reg1), .Reg2_2(Reg2), .v0_Value(Reg_0_Value),
    .a0_Value(Reg_1_Value), .s2_Value(Reg_2_Value), .ra_Value(Reg_3_Value));
  ROM #(.addrWidth(10), .dataWidth(32)) rom_4 (.addr(test_num), .data(R2_Ref));  // open: sel
  Counter #(.width(10), .max('h3ff)) counter_1 (.count(NEQ), .Q(counter_1_q), .clk(CLK));  // open: load, D, carry, clr
  // Probe on counter_1_q
  RAM #(.addrWidth(10), .dataWidth(10), .bus("separate")) ram_1 (
    .addr(counter_1_q), .din(test_num), .str(NEQ), .clk(CLK));  // open: data, sel, ld, clr
  Multiplexer #(.width(5), .enable("false")) multiplexer_1 (
    .in0({5{1'b0}}), .in1(otherinput[4:0]), .out(multiplexer_1_out), .sel(R1_NEQ));
  Multiplexer #(.width(5), .enable("false")) multiplexer_2 (
    .in0({5{1'b0}}), .in1(otherinput[9:5]), .out(multiplexer_2_out), .sel(R2_NEQ));
  Comparator #(.width(32)) comparator_1 (.a(R1_Ref), .b(Reg1), .eq(comparator_1_eq));  // open: gt, lt
  Comparator #(.width(32)) comparator_2 (.a(R2_Ref), .b(Reg2), .eq(comparator_2_eq));  // open: gt, lt
  Comparator #(.width(32)) comparator_3 (.a(WriteData), .b({32{1'b0}}), .eq(comparator_3_eq));  // open: gt, lt
  Comparator #(.width(16)) comparator_4 (.a(otherinput), .b({16{1'b0}}), .eq(comparator_4_eq));  // open: gt, lt
  RAM #(.addrWidth(10), .dataWidth(5), .bus("separate")) ram_2 (
    .addr(counter_1_q), .din(multiplexer_1_out), .str(NEQ), .clk(CLK));  // open: data, sel, ld, clr
  not not_1 (R1_NEQ, comparator_1_eq);
  and and_1 (Equal, comparator_1_eq, comparator_2_eq);
  not not_2 (R2_NEQ, comparator_2_eq);
  and and_2 (Halt, comparator_3_eq, comparator_4_eq);
  Clock clock_1 (.out(clock_1_out));
  not not_3 (NEQ, Equal);
  and and_3 (CLK, ~Halt, clock_1_out);  // AND_Gate
  RAM #(.addrWidth(10), .dataWidth(5), .bus("separate")) ram_3 (
    .addr(counter_1_q), .din(multiplexer_2_out), .str(NEQ), .clk(CLK));  // open: data, sel, ld, clr

  // Other names for the same wires on the sheet: r1_num[4:0] = otherinput[4:0]; r2_num[4:0] = otherinput[9:5];
  //   trace_num[9:0] = test_num

  // Notes on the sheet:
  //   contents of rom_1 (hex, n*v repeats v):
  //   1dff 251a 66ee 5cc2 a60 739c 4b6b 107b 2b9f 691 5db 66e2 4b65 45f8 173a 9d9 ba3 5c0c 7105 1bba 101c
  //   622 1e29 933 1c35 6ee0 697a 2c9 3622 3b17 1352 68a7 4467 326c 3dca 5d07 5fee 124d 1682 7a82 7a3d 228
  //   5ae6 6f69 690b 7966 27f6 69cd 3bdd 7ca9 6859 5c2c 6e5f 714a 7622 7b6 1653 3bc0 6046 50e5 1819 35de
  //   78dc 9dd 3f5 713 5fc3 7675 604e 269a 3df7 710d 54bb 6162 13a7 382a 6200 49f4 4d8 3178 2e0 7215 7a7d
  //   1e7e 1e1e f00 30a1 2879 2053 447b 1a19 1916 2e3f 2f90 5bcb 7c3 6f03 ac0 292f 10b8 15a0 7e1d 6e41
  //   1ad4 196 795f 7e96 7649 3f11 2606 4848 6ded 1159 1e46 dfe 72a4 5177 6c75 5dc5 5f73 39a6 6dfe 7c4f
  //   2cb5 3f04 7e73 2413 590 3b44 7fab 5bb9 ea6 551a 12f1 3bef 7b0c 21d2 478e 1b80 168f 5696 538b 2b10
  //   1d66 6f19 3cdb 7b68 6b70 49cf 6a8 6211 37a 8f5 4002 2181 1976 7614 7f27 22fb b8f 6627 38c6 3c11 25a6
  //   6dfb 362e 5578 1324 792e 4cfe 1fae 5fc9 6683 6789 2d7b 3e36 654 6daa 4d8 3c1c 560f 1cf2 57b3 23d6
  //   43e4 2e0c 451d 6ee 7f3e 5f83 55e1 8e5 361e 1e21 7202 554d 60ff 3711 7392 6f67 2a23 1b9e 732d 39a5
  //   1098 18d8 1cdd 5a9 3eab 3cf0 5c9c 2f3a 69b9 5704 1c92 4872 1c8f 6944 1981 6505 17c 347a 5425 2201
  //   7516 7c6d 1d29 32a4 4818 60d7 4b30 1b63 1757 60f5 5c4d 77f2 7132 3b16 161a 23aa 72f9 48d 356a 5a6
  //   28ad 5469 2eed 765f 1d2b 24c1 1378 645 2567 3b38 66c2 4131 4727 59ce 615c 70cc 534 8cb 7efe 2a45
  //   419d 3acf 17e9 599b 552 6542 19c7 ec0 4d31 4bdd 6dfa 33ef 6c99 2293 40be 1012 103 4fe 20c4 66b1 4031
  //   67f6 42a1 7205 1f2a 6368 596d 4ae8 6477 7334 64a8 2764 7969 5ac3 4e02 1d76 535c 445e 470b 483f 2b8b
  //   2021 2009 4664 ea6 40eb 3139 1788 6cd9 1e3a 2ca2 4914 3666 4694 379e 1431 1ea7 4133 142b 5a74 5646
  //   16c1 648b 7c5d 46c1 6a5 7dc1 3cd8 4760 2d1b 1197 18c0 28e1 35c7 25e5 29a5 7c26 2fe1 118e 3e49 be5
  //   6e7d 722 d52 10e5 4088 10a 43fd 407e 721 7251 3eaa 330d b51 67ea 2222 7bc6 6073 2df5 110e 2130 7b1e
  //   599d 6495 7252 13cb 4c15 1467 1965 4383 2c8c 3707 637f 6b9a 67fa 76d4 c02 5ef6 4cf8 7a8f 150f 5d96
  //   3104 1cb6 4e09 5ae9 1402 65a4 3fcc 72f3 4fa7 438a 2715 2264 297c 53a9 2ee8 7775 1cf5 9db 6f0 242a
  //   1939 636e 27bc 19f da1 594c 6734 3cd7 ca7 4536 56d4 4b29 668d 929 762d 199b 6973 254a f91 716b 746a
  //   77bb 6754 dd6 220e 17c 807 363e 22e6 599b 17ce 226a 1e0 1f78 5602 5971 27a7 1304 56da 5405 5ed5 5f4d
  //   185c 75d2 7f29 3d54 142a 5435 2fe9 578a 594c f72 747e 5cad 67e3 65c0 55c8 1a0a 5e82 54c6 2dc7 4aec
  //   28de 59b0 514b 1e4b 3aae 3aff 17e9 6d55 6de9 692c 3841 63da 6fc5 7f4a 799d 16ec 42cd 6711 a4e 479f
  //   1163 7f09 262a 417e 3c71 360b 9be 5402 4fbb 35b1 1c2 12d5 31c 43a6 1d56 ab7 3944 361d 2944 5bd3 68c7
  //   355d 38e5 39a7 18cb 3448 7523 227a 2200 391c 3c4f 4692 20c4 160 4f14 24f7 d65 50ce 6002 406 639a
  //   4092 690 5666 10c8 3f62 17ca 6eed 68e0 503d 1978 79d3 76cb 3a44 18bc 623f
  //   contents of rom_2 (hex, n*v repeats v):
  //   825a 2c20 1462 28a4 e6 1128 616a 3dac 5ee 2230 5a72 2b4 6ef6 6338 37a 23bc 27fe 86c6 2420 1462 28a4
  //   48e6 3528 456a 49ac 59ee 3630 2672 52b4 52f6 5f38 7f7a 43bc 7ffe 881b 3820 7062 5ca4 14e6 4128 356a
  //   1dac 5dee 5230 6a72 72b4 6f6 5b38 5f7a 33bc 7fe 8fe4 6420 5862 60a4 58e6 3128 556a 5ac 35ee 1630
  //   4a72 16b4 af6 6338 7b7a 6bbc 67fe 905c 20 3c62 68a4 30e6 6d28 156a 35ac 51ee 4230 a72 6b4 42f6 6f38
  //   577a 7bbc 23fe 960f 3020 1c62 ca4 44e6 128 d6a 6dac 2dee 5e30 1672 62b4 4af6 5338 1b7a 37bc 7fe 9a3e
  //   1020 3462 38a4 44e6 1d28 516a 39ac 11ee 5a30 4a72 36b4 46f6 6f38 6b7a 37bc 53fe 9ef3 6420 3462 30a4
  //   48e6 4128 396a 1dac 1dee 4e30 6a72 36b4 2af6 6738 637a 6bbc 4ffe a1a3 1c20 5462 34a4 64e6 128 16a
  //   19ac 31ee 1630 6a72 2eb4 2af6 4738 37a 3bc 2bfe a455 6020 5c62 1ca4 74e6 3528 6d6a 29ac 41ee 1630
  //   a72 12b4 5ef6 6738 1f7a 7bbc 47fe ab64 c20 5862 38a4 60e6 4d28 696a 11ac 1ee 5a30 5e72 2b4 6ef6 1338
  //   737a 47bc bfe ac68 1c20 2862 30a4 10e6 3d28 7d6a 69ac 9ee 6230 1672 12b4 16f6 b38 637a 33bc 7bfe
  //   b3cf 1820 462 44a4 68e6 6d28 456a 19ac 4dee e30 5a72 56b4 72f6 6338 677a bbc 63fe b4a9 2420 2862
  //   5ca4 ce6 4928 756a 5dac 65ee 1a30 7a72 66b4 2ef6 5338 437a 7bbc 77fe b92f 6c20 6c62 70a4 7ce6 6928
  //   616a 7dac 7dee 630 e72 26b4 3ef6 5738 2f7a 6fbc 17fe bdaf 7020 5462 1ca4 3ce6 1d28 96a 1dac 25ee
  //   2a30 3a72 12b4 6af6 2f38 2f7a 23bc 1ffe c2d2 20 5062 6ca4 7ce6 6d28 96a 11ac 65ee 5630 5a72 2eb4 ef6
  //   1f38 277a 47bc 43fe c6bd 3820 3462 5ca4 6ce6 1d28 256a 25ac 35ee 3230 272 46b4 4af6 f38 737a 1fbc
  //   57fe c954 5820 1c62 78a4 68e6 2128 516a 69ac 21ee 4a30 2a72 36b4 5af6 2738 537a 1fbc 6ffe ccf3 7420
  //   4c62 24a4 1ce6 2928 556a 79ac 9ee 6230 7672 56b4 3ef6 4738 537a 6fbc 27fe d2a6 1420 5862 34a4 4e6
  //   928 256a 39ac 79ee 630 4672 56b4 66f6 5f38 577a fbc 4ffe d52f 1c20 7062 4ca4 14e6 7528 6d6a 55ac
  //   7dee 2a30 4a72 6ab4 16f6 2338 477a 43bc 27fe dbf8 2c20 6862 18a4 50e6 6528 416a 21ac 7dee 7a30 272
  //   3ab4 ef6 6f38 4b7a 57bc 47fe dd06 4c20 862 64a4 2ce6 6528 596a 5dac 19ee 2230 a72 26b4 22f6 4738 f7a
  //   13bc 7ffe e16a 6820 7c62 14a4 38e6 4d28 596a 59ac 7dee 5230 7a72 2ab4 6af6 4738 377a 3bc 37fe e692
  //   7c20 1062 54a4 e6 6528 d6a 59ac 35ee 3a30 6672 42b4 42f6 3738 777a 23bc 3fe ebed 1020 3c62 8a4 64e6
  //   1d28 596a 75ac 5dee 7630 2a72 5eb4 62f6 5338 4f7a 6bbc 3bfe ecf0 3420 4862 58a4 10e6 7528 96a 9ac
  //   1ee 4230 4a72 62b4 7ef6 7b38 5f7a 47bc 1bfe f021 2820 1c62 24a4 5ce6 6928 16a 71ac 15ee 3a30 e72
  //   56b4 56f6 6738 577a 43bc 13fe f43f 3020 6862 10a4 2ce6 4928 156a 35ac 6dee 230 5e72 7eb4 32f6 6f38
  //   377a 4fbc 73fe f9ce 3020 4862 8a4 1ce6 5928 56a 69ac 61ee 6e30 2272 26b4 72f6 5f38 2f7a 17bc ffe
  //   febd 5020 1c62 38a4 78e6 1d28 2d6a 35ac 15ee 6230 a72 72b4 12f6 1338 5b7a 6fbc 5ffe
  //   R1 Trace
  //   contents of rom_3 (hex, n*v repeats v):
  //   36*0 3dca 16*0 3dca 16*0 3dca 604e 15*0 3dca 604e 15*0 3dca 604e 6e41 14*0 3dca 604e 6e41 12*0 5c2c
  //   0 3dca 604e 6e41 21d2 13*0 3dca 604e 6e41 21d2 11*0 604e 0 3dca 604e 6e41 21d2 1fae 10*0 21d2 0 3dca
  //   604e 6e41 21d2 1fae 12*0 3dca 604e 6e41 21d2 1fae 1098 9*0 4002 0 3dca 604e 6e41 21d2 1fae 1098 11*0
  //   3dca 604e 6e41 21d2 1fae 1098 161a 10*0 3dca 604e 6e41 21d2 1fae 1098 161a 10*0 3dca 604e 6e41 21d2
  //   1fae 1098 161a 4d31 9*0 3dca 604e 6e41 21d2 1fae 1098 161a 4d31 9*0 3dca 604e 6e41 21d2 1fae 1098
  //   161a 4d31 2009 8*0 3dca 604e 6e41 21d2 1fae 1098 161a 4d31 2009 6*0 6e41 0 3dca 604e 6e41 21d2 1fae
  //   1098 161a 4d31 2009 7c26 5*0 4131 0 3dca 604e 6e41 21d2 1fae 1098 161a 4d31 2009 7c26 7*0 3dca 604e
  //   6e41 21d2 1fae 1098 161a 4d31 2009 7c26 2c8c 4*0 6e41 0 3dca 604e 6e41 21d2 1fae 1098 161a 4d31 2009
  //   7c26 2c8c 4*0 1fae 0 3dca 604e 6e41 21d2 1fae 1098 161a 4d31 2009 7c26 2c8c 27bc 0 0 0 2009 0 3dca
  //   604e 6e41 21d2 1fae 1098 161a 4d31 2009 7c26 2c8c 27bc 0 0 0 347a 0 3dca 604e 6e41 21d2 1fae 1098
  //   161a 4d31 2009 7c26 2c8c 27bc 27a7 0 0 4d31 0 3dca 604e 6e41 21d2 1fae 1098 161a 4d31 2009 7c26 2c8c
  //   27bc 27a7 0 0 5c0c 0 3dca 604e 6e41 21d2 1fae 1098 161a 4d31 2009 7c26 2c8c 27bc 27a7 6de9 0 0 0
  //   3dca 604e 6e41 21d2 1fae 1098 161a 4d31 2009 7c26 2c8c 27bc 27a7 6de9 0 161a 0 3dca 604e 6e41 21d2
  //   1fae 1098 161a 4d31 2009 7c26 2c8c 27bc 27a7 6de9 38e5 360b 0 3dca 604e 6e41 21d2 1fae 1098 161a
  //   4d31 2009 7c26 2c8c 27bc 27a7 6de9 38e5
  //   你的寄存器文件封装正好合适放在这里
  //   R2 Trace
  //   contents of rom_4 (hex, n*v repeats v):
  //   18*0 5c0c 16*0 5c0c 16*0 5c0c 5c2c 14*0 3dca 5c0c 5c2c 15*0 5c0c 5c2c f00 14*0 5c0c 5c2c f00 14*0
  //   5c0c 5c2c f00 5f73 13*0 5c0c 5c2c f00 5f73 12*0 3dca 5c0c 5c2c f00 5f73 4002 12*0 5c0c 5c2c f00 5f73
  //   4002 11*0 5c2c 5c0c 5c2c f00 5f73 4002 6ee 11*0 5c0c 5c2c f00 5f73 4002 6ee 10*0 f00 5c0c 5c2c f00
  //   5f73 4002 6ee 347a 9*0 4002 5c0c 5c2c f00 5f73 4002 6ee 347a 9*0 347a 5c0c 5c2c f00 5f73 4002 6ee
  //   347a 4131 9*0 5c0c 5c2c f00 5f73 4002 6ee 347a 4131 9*0 5c0c 5c2c f00 5f73 4002 6ee 347a 4131 6368
  //   7*0 1fae 5c0c 5c2c f00 5f73 4002 6ee 347a 4131 6368 7*0 5f73 5c0c 5c2c f00 5f73 4002 6ee 347a 4131
  //   6368 5a74 7*0 5c0c 5c2c f00 5f73 4002 6ee 347a 4131 6368 5a74 6*0 4002 5c0c 5c2c f00 5f73 4002 6ee
  //   347a 4131 6368 5a74 b51 6*0 5c0c 5c2c f00 5f73 4002 6ee 347a 4131 6368 5a74 b51 5*0 21d2 5c0c 5c2c
  //   f00 5f73 4002 6ee 347a 4131 6368 5a74 b51 65a4 4*0 6ee 5c0c 5c2c f00 5f73 4002 6ee 347a 4131 6368
  //   5a74 b51 65a4 4*0 7c26 5c0c 5c2c f00 5f73 4002 6ee 347a 4131 6368 5a74 b51 65a4 716b 4*0 5c0c 5c2c
  //   f00 5f73 4002 6ee 347a 4131 6368 5a74 b51 65a4 716b 0 0 0 5f73 5c0c 5c2c f00 5f73 4002 6ee 347a 4131
  //   6368 5a74 b51 65a4 716b 5cad 0 0 5c0c 5c0c 5c2c f00 5f73 4002 6ee 347a 4131 6368 5a74 b51 65a4 716b
  //   5cad 0 0 5c0c 5c0c 5c2c f00 5f73 4002 6ee 347a 4131 6368 5a74 b51 65a4 716b 5cad 360b 0 161a 5c0c
  //   5c2c f00 5f73 4002 6ee 347a 4131 6368 5a74 b51 65a4 716b 5cad 360b 0 b51 5c0c 5c2c f00 5f73 4002 6ee
  //   347a 4131 6368 5a74 b51 65a4 716b 5cad 360b 406
  //   trace全零停止
endmodule

// 评分
module grade (
  input  EQ,
  input  CLK,
  output [31:0] \正确条数 ,
  output [3:0] High,
  output [3:0] Low,
  output [3:0] Mid,
  output Right,
  output [31:0] Total
);

  wire and_1_out, priority_encoder_1_gs, priority_encoder_1_out;
  wire [31:0] divider_1_out, divider_2_out, multiplier_1_out;
  wire [31:4] divider_2_rem, divider_3_out, divider_3_rem;

  Priority_Encoder #(.select(1)) priority_encoder_1 (
    .in0(EQ), .in1(EQ), .out(priority_encoder_1_out), .gs(priority_encoder_1_gs));  // open: en_out, en_in
  Counter #(.width(32), .max('hffffffff)) counter_1 (.count(1'b1), .Q(Total), .clk(CLK));  // open: load, D, carry, clr
  and and_1 (and_1_out, priority_encoder_1_out, priority_encoder_1_gs);
  Counter #(.width(32), .max('hffffffff)) counter_2 (
    .count(and_1_out), .Q(\正确条数 ), .clk(CLK));  // open: load, D, carry, clr
  Multiplier #(.width(32)) multiplier_1 (.a(\正确条数 ), .b(32'h64), .out(multiplier_1_out));  // open: cin, cout
  Divider #(.width(32)) divider_1 (.a(multiplier_1_out), .b(Total), .out(divider_1_out));  // open: upper, rem
  Divider #(.width(32)) divider_2 (
    .a(divider_1_out), .b(32'ha), .out(divider_2_out), .rem({divider_2_rem, Low}));  // open: upper
  Comparator #(.width(32)) comparator_1 (.a(\正确条数 ), .b(Total), .eq(Right));  // open: gt, lt
  Divider #(.width(32)) divider_3 (
    .a(divider_2_out), .b(32'ha), .out({divider_3_out, High}), .rem({divider_3_rem, Mid}));  // open: upper

  // Notes on the sheet:
  //   只有使用优先编码器才能屏蔽掉位置状态
endmodule
