// Logisim project alu.circ as structural Verilog: 3 circuits, main circuit ALU
module ALU (
  input  [31:0] X,
  input  [31:0] Y,
  input  [3:0] AluOP,
  output Signed_Overflow,
  output UnSigned_Overflow,
  output Equal,
  output [31:0] Result,
  output [31:0] Result_2
);

  wire and_1_out, and_2_out, and_3_out, and_4_out, and_8_out, and_9_out, and_10_out, and_11_out, CF5, CF6,
       comparator_1_lt, comparator_2_lt, demultiplexer_1_out3, demultiplexer_1_out4, demultiplexer_1_out5,
       demultiplexer_1_out6, not_1_out, not_2_out, not_3_out, not_4_out, not_5_out, not_6_out, OF5, OF6;
  wire [31:0] and_6_out, and_7_out, bit_extender_1_out, bit_extender_2_out, bit_extender_5_out, R0, R1, R2,
       R5, R6, R7, R8, R9, R10, R11, R12, R31, R32, R41, R42;

  // Probe on X
  // Probe on X
  Demultiplexer #(.select(4), .enable("false")) demultiplexer_1 (
    .out3(demultiplexer_1_out3), .out4(demultiplexer_1_out4), .out5(demultiplexer_1_out5),
    .out6(demultiplexer_1_out6), .in(1'b1), .sel(AluOP));  // open: out0, out1, out2, out7, out8, out9, out10, out11, out12, out13, out14, out15
  // Probe on Y
  // Probe on Y
  Shifter #(.width(32)) shifter_1 (.in(X), .\dist (Y[4:0]), .out(R0));
  Shifter #(.width(32), .shift("ar")) shifter_2 (.in(X), .\dist (Y[4:0]), .out(R1));
  Shifter #(.width(32), .shift("lr")) shifter_3 (.in(X), .\dist (Y[4:0]), .out(R2));
  Multiplier #(.width(32)) multiplier_1 (.a(X), .b(Y), .out(R31), .cout(R32));  // open: cin
  Divider #(.width(32)) divider_1 (.a(X), .b(Y), .out(R41), .rem(R42));  // open: upper
  Adder #(.width(32)) adder_1 (.a(X), .b(Y), .out(R5), .cin(1'b0), .cout(CF5));
  Subtractor #(.width(32)) subtractor_1 (.a(X), .b(Y), .out(R6), .bin(1'b0), .bout(CF6));
  assign bit_extender_1_out = {{31{demultiplexer_1_out3}}, demultiplexer_1_out3};  // Bit_Extender bit_extender_1
  assign bit_extender_2_out = {{31{demultiplexer_1_out4}}, demultiplexer_1_out4};  // Bit_Extender bit_extender_2
  and and_1 (and_1_out, demultiplexer_1_out5, OF5);
  and and_2 (and_2_out, demultiplexer_1_out6, OF6);
  and and_3 (and_3_out, demultiplexer_1_out5, CF5);
  and and_4 (and_4_out, demultiplexer_1_out6, CF6);
  // Probe on AluOP
  assign R7 = X & Y;  // AND_Gate and_5, 32 bits wide
  assign R8 = X | Y;  // OR_Gate or_1, 32 bits wide
  assign R9 = X ^ Y;  // XOR_Gate xor_1, 32 bits wide
  assign R10 = ~(X | Y);  // NOR_Gate nor_1, 32 bits wide
  assign and_6_out = bit_extender_1_out & R32;  // AND_Gate and_6, 32 bits wide
  assign and_7_out = bit_extender_2_out & R42;  // AND_Gate and_7, 32 bits wide
  or or_2 (Signed_Overflow, and_1_out, and_2_out);
  or or_3 (UnSigned_Overflow, and_3_out, and_4_out);
  // Probe on Result
  // Probe on Result
  Comparator #(.width(32)) comparator_1 (.a(X), .b(Y), .lt(comparator_1_lt));  // open: gt, eq
  assign R11 = {{31{1'b0}}, comparator_1_lt};  // Bit_Extender bit_extender_3
  Comparator #(.width(32), .mode("unsigned")) comparator_2 (.a(X), .b(Y), .lt(comparator_2_lt));  // open: gt, eq
  assign R12 = {{31{1'b0}}, comparator_2_lt};  // Bit_Extender bit_extender_4
  Comparator #(.width(32), .mode("unsigned")) comparator_3 (.a(X), .b(Y), .eq(Equal));  // open: gt, lt
  assign Result_2 = and_6_out | and_7_out;  // OR_Gate or_4, 32 bits wide
  // Probe on Result_2
  assign bit_extender_5_out = {{31{1'b0}}, 1'b0};  // Bit_Extender bit_extender_5
  not not_1 (not_1_out, R5[31]);
  not not_2 (not_2_out, X[31]);
  not not_3 (not_3_out, Y[31]);
  not not_4 (not_4_out, X[31]);
  not not_5 (not_5_out, R6[31]);
  not not_6 (not_6_out, Y[31]);
  and and_8 (and_8_out, X[31], Y[31], not_1_out);
  and and_9 (and_9_out, not_2_out, not_3_out, R5[31]);
  and and_10 (and_10_out, R6[31], Y[31], not_4_out);
  and and_11 (and_11_out, not_5_out, not_6_out, X[31]);
  Multiplexer #(.select(4), .width(32), .enable("false")) multiplexer_1 (
    .in0(R0), .in1(R1), .in2(R2), .in3(R31), .in4(R41), .in5(R5), .in6(R6), .in7(R7), .in8(R8), .in9(R9),
    .in10(R10), .in11(R11), .in12(R12), .in13(bit_extender_5_out), .in14(bit_extender_5_out),
    .in15(bit_extender_5_out), .out(Result), .sel(AluOP));
  or or_5 (OF5, and_8_out, and_9_out);
  or or_6 (OF6, and_10_out, and_11_out);

  // Other names for the same wires on the sheet: CF = UnSigned_Overflow; OF = Signed_Overflow;
  //   Result2[31:0] = Result_2; S[3:0] = AluOP; YL[4:0] = Y[4:0]

  // Notes on the sheet:
  //   不要改变此引脚区域内容，也不要改变ALU封装形式
  //   输入引脚
  //   请在下方利用上方输入输出引脚的隧道信号构建ALU电路，ctrl+d复制选择部件
  //   华中科技大学计算机学院 计算机组成原理，鸣谢加州大学伯克利CS61C课程
  //   输出引脚
  //   探测区域
endmodule

module \演示电路  (
  input  [31:0] X,
  input  [31:0] Y,
  input  [3:0] ALUOP,
  output Signed_Overflow,
  output Unsigned_overflow,
  output [31:0] Result,
  output [31:0] Result_2,
  output Equal
);

  // Probe on X
  // Probe on X
  ALU alu_1 (
    .AluOP(ALUOP), .X(X), .Equal(Equal), .Result(Result), .Signed_Overflow(Signed_Overflow), .Y(Y),
    .Result_2(Result_2), .UnSigned_Overflow(Unsigned_overflow));
  // Probe on ALUOP
  // Probe on Y
  // Probe on Y
  // Probe on Result
  // Probe on Result
  // Probe on Result_2
endmodule

module dengcha (
  input  [31:0] in_1,
  input  [31:0] in_2,
  input  in_3,
  input  [3:0] in_4,
  input  in_5,
  input  in_6,
  output [31:0] out,
  output [31:0] out_2,
  output [31:0] out_3
);

  wire clock_1_out, clock_2_out, not_1_out, not_2_out, register_3_q;
  wire [31:0] alu_1_result, register_1_q, register_4_q;

  // Probe on in_1
  Clock clock_1 (.out(clock_1_out));
  Clock clock_2 (.out(clock_2_out));
  Register #(.width(32)) register_1 (.D(out_2), .en(not_1_out), .Q(register_1_q), .clk(clock_1_out), .clr(in_3));
  not not_1 (not_1_out, 1'b0);
  Register #(.width(32)) register_2 (.D(in_1), .en(in_5), .Q(out_3), .clk(clock_2_out), .clr(in_6));
  // Probe on in_2
  Register #(.width(1)) register_3 (.D(not_1_out), .en(not_1_out), .Q(register_3_q), .clk(clock_1_out), .clr(in_3));
  // Probe on out_3
  ALU alu_1 (
    .AluOP(in_4), .X(in_2), .Result(alu_1_result), .Y(register_1_q));  // open: Equal, Signed_Overflow, Result_2, UnSigned_Overflow
  Register #(.width(32)) register_4 (.D(out), .en(not_1_out), .Q(register_4_q), .clk(clock_1_out), .clr(in_3));
  // Probe on out
  Multiplexer #(.width(32)) multiplexer_1 (
    .in0(in_1), .in1(alu_1_result), .out(out_2), .sel(register_3_q), .en(not_2_out));
  not not_2 (not_2_out, 1'b0);
  // Probe on out_2
  ALU alu_2 (
    .AluOP(in_4), .X(out_2), .Result(out), .Y(register_4_q));  // open: Equal, Signed_Overflow, Result_2, UnSigned_Overflow

  // Other names for the same wires on the sheet: a[31:0] = in_1; clear = in_3; d[31:0] = in_2; result[31:0] = out
endmodule
