// Logisim project controlUnit.circ as structural Verilog: 3 circuits, main circuit main
module main (
  input  [5:0] op,
  input  [5:0] funct,
  output [3:0] aluContorl,
  output shamtsign,
  output link,
  output sign,
  output WE,
  output Hi,
  output lw,
  output Lo,
  output sw,
  output jr,
  output HiLoW,
  output imm,
  output jump,
  output Branch,
  output equal1,
  output R1_E,
  output R2_E,
  output fromALU
);

  wire add, addi, addiu, addu, \and , andi, beq, controlunit1_1_fenable, divu, jump_t, mult, \nor , \or ,
       ori, sll, slt, slti, sltu, sra, srl, sub;

  controlUnit1 controlunit1_1 (
    .op5(op[5]), .op4(op[4]), .op3(op[3]), .op2(op[2]), .op1(op[1]), .op0(op[0]), .addi(addi), .addiu(addiu),
    .andi(andi), .ori(ori), .lw(lw), .sw(sw), .beq(beq), .bne(equal1), .slti(slti), .jump(jump_t),
    .jal(link), .fenable(controlunit1_1_fenable));
  controlUnit2 controlunit2_1 (
    .fenable(controlunit1_1_fenable), .funct5(funct[5]), .funct4(funct[4]), .funct3(funct[3]),
    .funct2(funct[2]), .funct1(funct[1]), .funct0(funct[0]), .add(add), .addu(addu), .\and (\and ),
    .sll(sll), .sra(sra), .srl(srl), .sub(sub), .\or (\or ), .\nor (\nor ), .mfhi(Hi), .mflo(Lo),
    .divu(divu), .slt(slt), .sltu(sltu), .jr(jr), .mult(mult));
  nor nor_1 (R1_E, sll, sra, srl, Hi, Lo, jump_t, link);
  nor nor_2 (R2_E, addi, addiu, andi, ori, Hi, Lo, lw, slti, jump_t, link, jr);
  or or_1 (Branch, beq, equal1);
  or or_2 (shamtsign, sll, sra, srl);
  or or_3 (jump, jump_t, link);
  or or_4 (imm, addi, addiu, andi, ori, lw, sw, beq, equal1, slti);
  or or_5 (sign, addi, addiu, lw, sw, beq, equal1);
  nor nor_3 (WE, divu, sw, beq, mult, equal1, jump_t, jr);
  nor nor_4 (fromALU, Hi, link, lw, Lo);
  or or_6 (aluContorl[2], add, addi, addu, addiu, \and , andi, sub, divu, lw, sw, sltu);
  or or_7 (aluContorl[1], \and , andi, sub, \nor , mult, srl, slt, slti);
  or or_8 (aluContorl[0], add, addi, addu, addiu, \and , andi, sra, mult, lw, sw, slt, slti);
  or or_9 (HiLoW, mult, divu);
  or or_10 (aluContorl[3], \or , ori, \nor , slt, slti, sltu);

  // Other names for the same wires on the sheet: bne = equal1; jal = link; jmp = jump; mfhi = Hi; mflo = Lo
endmodule

module controlUnit1 (
  input  op5,
  input  op4,
  input  op3,
  input  op2,
  input  op1,
  input  op0,
  output addi,
  output addiu,
  output andi,
  output ori,
  output lw,
  output sw,
  output beq,
  output bne,
  output slti,
  output jump,
  output jal,
  output fenable
);

  wire not_1_out, not_2_out, not_3_out, not_4_out, not_5_out, not_6_out, not_7_out, not_8_out, not_9_out,
       not_10_out, not_11_out, not_12_out, not_13_out, not_14_out, not_15_out, not_16_out, not_17_out,
       not_18_out, not_19_out, not_20_out, not_21_out, not_22_out, not_23_out, not_24_out, not_25_out,
       not_26_out, not_27_out, not_28_out, not_29_out, not_30_out, not_31_out, not_32_out, not_33_out,
       not_34_out, not_35_out, not_36_out, not_37_out, not_38_out, not_39_out, not_40_out, not_41_out,
       not_42_out, not_43_out, not_44_out, not_45_out, not_46_out, not_47_out, not_48_out, not_49_out;

  not not_1 (not_1_out, op5);
  not not_2 (not_2_out, op4);
  not not_3 (not_3_out, op2);
  not not_4 (not_4_out, op1);
  not not_5 (not_5_out, op0);
  not not_6 (not_6_out, op5);
  not not_7 (not_7_out, op4);
  not not_8 (not_8_out, op2);
  not not_9 (not_9_out, op1);
  not not_10 (not_10_out, op5);
  not not_11 (not_11_out, op4);
  not not_12 (not_12_out, op1);
  not not_13 (not_13_out, op0);
  not not_14 (not_14_out, op5);
  not not_15 (not_15_out, op4);
  not not_16 (not_16_out, op1);
  not not_17 (not_17_out, op4);
  not not_18 (not_18_out, op3);
  not not_19 (not_19_out, op2);
  not not_20 (not_20_out, op4);
  not not_21 (not_21_out, op2);
  not not_22 (not_22_out, op5);
  not not_23 (not_23_out, op4);
  not not_24 (not_24_out, op3);
  not not_25 (not_25_out, op1);
  not not_26 (not_26_out, op0);
  not not_27 (not_27_out, op5);
  not not_28 (not_28_out, op4);
  not not_29 (not_29_out, op3);
  not not_30 (not_30_out, op1);
  not not_31 (not_31_out, op5);
  not not_32 (not_32_out, op4);
  not not_33 (not_33_out, op2);
  not not_34 (not_34_out, op0);
  not not_35 (not_35_out, op5);
  not not_36 (not_36_out, op4);
  not not_37 (not_37_out, op3);
  not not_38 (not_38_out, op2);
  not not_39 (not_39_out, op0);
  not not_40 (not_40_out, op5);
  not not_41 (not_41_out, op4);
  not not_42 (not_42_out, op3);
  not not_43 (not_43_out, op2);
  not not_44 (not_44_out, op5);
  not not_45 (not_45_out, op4);
  not not_46 (not_46_out, op3);
  not not_47 (not_47_out, op2);
  not not_48 (not_48_out, op1);
  not not_49 (not_49_out, op0);
  and and_1 (addi, not_1_out, not_2_out, op3, not_3_out, not_4_out, not_5_out);
  and and_2 (addiu, not_6_out, not_7_out, op3, not_8_out, not_9_out, op0);
  and and_3 (andi, not_10_out, not_11_out, op3, op2, not_12_out, not_13_out);
  and and_4 (ori, not_14_out, not_15_out, op3, op2, not_16_out, op0);
  and and_5 (lw, op5, not_17_out, not_18_out, not_19_out, op1, op0);
  and and_6 (sw, op5, not_20_out, op3, not_21_out, op1, op0);
  and and_7 (beq, not_22_out, not_23_out, not_24_out, op2, not_25_out, not_26_out);
  and and_8 (bne, not_27_out, not_28_out, not_29_out, op2, not_30_out, op0);
  and and_9 (slti, not_31_out, not_32_out, op3, not_33_out, op1, not_34_out);
  and and_10 (jump, not_35_out, not_36_out, not_37_out, not_38_out, op1, not_39_out);
  and and_11 (jal, not_40_out, not_41_out, not_42_out, not_43_out, op1, op0);
  and and_12 (fenable, not_44_out, not_45_out, not_46_out, not_47_out, not_48_out, not_49_out);
endmodule

module controlUnit2 (
  input  fenable,
  input  funct5,
  input  funct4,
  input  funct3,
  input  funct2,
  input  funct1,
  input  funct0,
  output add,
  output addu,
  output \and ,
  output sll,
  output sra,
  output srl,
  output sub,
  output \or ,
  output \nor ,
  output mfhi,
  output mflo,
  output divu,
  output slt,
  output sltu,
  output jr,
  output mult
);

  wire and_1_out, and_2_out, and_3_out, and_4_out, and_5_out, and_6_out, and_7_out, and_8_out, and_9_out,
       and_10_out, and_11_out, and_12_out, and_13_out, and_14_out, and_15_out, and_16_out, not_1_out,
       not_2_out, not_3_out, not_4_out, not_5_out, not_6_out, not_7_out, not_8_out, not_9_out, not_10_out,
       not_11_out, not_12_out, not_13_out, not_14_out, not_15_out, not_16_out, not_17_out, not_18_out,
       not_19_out, not_20_out, not_21_out, not_22_out, not_23_out, not_24_out, not_25_out, not_26_out,
       not_27_out, not_28_out, not_29_out, not_30_out, not_31_out, not_32_out, not_33_out, not_34_out,
       not_35_out, not_36_out, not_37_out, not_38_out, not_39_out, not_40_out, not_41_out, not_42_out,
       not_43_out, not_44_out, not_45_out, not_46_out, not_47_out, not_48_out, not_49_out, not_50_out,
       not_51_out, not_52_out, not_53_out, not_54_out, not_55_out, not_56_out, not_57_out, not_58_out,
       not_59_out, not_60_out, not_61_out, not_62_out;

  not not_1 (not_1_out, funct4);
  not not_2 (not_2_out, funct3);
  not not_3 (not_3_out, funct2);
  not not_4 (not_4_out, funct1);
  not not_5 (not_5_out, funct0);
  not not_6 (not_6_out, funct4);
  not not_7 (not_7_out, funct3);
  not not_8 (not_8_out, funct2);
  not not_9 (not_9_out, funct1);
  not not_10 (not_10_out, funct4);
  not not_11 (not_11_out, funct3);
  not not_12 (not_12_out, funct1);
  not not_13 (not_13_out, funct0);
  not not_14 (not_14_out, funct5);
  not not_15 (not_15_out, funct4);
  not not_16 (not_16_out, funct3);
  not not_17 (not_17_out, funct2);
  not not_18 (not_18_out, funct1);
  not not_19 (not_19_out, funct0);
  not not_20 (not_20_out, funct5);
  not not_21 (not_21_out, funct4);
  not not_22 (not_22_out, funct3);
  not not_23 (not_23_out, funct2);
  not not_24 (not_24_out, funct5);
  not not_25 (not_25_out, funct4);
  not not_26 (not_26_out, funct3);
  not not_27 (not_27_out, funct2);
  not not_28 (not_28_out, funct0);
  not not_29 (not_29_out, funct4);
  not not_30 (not_30_out, funct3);
  not not_31 (not_31_out, funct2);
  not not_32 (not_32_out, funct0);
  not not_33 (not_33_out, funct4);
  not not_34 (not_34_out, funct3);
  not not_35 (not_35_out, funct1);
  not not_36 (not_36_out, funct4);
  not not_37 (not_37_out, funct3);
  not not_38 (not_38_out, funct5);
  not not_39 (not_39_out, funct3);
  not not_40 (not_40_out, funct2);
  not not_41 (not_41_out, funct1);
  not not_42 (not_42_out, funct0);
  not not_43 (not_43_out, funct5);
  not not_44 (not_44_out, funct3);
  not not_45 (not_45_out, funct2);
  not not_46 (not_46_out, funct0);
  not not_47 (not_47_out, funct5);
  not not_48 (not_48_out, funct2);
  not not_49 (not_49_out, funct4);
  not not_50 (not_50_out, funct2);
  not not_51 (not_51_out, funct0);
  not not_52 (not_52_out, funct4);
  not not_53 (not_53_out, funct2);
  not not_54 (not_54_out, funct5);
  not not_55 (not_55_out, funct4);
  not not_56 (not_56_out, funct2);
  not not_57 (not_57_out, funct1);
  not not_58 (not_58_out, funct0);
  not not_59 (not_59_out, funct5);
  not not_60 (not_60_out, funct2);
  not not_61 (not_61_out, funct1);
  not not_62 (not_62_out, funct0);
  and and_1 (and_1_out, funct5, not_1_out, not_2_out, not_3_out, not_4_out, not_5_out);
  and and_2 (and_2_out, funct5, not_6_out, not_7_out, not_8_out, not_9_out, funct0);
  and and_3 (and_3_out, funct5, not_10_out, not_11_out, funct2, not_12_out, not_13_out);
  and and_4 (and_4_out, not_14_out, not_15_out, not_16_out, not_17_out, not_18_out, not_19_out);
  and and_5 (and_5_out, not_20_out, not_21_out, not_22_out, not_23_out, funct1, funct0);
  and and_6 (and_6_out, not_24_out, not_25_out, not_26_out, not_27_out, funct1, not_28_out);
  and and_7 (and_7_out, funct5, not_29_out, not_30_out, not_31_out, funct1, not_32_out);
  and and_8 (and_8_out, funct5, not_33_out, not_34_out, funct2, not_35_out, funct0);
  and and_9 (and_9_out, funct5, not_36_out, not_37_out, funct2, funct1, funct0);
  and and_10 (and_10_out, not_38_out, funct4, not_39_out, not_40_out, not_41_out, not_42_out);
  and and_11 (and_11_out, not_43_out, funct4, not_44_out, not_45_out, funct1, not_46_out);
  and and_12 (and_12_out, not_47_out, funct4, funct3, not_48_out, funct1, funct0);
  and and_13 (and_13_out, funct5, not_49_out, funct3, not_50_out, funct1, not_51_out);
  and and_14 (and_14_out, funct5, not_52_out, funct3, not_53_out, funct1, funct0);
  and and_15 (and_15_out, not_54_out, not_55_out, funct3, not_56_out, not_57_out, not_58_out);
  and and_16 (and_16_out, not_59_out, funct4, funct3, not_60_out, not_61_out, not_62_out);
  and and_17 (add, fenable, and_1_out);
  and and_18 (addu, fenable, and_2_out);
  and and_19 (\and , fenable, and_3_out);
  and and_20 (sll, fenable, and_4_out);
  and and_21 (sra, fenable, and_5_out);
  and and_22 (srl, fenable, and_6_out);
  and and_23 (sub, fenable, and_7_out);
  and and_24 (\or , fenable, and_8_out);
  and and_25 (\nor , fenable, and_9_out);
  and and_26 (mfhi, fenable, and_10_out);
  and and_27 (mflo, fenable, and_11_out);
  and and_28 (divu, fenable, and_12_out);
  and and_29 (slt, fenable, and_13_out);
  and and_30 (sltu, fenable, and_14_out);
  and and_31 (jr, fenable, and_15_out);
  and and_32 (mult, fenable, and_16_out);
endmodule
