// Logisim project counter.circ as structural Verilog: 1 circuit, main circuit main
module main (
  input  wrong,
  input  halt,
  input  noforecast,
  input  clk,
  input  clear,
  input  DataPk,
  input  forecast,
  input  Jumpnop,
  output [15:0] circle,
  output [15:0] jrTime,
  output [15:0] DataPkTime,
  output [15:0] noforecastTime,
  output [15:0] JumpnopTime,
  output [15:0] forecastTime
);

  wire and_1_out, and_2_out, and_3_out, and_4_out, and_5_out, not_1_out, register_1_q, register_2_q,
       register_3_q, register_4_q, register_5_q, register_6_q;
  wire [15:0] adder_1_out, bit_extender_1_out, bit_extender_2_out, bit_extender_3_out, bit_extender_4_out,
       bit_extender_5_out, bit_extender_6_out, counter_1_q, counter_2_q, counter_3_q, counter_4_q,
       counter_5_q, Jumpnopcounter_q, subtractor_1_out, subtractor_2_out, subtractor_3_out, subtractor_4_out,
       subtractor_5_out, subtractor_6_out;

  not not_1 (not_1_out, halt);
  and and_1 (and_1_out, not_1_out, DataPk);
  and and_2 (and_2_out, not_1_out, Jumpnop);
  Counter #(.width(16), .max('hffff)) counter_1 (
    .load(1'b0), .D(counter_1_q), .count(not_1_out), .Q(counter_1_q), .clk(clk), .clr(clear));  // open: carry
  Counter #(.width(16), .max('hffff)) counter_2 (
    .load(1'b0), .D(counter_2_q), .count(and_1_out), .Q(counter_2_q), .clk(clk), .clr(clear));  // open: carry
  Register #(.width(1)) register_1 (.D(DataPk), .en(1'b1), .Q(register_1_q), .clk(clk), .clr(clear));
  Counter #(.width(16), .max('hffff)) Jumpnopcounter (
    .load(1'b0), .D(Jumpnopcounter_q), .count(and_2_out), .Q(Jumpnopcounter_q), .clk(clk), .clr(clear));  // open: carry
  Register #(.width(1)) register_2 (.D(Jumpnop), .en(1'b1), .Q(register_2_q), .clk(clk), .clr(clear));
  Adder #(.width(16)) adder_1 (.a(16'h1), .b(counter_1_q), .out(adder_1_out));  // open: cin, cout
  assign bit_extender_1_out = {{15{1'b0}}, register_1_q};  // Bit_Extender bit_extender_1
  Register #(.width(1)) register_3 (.D(register_1_q), .en(1'b1), .Q(register_3_q), .clk(clk), .clr(clear));
  Subtractor #(.width(16)) subtractor_1 (
    .a(Jumpnopcounter_q), .b(bit_extender_2_out), .out(subtractor_1_out));  // open: bin, bout
  assign bit_extender_2_out = {{15{1'b0}}, register_2_q};  // Bit_Extender bit_extender_2
  // Probe on circle
  Multiplexer #(.width(16), .enable("false")) multiplexer_1 (
    .in0(counter_1_q), .in1(adder_1_out), .out(circle), .sel(halt));
  Subtractor #(.width(16)) subtractor_2 (
    .a(counter_2_q), .b(bit_extender_1_out), .out(subtractor_2_out));  // open: bin, bout
  assign bit_extender_3_out = {{15{1'b0}}, register_3_q};  // Bit_Extender bit_extender_3
  Multiplexer #(.width(16), .enable("false")) multiplexer_2 (
    .in0(Jumpnopcounter_q), .in1(subtractor_1_out), .out(JumpnopTime), .sel(halt));
  Multiplexer #(.width(16), .enable("false")) multiplexer_3 (
    .in0(counter_2_q), .in1(subtractor_3_out), .out(DataPkTime), .sel(halt));
  Subtractor #(.width(16)) subtractor_3 (
    .a(subtractor_2_out), .b(bit_extender_3_out), .out(subtractor_3_out));  // open: bin, bout
  and and_3 (and_3_out, not_1_out, wrong);
  and and_4 (and_4_out, not_1_out, forecast);
  and and_5 (and_5_out, not_1_out, noforecast);
  Counter #(.width(16), .max('hffff)) counter_3 (
    .load(1'b0), .D(counter_3_q), .count(and_3_out), .Q(counter_3_q), .clk(clk), .clr(clear));  // open: carry
  Register #(.width(1)) register_4 (.D(wrong), .en(1'b1), .Q(register_4_q), .clk(clk), .clr(clear));
  Counter #(.width(16), .max('hffff)) counter_4 (
    .load(1'b0), .D(counter_4_q), .count(and_4_out), .Q(counter_4_q), .clk(clk), .clr(clear));  // open: carry
  Register #(.width(1)) register_5 (.D(forecast), .en(1'b1), .Q(register_5_q), .clk(clk), .clr(clear));
  Counter #(.width(16), .max('hffff)) counter_5 (
    .load(1'b0), .D(counter_5_q), .count(and_5_out), .Q(counter_5_q), .clk(clk), .clr(clear));  // open: carry
  Register #(.width(1)) register_6 (.D(noforecast), .en(1'b1), .Q(register_6_q), .clk(clk), .clr(clear));
  assign bit_extender_4_out = {{15{1'b0}}, register_4_q};  // Bit_Extender bit_extender_4
  assign bit_extender_5_out = {{15{1'b0}}, register_5_q};  // Bit_Extender bit_extender_5
  assign bit_extender_6_out = {{15{1'b0}}, register_6_q};  // Bit_Extender bit_extender_6
  Multiplexer #(.width(16), .enable("false")) multiplexer_4 (
    .in0(counter_3_q), .in1(subtractor_4_out), .out(jrTime), .sel(halt));
  Subtractor #(.width(16)) subtractor_4 (
    .a(counter_3_q), .b(bit_extender_4_out), .out(subtractor_4_out));  // open: bin, bout
  Subtractor #(.width(16)) subtractor_5 (
    .a(counter_4_q), .b(bit_extender_5_out), .out(subtractor_5_out));  // open: bin, bout
  Subtractor #(.width(16)) subtractor_6 (
    .a(counter_5_q), .b(bit_extender_6_out), .out(subtractor_6_out));  // open: bin, bout
  Multiplexer #(.width(16), .enable("false")) multiplexer_5 (
    .in0(counter_4_q), .in1(subtractor_5_out), .out(forecastTime), .sel(halt));
  Multiplexer #(.width(16), .enable("false")) multiplexer_6 (
    .in0(counter_5_q), .in1(subtractor_6_out), .out(noforecastTime), .sel(halt));
endmodule
