// Logisim project extend.circ as structural Verilog: 1 circuit, main circuit main
module main (
  input  sign,
  input  shamtsign,
  input  [15:0] IMM,
  input  [4:0] shamt,
  output [31:0] result
);

  wire not_1_out;
  wire [31:0] bit_extender_1_out, bit_extender_2_out, bit_extender_3_out, multiplexer_1_out;

  assign bit_extender_1_out = {{16{1'b0}}, IMM};  // Bit_Extender bit_extender_1
  assign bit_extender_2_out = {{16{IMM[15]}}, IMM};  // Bit_Extender bit_extender_2
  assign bit_extender_3_out = {{27{1'b0}}, shamt};  // Bit_Extender bit_extender_3
  Multiplexer #(.width(32)) multiplexer_1 (
    .in0(bit_extender_1_out), .in1(bit_extender_2_out), .out(multiplexer_1_out), .sel(sign), .en(not_1_out));
  not not_1 (not_1_out, 1'b0);
  Multiplexer #(.width(32)) multiplexer_2 (
    .in0(multiplexer_1_out), .in1(bit_extender_3_out), .out(result), .sel(shamtsign), .en(not_1_out));
endmodule
