// Logisim project format.circ as structural Verilog: 1 circuit, main circuit format
module format (
  input  [31:0] IR,
  output [5:0] OP,
  output [5:0] funct,
  output [25:0] ADDR,
  output [4:0] rs,
  output [4:0] shamt,
  output [4:0] rt,
  output [4:0] rd,
  output [15:0] IMM
);


  assign ADDR = IR[25:0];
  assign funct = IR[5:0];
  assign IMM = IR[15:0];
  assign OP = IR[31:26];
  assign rd = IR[15:11];
  assign rs = IR[25:21];
  assign rt = IR[20:16];
  assign shamt = IR[10:6];
endmodule
