// Logisim project mips.circ as structural Verilog: 6 circuits, main circuit main
module main (
  input  in_1
);

  wire alu_1_equal, and_1_out, and_2_out, and_3_out, and_5_out, and_6_out, and_7_out, clk, clock_1_out,
       comparator_1_eq, comparator_2_eq, datatest_1_datanop, datatest_1_forecast, datatest_1_ir_idlock,
       datatest_1_jumpnopid_ex, datatest_1_jumpnopir_id, datatest_1_noforecast, datatest_1_pclock,
       datatest_1_wrong, ex_mem_1_hiout, ex_mem_1_linkout, ex_mem_1_loout, ex_mem_1_lwout, ex_mem_1_swout,
       ex_mem_1_syscallout, ex_mem_1_weout, halt, id_ex_1_branchout, id_ex_1_equal1out, id_ex_1_fromaluout,
       id_ex_1_hilowout, id_ex_1_hiout, id_ex_1_jrout, id_ex_1_jumpout, id_ex_1_linkout, id_ex_1_loout,
       id_ex_1_lwout, id_ex_1_swout, id_ex_1_syscallout, id_ex_1_weout, imm, IR_ID_syscallout, main_1_branch,
       main_1_equal1, main_1_fromalu, main_1_hi, main_1_hilow, main_1_jr, main_1_jump, main_1_link,
       main_1_lo, main_1_lw, main_1_r1_e, main_1_r2_e, main_1_sw, main_1_we, mem_wb_1_syscallout, not_1_out,
       not_2_out, not_3_out, not_4_out, or_1_out, or_3_out, or_4_out, or_5_out, or_6_out, or_7_out, or_8_out,
       or_9_out, shamtsign, sign, WE, xor_1_out;
  wire [3:0] id_ex_1_alucontrolout, main_1_alucontorl, register_1_q, register_1_q_2, register_1_q_3,
       register_1_q_4, register_1_q_5, register_1_q_6, register_1_q_7, register_1_q_8;
  wire [4:0] ex_mem_1_rw_out, format_1_rd, format_1_rs, format_1_rt, format_1_shamt, id_ex_1_rw_out,
       multiplexer_1_out, multiplexer_2_out, RW_num;
  wire [5:0] format_1_funct, format_1_op;
  wire [15:0] format_1_imm, main_4_circle, main_4_datapktime, main_4_forecasttime, main_4_jrtime,
       main_4_jumpnoptime, main_4_noforecasttime;
  wire [25:0] format_1_addr;
  wire [31:0] a0, adder_1_out, adder_2_out, alu_1_result, alu_1_result_2, and_4_out, bit_extender_1_out,
       Data, datatest_1_pcout, datatest_1_rfr1out, datatest_1_rfr2out, ex_mem_1_irout, ex_mem_1_pcout,
       ex_mem_1_result1out, ex_mem_1_rfr2out, Hi_q, id_ex_1_addrout, id_ex_1_irout, id_ex_1_offsetout,
       id_ex_1_pcout, id_ex_1_rfr1out, id_ex_1_rfr2out, id_ex_1_xout, id_ex_1_yout, IR_ID_irout, IR_ID_pcout,
       Lo_q, main_2_reg1, main_2_reg2_2, main_3_result, multiplexer_3_out, multiplexer_4_out,
       multiplexer_5_out, multiplexer_6_out, multiplexer_7_out, multiplexer_8_out, multiplexer_9_out,
       multiplexer_10_out, multiplexer_11_out, or_2_out, PC_q, ram_1_data, rom_1_data, shifter_1_out,
       shifter_2_out, v0;

  Register #(.width(32)) PC (.D(datatest_1_pcout), .en(1'b1), .Q(PC_q), .clk(and_1_out), .clr(in_1));
  and and_1 (and_1_out, not_1_out, clk);
  not not_1 (not_1_out, datatest_1_pclock);
  Adder #(.width(32)) adder_1 (.a(32'h4), .b(PC_q), .out(adder_1_out));  // open: cin, cout
  ROM #(.addrWidth(10), .dataWidth(32)) rom_1 (.addr(PC_q[11:2]), .data(rom_1_data), .sel(1'b1));
  IF_ID IR_ID (
    .Syscallin(comparator_1_eq), .PCin(adder_1_out), .IRin(rom_1_data), .Syscallout(IR_ID_syscallout),
    .PCout(IR_ID_pcout), .IRout(IR_ID_irout), .clk(and_2_out), .clear(or_1_out));
  Comparator #(.width(32)) comparator_1 (.a(32'hc), .b(rom_1_data), .eq(comparator_1_eq));  // open: gt, lt
  and and_2 (and_2_out, clk, not_2_out);
  or or_1 (or_1_out, and_3_out, in_1);
  and and_3 (and_3_out, clk, datatest_1_jumpnopir_id);
  not not_2 (not_2_out, datatest_1_ir_idlock);
  format format_1 (
    .IR(IR_ID_irout), .ADDR(format_1_addr), .shamt(format_1_shamt), .OP(format_1_op), .funct(format_1_funct),
    .rs(format_1_rs), .rt(format_1_rt), .rd(format_1_rd), .IMM(format_1_imm));
  DATAtest datatest_1 (
    .EXWE(id_ex_1_weout), .MEMWE(ex_mem_1_weout), .R1_E(main_1_r1_e), .R2_E(main_1_r2_e),
    .EXRW_num(id_ex_1_rw_out), .MEMRW_num(ex_mem_1_rw_out), .R1_num(format_1_rs), .R2_num(format_1_rt),
    .PClock(datatest_1_pclock), .IR_IDlock(datatest_1_ir_idlock), .datanop(datatest_1_datanop), .in_16(clk),
    .in_17(in_1), .jumppk(or_7_out), .jumpnopIR_ID(datatest_1_jumpnopir_id),
    .jumpnopID_EX(datatest_1_jumpnopid_ex), .fromALUEX(id_ex_1_fromaluout), .ALUEX(alu_1_result),
    .Din(multiplexer_11_out), .RFR1(main_2_reg1), .RFR2(main_2_reg2_2), .RFR2out(datatest_1_rfr2out),
    .RFR1out(datatest_1_rfr1out), .PCout(datatest_1_pcout), .PCin(adder_1_out), .PC(id_ex_1_pcout),
    .jumpPC(multiplexer_7_out), .branch(or_6_out), .wrong(datatest_1_wrong),
    .noforecast(datatest_1_noforecast), .forecast(datatest_1_forecast));
  controlUnit_main main_1 (
    .op(format_1_op), .funct(format_1_funct), .aluContorl(main_1_alucontorl), .shamtsign(shamtsign),
    .link(main_1_link), .sign(sign), .WE(main_1_we), .Hi(main_1_hi), .lw(main_1_lw), .Lo(main_1_lo),
    .sw(main_1_sw), .jr(main_1_jr), .HiLoW(main_1_hilow), .imm(imm), .jump(main_1_jump),
    .Branch(main_1_branch), .equal1(main_1_equal1), .R1_E(main_1_r1_e), .R2_E(main_1_r2_e),
    .fromALU(main_1_fromalu));
  Multiplexer #(.width(5), .enable("false")) multiplexer_1 (
    .in0(format_1_rd), .in1(format_1_rt), .out(multiplexer_1_out), .sel(imm));
  Multiplexer #(.width(5), .enable("false")) multiplexer_2 (
    .in0(multiplexer_1_out), .in1({5{1'b1}}), .out(multiplexer_2_out), .sel(main_1_link));
  assign bit_extender_1_out = {{6{1'b0}}, format_1_addr};  // Bit_Extender bit_extender_1
  assign and_4_out = IR_ID_pcout & 32'hf0000000;  // AND_Gate and_4, 32 bits wide
  regfile_main main_2 (
    .Reg1_num(format_1_rs), .Reg2(format_1_rt), .Write_Reg_num(RW_num), .Din(Data), .Write_Enable(WE),
    .Clock(clk), .Reg1(main_2_reg1), .Reg2_2(main_2_reg2_2), .v0_Value(v0), .a0_Value(a0));  // open: s2_Value, ra_Value
  extend_main main_3 (
    .sign(sign), .shamtsign(shamtsign), .IMM(format_1_imm), .shamt(format_1_shamt), .result(main_3_result));
  Shifter #(.width(32)) shifter_1 (.in(bit_extender_1_out), .\dist (5'b00010), .out(shifter_1_out));
  assign or_2_out = shifter_1_out | and_4_out;  // OR_Gate or_2, 32 bits wide
  Multiplexer #(.width(32), .enable("false")) multiplexer_3 (
    .in0(datatest_1_rfr1out), .in1(datatest_1_rfr2out), .out(multiplexer_3_out), .sel(shamtsign));
  Multiplexer #(.width(32), .enable("false")) multiplexer_4 (
    .in0(datatest_1_rfr2out), .in1(main_3_result), .out(multiplexer_4_out), .sel(and_5_out));
  and and_5 (and_5_out, not_3_out, or_3_out);
  not not_3 (not_3_out, main_1_branch);
  or or_3 (or_3_out, shamtsign, imm);
  Shifter #(.width(32)) shifter_2 (.in(main_3_result), .\dist (5'b00010), .out(shifter_2_out));
  ID_EX id_ex_1 (
    .Xin(multiplexer_3_out), .Yin(multiplexer_4_out), .RFR2in(datatest_1_rfr2out), .Xout(id_ex_1_xout),
    .Yout(id_ex_1_yout), .RFR2out(id_ex_1_rfr2out), .clk(clk), .clear(or_5_out), .RFR1in(datatest_1_rfr1out),
    .RFR1out(id_ex_1_rfr1out), .ALUcontrolin(main_1_alucontorl), .ALUcontrolout(id_ex_1_alucontrolout),
    .lwin(main_1_lw), .lwout(id_ex_1_lwout), .swin(main_1_sw), .swout(id_ex_1_swout),
    .RW_in(multiplexer_2_out), .RW_out(id_ex_1_rw_out), .PCin(IR_ID_pcout), .PCout(id_ex_1_pcout),
    .IRin(IR_ID_irout), .IRout(id_ex_1_irout), .WEin(main_1_we), .WEout(id_ex_1_weout),
    .HiLoWin(main_1_hilow), .HiLoWout(id_ex_1_hilowout), .linkin(main_1_link), .linkout(id_ex_1_linkout),
    .Hiin(main_1_hi), .Hiout(id_ex_1_hiout), .Loin(main_1_lo), .Loout(id_ex_1_loout), .jrin(main_1_jr),
    .jrout(id_ex_1_jrout), .jumpin(main_1_jump), .jumpout(id_ex_1_jumpout), .Branchin(main_1_branch),
    .Branchout(id_ex_1_branchout), .equal1in(main_1_equal1), .equal1out(id_ex_1_equal1out),
    .offsetin(shifter_2_out), .offsetout(id_ex_1_offsetout), .addrin(or_2_out), .addrout(id_ex_1_addrout),
    .Syscallin(IR_ID_syscallout), .Syscallout(id_ex_1_syscallout), .fromALUin(main_1_fromalu),
    .fromALUout(id_ex_1_fromaluout));
  and and_6 (and_6_out, clk, or_4_out);
  or or_4 (or_4_out, datatest_1_jumpnopid_ex, datatest_1_datanop);
  or or_5 (or_5_out, and_6_out, in_1);
  Multiplexer #(.width(32), .enable("false")) multiplexer_5 (
    .in0(adder_1_out), .in1(id_ex_1_addrout), .out(multiplexer_5_out), .sel(id_ex_1_jumpout));
  Adder #(.width(32)) adder_2 (.a(id_ex_1_pcout), .b(id_ex_1_offsetout), .out(adder_2_out));  // open: cin, cout
  ALU alu_1 (
    .AluOP(id_ex_1_alucontrolout), .X(id_ex_1_xout), .Equal(alu_1_equal), .Result(alu_1_result),
    .Y(id_ex_1_yout), .Result_2(alu_1_result_2));  // open: Signed_Overflow, UnSigned_Overflow
  xor xor_1 (xor_1_out, alu_1_equal, id_ex_1_equal1out);
  or or_6 (or_6_out, id_ex_1_branchout, id_ex_1_jumpout, id_ex_1_jrout);
  Multiplexer #(.width(32), .enable("false")) multiplexer_6 (
    .in0(multiplexer_5_out), .in1(adder_2_out), .out(multiplexer_6_out), .sel(and_7_out));
  Multiplexer #(.width(32), .enable("false")) multiplexer_7 (
    .in0(multiplexer_6_out), .in1(id_ex_1_rfr1out), .out(multiplexer_7_out), .sel(id_ex_1_jrout));
  and and_7 (and_7_out, xor_1_out, id_ex_1_branchout);
  or or_7 (or_7_out, id_ex_1_jumpout, and_7_out, id_ex_1_jrout);
  EX_MEM ex_mem_1 (
    .Result1in(alu_1_result), .Result1out(ex_mem_1_result1out), .clk(clk), .clear(in_1),
    .swin(id_ex_1_swout), .swout(ex_mem_1_swout), .lwin(id_ex_1_lwout), .lwout(ex_mem_1_lwout),
    .RFR2in(id_ex_1_rfr2out), .RFR2out(ex_mem_1_rfr2out), .PCin(id_ex_1_pcout), .PCout(ex_mem_1_pcout),
    .IRin(id_ex_1_irout), .IRout(ex_mem_1_irout), .WEin(id_ex_1_weout), .WEout(ex_mem_1_weout),
    .linkin(id_ex_1_linkout), .linkout(ex_mem_1_linkout), .Hiin(id_ex_1_hiout), .Hiout(ex_mem_1_hiout),
    .Loin(id_ex_1_loout), .Loout(ex_mem_1_loout), .RW_in(id_ex_1_rw_out), .RW_out(ex_mem_1_rw_out),
    .Syscallin(id_ex_1_syscallout), .Syscallout(ex_mem_1_syscallout));
  Register #(.width(32)) Lo (.D(alu_1_result), .en(id_ex_1_hilowout), .Q(Lo_q), .clk(clk), .clr(in_1));
  Register #(.width(32)) Hi (.D(alu_1_result_2), .en(id_ex_1_hilowout), .Q(Hi_q), .clk(clk), .clr(in_1));
  not not_4 (not_4_out, halt);
  Clock clock_1 (.out(clock_1_out));
  Multiplexer #(.width(32), .enable("false")) multiplexer_8 (
    .in0(ex_mem_1_result1out), .in1(ex_mem_1_pcout), .out(multiplexer_8_out), .sel(ex_mem_1_linkout));
  and and_8 (clk, not_4_out, clock_1_out);
  Multiplexer #(.width(32), .enable("false")) multiplexer_9 (
    .in0(multiplexer_8_out), .in1(Lo_q), .out(multiplexer_9_out), .sel(ex_mem_1_loout));
  Multiplexer #(.width(32), .enable("false")) multiplexer_10 (
    .in0(multiplexer_9_out), .in1(Hi_q), .out(multiplexer_10_out), .sel(ex_mem_1_hiout));
  or or_8 (or_8_out, ex_mem_1_swout, ex_mem_1_lwout);
  Multiplexer #(.width(32), .enable("false")) multiplexer_11 (
    .in0(multiplexer_10_out), .in1(ram_1_data), .out(multiplexer_11_out), .sel(ex_mem_1_lwout));
  RAM #(.addrWidth(24), .dataWidth(32), .bus("separate")) ram_1 (
    .addr(ex_mem_1_result1out[25:2]), .din(ex_mem_1_rfr2out), .data(ram_1_data), .str(ex_mem_1_swout),
    .sel(or_8_out), .clk(clk), .ld(ex_mem_1_lwout), .clr(in_1));
  Hex_Digit_Display hex_digit_display_1 (.value(register_1_q_7));  // open: dp
  Hex_Digit_Display hex_digit_display_2 (.value(register_1_q_8));  // open: dp
  MEM_WB mem_wb_1 (
    .datain(multiplexer_11_out), .dataout(Data), .clk(clk), .clear(in_1), .PCin(ex_mem_1_pcout),
    .IRin(ex_mem_1_irout), .RW_in(ex_mem_1_rw_out), .RW_out(RW_num), .WEin(ex_mem_1_weout), .WEout(WE),
    .Syscallin(ex_mem_1_syscallout), .Syscallout(mem_wb_1_syscallout));  // open: PCout, IRout
  Hex_Digit_Display hex_digit_display_3 (.value(register_1_q_5));  // open: dp
  Hex_Digit_Display hex_digit_display_4 (.value(register_1_q_6));  // open: dp
  Hex_Digit_Display hex_digit_display_5 (.value(register_1_q_3));  // open: dp
  Hex_Digit_Display hex_digit_display_6 (.value(register_1_q_4));  // open: dp
  or or_9 (or_9_out, mem_wb_1_syscallout, halt);
  // Probe on main_4_circle
  counter_main main_4 (
    .halt(halt), .DataPk(datatest_1_datanop), .Jumpnop(datatest_1_jumpnopir_id), .circle(main_4_circle),
    .DataPkTime(main_4_datapktime), .clk(clk), .clear(in_1), .jrTime(main_4_jrtime),
    .noforecastTime(main_4_noforecasttime), .forecastTime(main_4_forecasttime), .wrong(datatest_1_wrong),
    .noforecast(datatest_1_noforecast), .forecast(datatest_1_forecast), .JumpnopTime(main_4_jumpnoptime));
  // Probe on main_4_datapktime
  // Probe on main_4_jumpnoptime
  Hex_Digit_Display hex_digit_display_7 (.value(register_1_q));  // open: dp
  Hex_Digit_Display hex_digit_display_8 (.value(register_1_q_2));  // open: dp
  Register #(.width(32)) register_1 (
    .D(a0), .en(or_9_out),
    .Q({register_1_q_8, register_1_q_7, register_1_q_6, register_1_q_5, register_1_q_4, register_1_q_3, register_1_q_2, register_1_q}),
    .clk(clk), .clr(in_1));
  and and_9 (halt, or_9_out, comparator_2_eq);
  Comparator #(.width(32)) comparator_2 (.a(v0), .b(32'ha), .eq(comparator_2_eq));  // open: gt, lt
  // Probe on main_4_jrtime
  // Probe on main_4_noforecasttime
  // Probe on main_4_forecasttime

  // Other names for the same wires on the sheet: clear = in_1

  // Notes on the sheet:
  //   contents of rom_1 (hex, n*v repeats v):
  //   20110001 8000c05 20110001 20120002 20130003 8000c09 20110001 20120002 20130003 8000c0d 20110001
  //   20120002 20130003 8000c11 20110001 20120002 20130003 c000cce 20110001 20120010 112020 20020022 c
  //   2320018 4810 8812 112020 20020022 c 1120fff9 20110001 20120010 118fc0 112020 20020022 c 232001b 4810
  //   8812 1620fff9 20100001 20110001 118fc0 112020 20020022 c 118882 12200001 8000c2b 112020 20020022 c
  //   20110001 118880 112020 20020022 c 12200001 8000c35 20110001 118fc0 112020 20020022 c 1188c3 112020
  //   20020022 c 118903 112020 20020022 c 118903 112020 20020022 c 118903 112020 20020022 c 118903 112020
  //   20020022 c 118903 112020 20020022 c 118903 112020 20020022 c 118903 112020 20020022 c 20100001
  //   109fc0 139fc3 8021 2012000c 24160003 26100001 3210000f 20080008 20090001 139900 2709825 132020
  //   20020022 c 1094022 1500fff9 22100001 2018000f 2188024 108700 20080008 20090001 139902 2709825 132021
  //   20020022 c 1094022 1500fff9 108702 2c9b022 12c00001 8000c66 4020 1084027 84400 3508ffff 82021
  //   20020022 c 2010ffff 20110000 ae300000 22100001 22310004 ae300000 22100001 22310004 ae300000 22100001
  //   22310004 ae300000 22100001 22310004 ae300000 22100001 22310004 ae300000 22100001 22310004 ae300000
  //   22100001 22310004 ae300000 22100001 22310004 ae300000 22100001 22310004 ae300000 22100001 22310004
  //   ae300000 22100001 22310004 ae300000 22100001 22310004 ae300000 22100001 22310004 ae300000 22100001
  //   22310004 ae300000 22100001 22310004 ae300000 22100001 22310004 22100001 8020 2011003c 8e130000
  //   8e340000 274402a 11000002 ae330000 ae140000 2231fffc 1611fff8 102020 20020022 c 22100004 2011003c
  //   1611fff2 2002000a c 20100000 22100001 102020 20020022 c 22100002 102020 20020022 c 22100003 102020
  //   20020022 c 22100004 102020 20020022 c 22100005 102020 20020022 c 22100006 102020 20020022 c 22100007
  //   102020 20020022 c 22100008 102020 20020022 20020022 c 3e00008
endmodule

module IF_ID (
  input  Syscallin,
  input  clk,
  input  clear,
  input  [31:0] PCin,
  input  [31:0] IRin,
  output Syscallout,
  output [31:0] PCout,
  output [31:0] IRout
);

  Register #(.width(1)) SyscallR (.D(Syscallin), .en(1'b1), .Q(Syscallout), .clk(clk), .clr(clear));
  Register #(.width(32)) PCR (.D(PCin), .en(1'b1), .Q(PCout), .clk(clk), .clr(clear));
  Register #(.width(32)) IRR (.D(IRin), .en(1'b1), .Q(IRout), .clk(clk), .clr(clear));
endmodule

module ID_EX (
  input  [3:0] ALUcontrolin,
  input  [31:0] RFR1in,
  input  [31:0] PCin,
  input  lwin,
  input  swin,
  input  [31:0] Xin,
  input  [31:0] IRin,
  input  WEin,
  input  clk,
  input  clear,
  input  HiLoWin,
  input  linkin,
  input  [4:0] RW_in,
  input  [31:0] Yin,
  input  Hiin,
  input  [31:0] addrin,
  input  Loin,
  input  jrin,
  input  [31:0] RFR2in,
  input  Syscallin,
  input  [31:0] offsetin,
  input  fromALUin,
  input  jumpin,
  input  Branchin,
  input  equal1in,
  output [3:0] ALUcontrolout,
  output [31:0] RFR1out,
  output [31:0] PCout,
  output lwout,
  output swout,
  output [31:0] Xout,
  output [31:0] IRout,
  output WEout,
  output HiLoWout,
  output linkout,
  output [4:0] RW_out,
  output [31:0] Yout,
  output Hiout,
  output [31:0] addrout,
  output Loout,
  output jrout,
  output [31:0] RFR2out,
  output Syscallout,
  output [31:0] offsetout,
  output fromALUout,
  output jumpout,
  output Branchout,
  output equal1out
);

  Register #(.width(32)) XR (.D(Xin), .en(1'b1), .Q(Xout), .clk(clk), .clr(clear));
  Register #(.width(32)) YR (.D(Yin), .en(1'b1), .Q(Yout), .clk(clk), .clr(clear));
  Register #(.width(32)) PCR (.D(RFR1in), .en(1'b1), .Q(RFR1out), .clk(clk), .clr(clear));
  Register #(.width(32)) RFR2R (.D(RFR2in), .en(1'b1), .Q(RFR2out), .clk(clk), .clr(clear));
  Register #(.width(32)) addrR (.D(addrin), .en(1'b1), .Q(addrout), .clk(clk), .clr(clear));
  Register #(.width(1)) HiLoWR (.D(HiLoWin), .en(1'b1), .Q(HiLoWout), .clk(clk), .clr(clear));
  Register #(.width(1)) WER (.D(WEin), .en(1'b1), .Q(WEout), .clk(clk), .clr(clear));
  Register #(.width(1)) lwR (.D(lwin), .en(1'b1), .Q(lwout), .clk(clk), .clr(clear));
  Register #(.width(1)) swR (.D(swin), .en(1'b1), .Q(swout), .clk(clk), .clr(clear));
  Register #(.width(32)) offsetR (.D(offsetin), .en(1'b1), .Q(offsetout), .clk(clk), .clr(clear));
  Register #(.width(5)) RW_R (.D(RW_in), .en(1'b1), .Q(RW_out), .clk(clk), .clr(clear));
  Register #(.width(4)) ALUcontrolR (.D(ALUcontrolin), .en(1'b1), .Q(ALUcontrolout), .clk(clk), .clr(clear));
  Register #(.width(32)) PCR_2 (.D(PCin), .en(1'b1), .Q(PCout), .clk(clk), .clr(clear));
  Register #(.width(32)) IRR (.D(IRin), .en(1'b1), .Q(IRout), .clk(clk), .clr(clear));
  Register #(.width(1)) HiR (.D(Hiin), .en(1'b1), .Q(Hiout), .clk(clk), .clr(clear));
  Register #(.width(1)) linkR (.D(linkin), .en(1'b1), .Q(linkout), .clk(clk), .clr(clear));
  Register #(.width(1)) LoR (.D(Loin), .en(1'b1), .Q(Loout), .clk(clk), .clr(clear));
  Register #(.width(1)) jrR (.D(jrin), .en(1'b1), .Q(jrout), .clk(clk), .clr(clear));
  Register #(.width(1)) fromALUR (.D(fromALUin), .en(1'b1), .Q(fromALUout), .clk(clk), .clr(clear));
  Register #(.width(1)) SyscallR (.D(Syscallin), .en(1'b1), .Q(Syscallout), .clk(clk), .clr(clear));
  Register #(.width(1)) jumpR (.D(jumpin), .en(1'b1), .Q(jumpout), .clk(clk), .clr(clear));
  Register #(.width(1)) BranchR (.D(Branchin), .en(1'b1), .Q(Branchout), .clk(clk), .clr(clear));
  Register #(.width(1)) equal1R (.D(equal1in), .en(1'b1), .Q(equal1out), .clk(clk), .clr(clear));
endmodule

module EX_MEM (
  input  [31:0] Result1in,
  input  [31:0] RFR2in,
  input  [31:0] PCin,
  input  [31:0] IRin,
  input  [4:0] RW_in,
  input  WEin,
  input  clk,
  input  clear,
  input  linkin,
  input  Hiin,
  input  Loin,
  input  lwin,
  input  swin,
  input  Syscallin,
  output [31:0] Result1out,
  output [31:0] RFR2out,
  output [31:0] PCout,
  output [31:0] IRout,
  output [4:0] RW_out,
  output WEout,
  output linkout,
  output Hiout,
  output Loout,
  output lwout,
  output swout,
  output Syscallout
);

  wire [31:0] Result2in, Result2out;

  Register #(.width(32)) Result1R (.D(Result1in), .en(1'b1), .Q(Result1out), .clk(clk), .clr(clear));
  Register #(.width(32)) Result2R (.D(Result2in), .en(1'b1), .Q(Result2out), .clk(clk), .clr(clear));
  Register #(.width(32)) RFR2R (.D(RFR2in), .en(1'b1), .Q(RFR2out), .clk(clk), .clr(clear));
  Register #(.width(32)) PCR (.D(PCin), .en(1'b1), .Q(PCout), .clk(clk), .clr(clear));
  Register #(.width(32)) IRR (.D(IRin), .en(1'b1), .Q(IRout), .clk(clk), .clr(clear));
  Register #(.width(1)) SyscallR (.D(Syscallin), .en(1'b1), .Q(Syscallout), .clk(clk), .clr(clear));
  Register #(.width(5)) RW_R (.D(RW_in), .en(1'b1), .Q(RW_out), .clk(clk), .clr(clear));
  Register #(.width(1)) WER (.D(WEin), .en(1'b1), .Q(WEout), .clk(clk), .clr(clear));
  Register #(.width(1)) HiR (.D(Hiin), .en(1'b1), .Q(Hiout), .clk(clk), .clr(clear));
  Register #(.width(1)) linkR (.D(linkin), .en(1'b1), .Q(linkout), .clk(clk), .clr(clear));
  Register #(.width(1)) LoR (.D(Loin), .en(1'b1), .Q(Loout), .clk(clk), .clr(clear));
  Register #(.width(1)) lwR (.D(lwin), .en(1'b1), .Q(lwout), .clk(clk), .clr(clear));
  Register #(.width(1)) swR (.D(swin), .en(1'b1), .Q(swout), .clk(clk), .clr(clear));
endmodule

module MEM_WB (
  input  [31:0] PCin,
  input  [31:0] IRin,
  input  WEin,
  input  [4:0] RW_in,
  input  [31:0] datain,
  input  Syscallin,
  input  clk,
  input  clear,
  output [31:0] PCout,
  output [31:0] IRout,
  output WEout,
  output [4:0] RW_out,
  output [31:0] dataout,
  output Syscallout
);

  Register #(.width(1)) SyscallR (.D(Syscallin), .en(1'b1), .Q(Syscallout), .clk(clk), .clr(clear));
  Register #(.width(32)) PCR (.D(PCin), .en(1'b1), .Q(PCout), .clk(clk), .clr(clear));
  Register #(.width(32)) IRR (.D(IRin), .en(1'b1), .Q(IRout), .clk(clk), .clr(clear));
  Register #(.width(5)) RW_R (.D(RW_in), .en(1'b1), .Q(RW_out), .clk(clk), .clr(clear));
  Register #(.width(1)) WER (.D(WEin), .en(1'b1), .Q(WEout), .clk(clk), .clr(clear));
  Register #(.width(32)) dataR (.D(datain), .en(1'b1), .Q(dataout), .clk(clk), .clr(clear));
endmodule

module DATAtest (
  input  EXWE,
  input  MEMWE,
  input  R1_E,
  input  R2_E,
  input  [4:0] EXRW_num,
  input  [4:0] MEMRW_num,
  input  [4:0] R1_num,
  input  [4:0] R2_num,
  input  [31:0] ALUEX,
  input  [31:0] Din,
  input  [31:0] PCin,
  input  [31:0] PC,
  input  [31:0] jumpPC,
  input  fromALUEX,
  input  jumppk,
  input  in_16,
  input  in_17,
  input  [31:0] RFR1,
  input  [31:0] RFR2,
  input  branch,
  output PClock,
  output IR_IDlock,
  output datanop,
  output jumpnopIR_ID,
  output jumpnopID_EX,
  output [31:0] RFR1out,
  output [31:0] RFR2out,
  output [31:0] PCout,
  output wrong,
  output noforecast,
  output forecast
);

  wire _1write, _2write, _3write, _4write, and_1_out, and_2_out, and_7_out, and_8_out, and_9_out, and_10_out,
       and_11_out, and_12_out, and_13_out, and_14_out, and_15_out, and_16_out, and_17_out, and_18_out,
       and_19_out, and_20_out, and_22_out, and_23_out, and_24_out, and_25_out, and_26_out, and_27_out,
       and_28_out, and_29_out, branchclk, comparator_1_eq, comparator_2_eq, comparator_3_eq, comparator_4_eq,
       comparator_5_eq, comparator_6_eq, comparator_7_eq, comparator_8_eq, comparator_9_eq, comparator_10_eq,
       comparator_11_eq, comparator_12_eq, comparator_13_eq, comparator_14_eq, comparator_15_eq,
       comparator_15_gt, comparator_15_lt, comparator_16_eq, comparator_16_gt, comparator_16_lt,
       comparator_17_eq, comparator_17_gt, comparator_17_lt, comparator_18_eq, comparator_18_gt,
       comparator_18_lt, comparator_19_eq, comparator_19_gt, comparator_19_lt, comparator_20_eq,
       comparator_20_gt, comparator_20_lt, comparator_21_eq, comparator_22_eq, comparator_23_eq,
       comparator_24_eq, nor_1_out, nor_2_out, nor_3_out, nor_4_out, not_1_out, not_2_out, not_3_out,
       not_4_out, not_5_out, not_6_out, not_7_out, not_8_out, not_9_out, not_10_out, not_11_out, not_12_out,
       not_13_out, not_14_out, not_15_out, not_16_out, or_1_out, or_2_out, or_3_out, or_4_out, or_5_out,
       or_6_out, or_7_out, or_14_out, R1EX, R1MEM, R2EX, R2MEM, register_2_q, vaild1_q, vaild2_q, vaild3_q,
       vaild4_q;
  wire [7:0] count_2_q, count_3_q, count_4_q, count_q;
  wire [31:0] jumpPC1_q, jumpPC2_q, jumpPC3_q, jumpPC4_q, multiplexer_1_out, multiplexer_2_out,
       multiplexer_5_out, multiplexer_6_out, multiplexer_7_out, multiplexer_8_out, multiplexer_9_out,
       multiplexer_10_out, multiplexer_11_out, multiplexer_12_out, multiplexer_13_out, PC1_q, PC2_q, PC3_q,
       PC4_q, subtractor_1_out, subtractor_2_out, subtractor_3_out, subtractor_4_out;

  Counter count (
    .load(_1write), .D({8{1'b0}}), .count(not_1_out), .Q(count_q), .clk(branchclk), .clr(in_17));  // open: carry
  not not_1 (not_1_out, _1write);
  Counter count_2 (
    .load(_2write), .D({8{1'b0}}), .count(not_2_out), .Q(count_2_q), .clk(branchclk), .clr(in_17));  // open: carry
  not not_2 (not_2_out, _2write);
  Counter count_3 (
    .load(_3write), .D({8{1'b0}}), .count(not_3_out), .Q(count_3_q), .clk(branchclk), .clr(in_17));  // open: carry
  not not_3 (not_3_out, _3write);
  Counter count_4 (
    .load(_4write), .D({8{1'b0}}), .count(not_4_out), .Q(count_4_q), .clk(branchclk), .clr(in_17));  // open: carry
  not not_4 (not_4_out, _4write);
  Comparator #(.width(5)) comparator_1 (.a({5{1'b0}}), .b(EXRW_num), .eq(comparator_1_eq));  // open: gt, lt
  Comparator #(.width(5)) comparator_2 (.a(R1_num), .b(EXRW_num), .eq(comparator_2_eq));  // open: gt, lt
  Comparator #(.width(5)) comparator_3 (.a(R2_num), .b(EXRW_num), .eq(comparator_3_eq));  // open: gt, lt
  Comparator #(.width(5)) comparator_4 (.a(R1_num), .b(MEMRW_num), .eq(comparator_4_eq));  // open: gt, lt
  Comparator #(.width(5)) comparator_5 (.a(R2_num), .b(MEMRW_num), .eq(comparator_5_eq));  // open: gt, lt
  Comparator #(.width(5)) comparator_6 (.a({5{1'b0}}), .b(MEMRW_num), .eq(comparator_6_eq));  // open: gt, lt
  Multiplexer #(.width(32), .enable("false")) multiplexer_1 (
    .in0(RFR1), .in1(Din), .out(multiplexer_1_out), .sel(R1MEM));
  Multiplexer #(.width(32), .enable("false")) multiplexer_2 (
    .in0(RFR2), .in1(Din), .out(multiplexer_2_out), .sel(R2MEM));
  not not_5 (not_5_out, comparator_1_eq);
  not not_6 (not_6_out, comparator_6_eq);
  Multiplexer #(.width(32), .enable("false")) multiplexer_3 (
    .in0(multiplexer_1_out), .in1(ALUEX), .out(RFR1out), .sel(and_1_out));
  and and_1 (and_1_out, R1EX, fromALUEX);
  and and_2 (and_2_out, R2EX, fromALUEX);
  Register #(.width(1)) vaild1 (.D(1'b1), .en(_1write), .Q(vaild1_q), .clk(branchclk), .clr(in_17));
  Register #(.width(1)) vaild2 (.D(1'b1), .en(_2write), .Q(vaild2_q), .clk(branchclk), .clr(in_17));
  Register #(.width(1)) vaild3 (.D(1'b1), .en(_3write), .Q(vaild3_q), .clk(branchclk), .clr(in_17));
  Register #(.width(1)) vaild4 (.D(1'b1), .en(_4write), .Q(vaild4_q), .clk(branchclk), .clr(in_17));
  and and_3 (R1EX, R1_E, EXWE, comparator_2_eq, not_5_out);
  and and_4 (R2EX, R2_E, EXWE, comparator_3_eq, not_5_out);
  and and_5 (R1MEM, not_6_out, comparator_4_eq, MEMWE, R1_E);
  and and_6 (R2MEM, not_6_out, comparator_5_eq, MEMWE, R2_E);
  Multiplexer #(.width(32), .enable("false")) multiplexer_4 (
    .in0(multiplexer_2_out), .in1(ALUEX), .out(RFR2out), .sel(and_2_out));
  Register #(.width(32)) PC1 (.D(PC), .en(_1write), .Q(PC1_q), .clk(branchclk), .clr(in_17));
  Register #(.width(32)) PC2 (.D(PC), .en(_2write), .Q(PC2_q), .clk(branchclk), .clr(in_17));
  Register #(.width(32)) PC3 (.D(PC), .en(_3write), .Q(PC3_q), .clk(branchclk), .clr(in_17));
  Register #(.width(32)) PC4 (.D(PC), .en(_4write), .Q(PC4_q), .clk(branchclk), .clr(in_17));
  or or_1 (or_1_out, R1EX, R2EX);
  Comparator #(.width(32), .mode("unsigned")) comparator_7 (.a(PC), .b(PC1_q), .eq(comparator_7_eq));  // open: gt, lt
  Comparator #(.width(32), .mode("unsigned")) comparator_8 (.a(PC1_q), .b(PCin), .eq(comparator_8_eq));  // open: gt, lt
  Comparator #(.width(32), .mode("unsigned")) comparator_9 (.a(PC), .b(PC2_q), .eq(comparator_9_eq));  // open: gt, lt
  Comparator #(.width(32), .mode("unsigned")) comparator_10 (
    .a(PC2_q), .b(PCin), .eq(comparator_10_eq));  // open: gt, lt
  Comparator #(.width(32), .mode("unsigned")) comparator_11 (.a(PC), .b(PC3_q), .eq(comparator_11_eq));  // open: gt, lt
  Comparator #(.width(32), .mode("unsigned")) comparator_12 (
    .a(PC3_q), .b(PCin), .eq(comparator_12_eq));  // open: gt, lt
  Comparator #(.width(32), .mode("unsigned")) comparator_13 (.a(PC), .b(PC4_q), .eq(comparator_13_eq));  // open: gt, lt
  Comparator #(.width(32), .mode("unsigned")) comparator_14 (
    .a(PC4_q), .b(PCin), .eq(comparator_14_eq));  // open: gt, lt
  or or_2 (or_2_out, comparator_15_gt, comparator_15_eq);
  Comparator comparator_15 (
    .a(count_q), .b(count_2_q), .gt(comparator_15_gt), .eq(comparator_15_eq), .lt(comparator_15_lt));
  or or_3 (or_3_out, comparator_16_gt, comparator_16_eq);
  Comparator comparator_16 (
    .a(count_q), .b(count_3_q), .gt(comparator_16_gt), .eq(comparator_16_eq), .lt(comparator_16_lt));
  or or_4 (or_4_out, comparator_17_gt, comparator_17_eq);
  Comparator comparator_17 (
    .a(count_q), .b(count_4_q), .gt(comparator_17_gt), .eq(comparator_17_eq), .lt(comparator_17_lt));
  or or_5 (or_5_out, comparator_18_gt, comparator_18_eq);
  Comparator comparator_18 (
    .a(count_2_q), .b(count_3_q), .gt(comparator_18_gt), .eq(comparator_18_eq), .lt(comparator_18_lt));
  or or_6 (or_6_out, comparator_19_gt, comparator_19_eq);
  Comparator comparator_19 (
    .a(count_2_q), .b(count_4_q), .gt(comparator_19_gt), .eq(comparator_19_eq), .lt(comparator_19_lt));
  or or_7 (or_7_out, comparator_20_gt, comparator_20_eq);
  Comparator comparator_20 (
    .a(count_3_q), .b(count_4_q), .gt(comparator_20_gt), .eq(comparator_20_eq), .lt(comparator_20_lt));
  not not_7 (not_7_out, fromALUEX);
  not not_8 (not_8_out, comparator_7_eq);
  not not_9 (not_9_out, comparator_9_eq);
  not not_10 (not_10_out, comparator_11_eq);
  and and_7 (and_7_out, vaild4_q, not_11_out);
  not not_11 (not_11_out, comparator_13_eq);
  and and_8 (and_8_out, vaild4_q, comparator_14_eq);
  and and_9 (and_9_out, or_1_out, not_7_out);
  and and_10 (and_10_out, vaild1_q, not_8_out);
  and and_11 (and_11_out, vaild1_q, comparator_8_eq);
  and and_12 (and_12_out, vaild2_q, not_9_out);
  and and_13 (and_13_out, vaild2_q, comparator_10_eq);
  and and_14 (and_14_out, vaild3_q, not_10_out);
  and and_15 (and_15_out, vaild3_q, comparator_12_eq);
  and and_16 (and_16_out, and_7_out, and_14_out, and_12_out, and_10_out);
  Register #(.width(1), .trigger("falling")) register_1 (
    .D(and_9_out), .en(1'b1), .Q(datanop), .clk(in_16), .clr(in_17));
  or or_8 (forecast, and_11_out, and_13_out, and_15_out, and_8_out);
  not not_12 (not_12_out, and_10_out);
  and and_17 (and_17_out, and_16_out, or_2_out, or_3_out, or_4_out);
  nor nor_1 (nor_1_out, _1write, and_12_out);
  nor nor_2 (nor_2_out, _2write, _1write, and_14_out);
  nor nor_3 (nor_3_out, _3write, _2write, _1write, and_7_out);
  and and_18 (and_18_out, and_16_out, comparator_15_lt, or_5_out, or_6_out);
  and and_19 (and_19_out, and_16_out, comparator_16_lt, comparator_18_lt, or_7_out);
  and and_20 (and_20_out, and_16_out, comparator_17_lt, comparator_19_lt, comparator_20_lt);
  Multiplexer #(.width(32), .enable("false")) multiplexer_5 (
    .in0(PC), .in1(jumpPC), .out(multiplexer_5_out), .sel(jumppk));
  or or_9 (_1write, not_12_out, and_17_out);
  or or_10 (_2write, nor_1_out, and_18_out);
  or or_11 (_3write, nor_2_out, and_19_out);
  or or_12 (_4write, nor_3_out, and_20_out);
  Register #(.width(32)) jumpPC1 (.D(multiplexer_5_out), .en(_1write), .Q(jumpPC1_q), .clk(branchclk), .clr(in_17));
  Register #(.width(32)) jumpPC2 (.D(multiplexer_5_out), .en(_2write), .Q(jumpPC2_q), .clk(branchclk), .clr(in_17));
  Register #(.width(32)) jumpPC3 (.D(multiplexer_5_out), .en(_3write), .Q(jumpPC3_q), .clk(branchclk), .clr(in_17));
  Register #(.width(32)) jumpPC4 (.D(multiplexer_5_out), .en(_4write), .Q(jumpPC4_q), .clk(branchclk), .clr(in_17));
  Multiplexer #(.width(32), .enable("false")) multiplexer_6 (
    .in0(PCin), .in1(jumpPC1_q), .out(multiplexer_6_out), .sel(and_11_out));
  Multiplexer #(.width(32), .enable("false")) multiplexer_7 (
    .in0(multiplexer_6_out), .in1(jumpPC2_q), .out(multiplexer_7_out), .sel(and_13_out));
  Multiplexer #(.width(32), .enable("false")) multiplexer_8 (
    .in0(multiplexer_7_out), .in1(jumpPC3_q), .out(multiplexer_8_out), .sel(and_15_out));
  Multiplexer #(.width(32), .enable("false")) multiplexer_9 (
    .in0(multiplexer_8_out), .in1(jumpPC4_q), .out(multiplexer_9_out), .sel(and_8_out));
  and and_21 (branchclk, in_16, register_2_q);
  Register #(.width(1), .trigger("falling")) register_2 (
    .D(branch), .en(1'b1), .Q(register_2_q), .clk(in_16), .clr(in_17));
  not not_13 (not_13_out, comparator_21_eq);
  Comparator #(.width(32), .mode("unsigned")) comparator_21 (
    .a(multiplexer_5_out), .b(jumpPC1_q), .eq(comparator_21_eq));  // open: gt, lt
  not not_14 (not_14_out, comparator_22_eq);
  Comparator #(.width(32), .mode("unsigned")) comparator_22 (
    .a(multiplexer_5_out), .b(jumpPC2_q), .eq(comparator_22_eq));  // open: gt, lt
  not not_15 (not_15_out, comparator_23_eq);
  Comparator #(.width(32), .mode("unsigned")) comparator_23 (
    .a(multiplexer_5_out), .b(jumpPC3_q), .eq(comparator_23_eq));  // open: gt, lt
  not not_16 (not_16_out, comparator_24_eq);
  Comparator #(.width(32), .mode("unsigned")) comparator_24 (
    .a(multiplexer_5_out), .b(jumpPC4_q), .eq(comparator_24_eq));  // open: gt, lt
  Multiplexer #(.width(32), .enable("false")) multiplexer_10 (
    .in0(multiplexer_9_out), .in1(subtractor_1_out), .out(multiplexer_10_out), .sel(and_22_out));
  Subtractor #(.width(32)) subtractor_1 (.a(PC1_q), .b(32'h4), .out(subtractor_1_out));  // open: bin, bout
  and and_22 (and_22_out, not_13_out, and_23_out);
  and and_23 (and_23_out, vaild1_q, comparator_7_eq);
  Subtractor #(.width(32)) subtractor_2 (.a(PC2_q), .b(32'h4), .out(subtractor_2_out));  // open: bin, bout
  and and_24 (and_24_out, not_14_out, and_25_out);
  and and_25 (and_25_out, vaild2_q, comparator_9_eq);
  and and_26 (and_26_out, not_15_out, and_27_out);
  and and_27 (and_27_out, vaild3_q, comparator_11_eq);
  and and_28 (and_28_out, not_16_out, and_29_out);
  and and_29 (and_29_out, vaild4_q, comparator_13_eq);
  Multiplexer #(.width(32), .enable("false")) multiplexer_11 (
    .in0(multiplexer_10_out), .in1(subtractor_2_out), .out(multiplexer_11_out), .sel(and_24_out));
  Subtractor #(.width(32)) subtractor_3 (.a(PC3_q), .b(32'h4), .out(subtractor_3_out));  // open: bin, bout
  Subtractor #(.width(32)) subtractor_4 (.a(PC4_q), .b(32'h4), .out(subtractor_4_out));  // open: bin, bout
  Multiplexer #(.width(32), .enable("false")) multiplexer_12 (
    .in0(multiplexer_11_out), .in1(subtractor_3_out), .out(multiplexer_12_out), .sel(and_26_out));
  Multiplexer #(.width(32), .enable("false")) multiplexer_13 (
    .in0(multiplexer_12_out), .in1(subtractor_4_out), .out(multiplexer_13_out), .sel(and_28_out));
  nor nor_4 (nor_4_out, and_23_out, and_25_out, and_27_out, and_29_out);
  and and_30 (noforecast, jumppk, nor_4_out);
  Multiplexer #(.width(32), .enable("false")) multiplexer_14 (
    .in0(multiplexer_13_out), .in1(jumpPC), .out(PCout), .sel(noforecast));
  or or_13 (wrong, and_22_out, and_24_out, and_26_out, and_28_out);
  or or_14 (or_14_out, noforecast, wrong);
  Register #(.width(1), .trigger("falling")) register_3 (
    .D(or_14_out), .en(1'b1), .Q(jumpnopID_EX), .clk(in_16), .clr(in_17));

  assign IR_IDlock = datanop;
  assign jumpnopIR_ID = jumpnopID_EX;
  assign PClock = datanop;

  // Other names for the same wires on the sheet: clear = in_17; clk = in_16

  // Notes on the sheet:
  //   datapk
  //   noforecast
  //   wrong
endmodule
