// Logisim project regfile.circ as structural Verilog: 2 circuits, main circuit main
module main (
  input  [4:0] Reg1_num,
  input  [4:0] Reg2,
  input  [4:0] Write_Reg_num,
  input  [31:0] Din,
  input  Write_Enable,
  input  Clock,
  output [31:0] Reg1,
  output [31:0] v0_Value,
  output [31:0] a0_Value,
  output [31:0] s2_Value,
  output [31:0] ra_Value,
  output [31:0] Reg2_2
);

  wire demultiplexer_1_out1, demultiplexer_1_out2, demultiplexer_1_out3, demultiplexer_1_out4,
       demultiplexer_1_out5, demultiplexer_1_out6, demultiplexer_1_out7, demultiplexer_1_out8,
       demultiplexer_1_out9, demultiplexer_1_out10, demultiplexer_1_out11, demultiplexer_1_out12,
       demultiplexer_1_out13, demultiplexer_1_out14, demultiplexer_1_out15, demultiplexer_1_out16,
       demultiplexer_1_out17, demultiplexer_1_out18, demultiplexer_1_out19, demultiplexer_1_out20,
       demultiplexer_1_out21, demultiplexer_1_out22, demultiplexer_1_out23, demultiplexer_1_out24,
       demultiplexer_1_out25, demultiplexer_1_out26, demultiplexer_1_out27, demultiplexer_1_out28,
       demultiplexer_1_out29, demultiplexer_1_out30, demultiplexer_1_out31;
  wire [31:0] R0_q, R1_q, R3_q, R5_q, R6_q, R7_q, R8_q, R9_q, R10_q, R11_q, R12_q, R13_q, R14_q, R15_q,
       R16_q, R17_q, R19_q, R20_q, R21_q, R22_q, R23_q, R24_q, R25_q, R26_q, R27_q, R28_q, R29_q, R30_q;

  Demultiplexer #(.select(5), .enable("false")) demultiplexer_1 (
    .out1(demultiplexer_1_out1), .out2(demultiplexer_1_out2), .out3(demultiplexer_1_out3),
    .out4(demultiplexer_1_out4), .out5(demultiplexer_1_out5), .out6(demultiplexer_1_out6),
    .out7(demultiplexer_1_out7), .out8(demultiplexer_1_out8), .out9(demultiplexer_1_out9),
    .out10(demultiplexer_1_out10), .out11(demultiplexer_1_out11), .out12(demultiplexer_1_out12),
    .out13(demultiplexer_1_out13), .out14(demultiplexer_1_out14), .out15(demultiplexer_1_out15),
    .out16(demultiplexer_1_out16), .out17(demultiplexer_1_out17), .out18(demultiplexer_1_out18),
    .out19(demultiplexer_1_out19), .out20(demultiplexer_1_out20), .out21(demultiplexer_1_out21),
    .out22(demultiplexer_1_out22), .out23(demultiplexer_1_out23), .out24(demultiplexer_1_out24),
    .out25(demultiplexer_1_out25), .out26(demultiplexer_1_out26), .out27(demultiplexer_1_out27),
    .out28(demultiplexer_1_out28), .out29(demultiplexer_1_out29), .out30(demultiplexer_1_out30),
    .out31(demultiplexer_1_out31), .in(Write_Enable), .sel(Write_Reg_num));  // open: out0
  Register #(.width(32), .trigger("falling")) R0 (.D(Din), .en(1'b0), .Q(R0_q), .clk(Clock), .clr(1'b0));
  Register #(.width(32), .trigger("falling")) R4 (
    .D(Din), .en(demultiplexer_1_out4), .Q(a0_Value), .clk(Clock), .clr(1'b0));
  Register #(.width(32), .trigger("falling")) R8 (
    .D(Din), .en(demultiplexer_1_out8), .Q(R8_q), .clk(Clock), .clr(1'b0));
  Register #(.width(32), .trigger("falling")) R12 (
    .D(Din), .en(demultiplexer_1_out12), .Q(R12_q), .clk(Clock), .clr(1'b0));
  Register #(.width(32), .trigger("falling")) R16 (
    .D(Din), .en(demultiplexer_1_out16), .Q(R16_q), .clk(Clock), .clr(1'b0));
  Register #(.width(32), .trigger("falling")) R20 (
    .D(Din), .en(demultiplexer_1_out20), .Q(R20_q), .clk(Clock), .clr(1'b0));
  Register #(.width(32), .trigger("falling")) R24 (
    .D(Din), .en(demultiplexer_1_out24), .Q(R24_q), .clk(Clock), .clr(1'b0));
  Register #(.width(32), .trigger("falling")) R28 (
    .D(Din), .en(demultiplexer_1_out28), .Q(R28_q), .clk(Clock), .clr(1'b0));
  Register #(.width(32), .trigger("falling")) R1 (
    .D(Din), .en(demultiplexer_1_out1), .Q(R1_q), .clk(Clock), .clr(1'b0));
  Register #(.width(32), .trigger("falling")) R5 (
    .D(Din), .en(demultiplexer_1_out5), .Q(R5_q), .clk(Clock), .clr(1'b0));
  Register #(.width(32), .trigger("falling")) R9 (
    .D(Din), .en(demultiplexer_1_out9), .Q(R9_q), .clk(Clock), .clr(1'b0));
  Register #(.width(32), .trigger("falling")) R13 (
    .D(Din), .en(demultiplexer_1_out13), .Q(R13_q), .clk(Clock), .clr(1'b0));
  Register #(.width(32), .trigger("falling")) R17 (
    .D(Din), .en(demultiplexer_1_out17), .Q(R17_q), .clk(Clock), .clr(1'b0));
  Register #(.width(32), .trigger("falling")) R21 (
    .D(Din), .en(demultiplexer_1_out21), .Q(R21_q), .clk(Clock), .clr(1'b0));
  Register #(.width(32), .trigger("falling")) R25 (
    .D(Din), .en(demultiplexer_1_out25), .Q(R25_q), .clk(Clock), .clr(1'b0));
  Register #(.width(32), .trigger("falling")) R29 (
    .D(Din), .en(demultiplexer_1_out29), .Q(R29_q), .clk(Clock), .clr(1'b0));
  Register #(.width(32), .trigger("falling")) R2 (
    .D(Din), .en(demultiplexer_1_out2), .Q(v0_Value), .clk(Clock), .clr(1'b0));
  Register #(.width(32), .trigger("falling")) R6 (
    .D(Din), .en(demultiplexer_1_out6), .Q(R6_q), .clk(Clock), .clr(1'b0));
  Register #(.width(32), .trigger("falling")) R10 (
    .D(Din), .en(demultiplexer_1_out10), .Q(R10_q), .clk(Clock), .clr(1'b0));
  Register #(.width(32), .trigger("falling")) R14 (
    .D(Din), .en(demultiplexer_1_out14), .Q(R14_q), .clk(Clock), .clr(1'b0));
  Register #(.width(32), .trigger("falling")) R18 (
    .D(Din), .en(demultiplexer_1_out18), .Q(s2_Value), .clk(Clock), .clr(1'b0));
  Register #(.width(32), .trigger("falling")) R22 (
    .D(Din), .en(demultiplexer_1_out22), .Q(R22_q), .clk(Clock), .clr(1'b0));
  Register #(.width(32), .trigger("falling")) R26 (
    .D(Din), .en(demultiplexer_1_out26), .Q(R26_q), .clk(Clock), .clr(1'b0));
  Register #(.width(32), .trigger("falling")) R30 (
    .D(Din), .en(demultiplexer_1_out30), .Q(R30_q), .clk(Clock), .clr(1'b0));
  Register #(.width(32), .trigger("falling")) R3 (
    .D(Din), .en(demultiplexer_1_out3), .Q(R3_q), .clk(Clock), .clr(1'b0));
  Register #(.width(32), .trigger("falling")) R7 (
    .D(Din), .en(demultiplexer_1_out7), .Q(R7_q), .clk(Clock), .clr(1'b0));
  Register #(.width(32), .trigger("falling")) R11 (
    .D(Din), .en(demultiplexer_1_out11), .Q(R11_q), .clk(Clock), .clr(1'b0));
  Register #(.width(32), .trigger("falling")) R15 (
    .D(Din), .en(demultiplexer_1_out15), .Q(R15_q), .clk(Clock), .clr(1'b0));
  Register #(.width(32), .trigger("falling")) R19 (
    .D(Din), .en(demultiplexer_1_out19), .Q(R19_q), .clk(Clock), .clr(1'b0));
  Register #(.width(32), .trigger("falling")) R23 (
    .D(Din), .en(demultiplexer_1_out23), .Q(R23_q), .clk(Clock), .clr(1'b0));
  Register #(.width(32), .trigger("falling")) R27 (
    .D(Din), .en(demultiplexer_1_out27), .Q(R27_q), .clk(Clock), .clr(1'b0));
  Register #(.width(32), .trigger("falling")) R31 (
    .D(Din), .en(demultiplexer_1_out31), .Q(ra_Value), .clk(Clock), .clr(1'b0));
  Multiplexer #(.select(5), .width(32), .enable("false")) multiplexer_1 (
    .in0(R0_q), .in1(R1_q), .in2(v0_Value), .in3(R3_q), .in4(a0_Value), .in5(R5_q), .in6(R6_q), .in7(R7_q),
    .in8(R8_q), .in9(R9_q), .in10(R10_q), .in11(R11_q), .in12(R12_q), .in13(R13_q), .in14(R14_q),
    .in15(R15_q), .in16(R16_q), .in17(R17_q), .in18(s2_Value), .in19(R19_q), .in20(R20_q), .in21(R21_q),
    .in22(R22_q), .in23(R23_q), .in24(R24_q), .in25(R25_q), .in26(R26_q), .in27(R27_q), .in28(R28_q),
    .in29(R29_q), .in30(R30_q), .in31(ra_Value), .out(Reg1), .sel(Reg1_num));
  Multiplexer #(.select(5), .width(32), .enable("false")) multiplexer_2 (
    .in0(R0_q), .in1(R1_q), .in2(v0_Value), .in3(R3_q), .in4(a0_Value), .in5(R5_q), .in6(R6_q), .in7(R7_q),
    .in8(R8_q), .in9(R9_q), .in10(R10_q), .in11(R11_q), .in12(R12_q), .in13(R13_q), .in14(R14_q),
    .in15(R15_q), .in16(R16_q), .in17(R17_q), .in18(s2_Value), .in19(R19_q), .in20(R20_q), .in21(R21_q),
    .in22(R22_q), .in23(R23_q), .in24(R24_q), .in25(R25_q), .in26(R26_q), .in27(R27_q), .in28(R28_q),
    .in29(R29_q), .in30(R30_q), .in31(ra_Value), .out(Reg2_2), .sel(Reg2));

  // Other names for the same wires on the sheet: a0[31:0] = a0_Value; clk = Clock; ra[31:0] = ra_Value;
  //   reg2_num[4:0] = Reg2; reg2_t[31:0] = Reg2_2; s2[31:0] = s2_Value; v0[31:0] = v0_Value; WE = Write_Enable;
  //   write_data[31:0] = Din

  // Notes on the sheet:
  //   输入引脚
  //   输出引脚
  //   Debug引脚，便于观测寄存器值
  //   请勿修改引脚以及封装，直接使用隧道连接电路
endmodule

module test (
);

  wire undriven;

  main main_1 (.Clock(undriven));  // open: Reg1_num, Reg2, Write_Reg_num, Din, Write_Enable, Reg1, Reg2_2, v0_Value, a0_Value, s2_Value, ra_Value
endmodule
